// Logisim project cpu24-riscv.circ as structural Verilog: 16 circuits, main circuit ◇单周期RISC-V
module \单周期RISC_V  (
  input  IR1,
  input  IR2,
  input  IR3,
  output RegWrite,
  output MemWrite,
  output [31:0] PC,
  output [31:0] IR,
  output [31:0] RDin,
  output [31:0] MDin,
  output [31:0] LedData
);

  wire and_2_out, and_3_out, and_4_out, and_5_out, and_6_out, AUIPC, Beq, Bge, Bne, CLK, clock_1_out,
       comparator_1_eq, comparator_1_lt, comparator_2_eq, comparator_3_eq, comparator_3_gt, d_ff_1_q, ecall,
       equal, Go, halt, IR1_t, IR2_t, IR3_t, IRA, IRB, IRC, J, lb, nand_1_out, not_1_out, not_2_out,
       not_3_out, not_4_out, PCSrc, RST, tunnel, URET, W1, W2, W3, \单周期硬布线控制器_1_alu_src ,
       \单周期硬布线控制器_1_s_type ;
  wire [0:0] \单周期硬布线控制器_1_memtoreg ;
  wire [2:0] Instr;
  wire [3:0] \单周期硬布线控制器_1_alu_op ;
  wire [4:0] multiplexer_2_out, multiplexer_3_out;
  wire [11:0] multiplexer_4_out;
  wire [12:0] CNT_num;
  wire [15:0] \总周期数 ;
  wire [31:0] adder_2_out, adder_3_out, adder_4_out, alu_1_result, and_1_out, auipc_res, bit_extender_1_out,
       bit_extender_2_out, bit_extender_3_out, bit_extender_4_out, bit_extender_5_out, bit_extender_6_out,
       bit_extender_7_out, bit_extender_8_out, multiplexer_1_out, multiplexer_5_out, multiplexer_6_out,
       multiplexer_7_out, multiplexer_8_out, PC_4, R1, ram_1_data, shifter_1_out, shifter_2_out,
       shifter_3_out;

  Button \u_继续运行  (.out(Go));
  Button _1 (.out(IRA));
  Button _2 (.out(IRB));
  Button _3 (.out(IRC));
  LED #(.active("true")) led_1 (.in(W1));
  LED #(.active("true")) led_2 (.in(W2));
  LED #(.active("true")) led_3 (.in(W3));
  Hex_Digit_Display hex_digit_display_1 (.value(LedData[31:28]));  // open: dp
  Multiplexer #(.select(1), .width(32), .disabled("Z"), .enable("false")) multiplexer_1 (
    .in0(PC_4), .in1(multiplexer_6_out), .out(multiplexer_1_out), .sel(PCSrc));
  Hex_Digit_Display hex_digit_display_2 (.value(LedData[23:20]));  // open: dp
  Hex_Digit_Display hex_digit_display_3 (.value(LedData[27:24]));  // open: dp
  not not_1 (not_1_out, halt);
  Hex_Digit_Display hex_digit_display_4 (.value(LedData[19:16]));  // open: dp
  Hex_Digit_Display hex_digit_display_5 (.value(LedData[15:12]));  // open: dp
  Register #(.width(32), .trigger("rising"), .Select("low")) u_PC (
    .D(multiplexer_1_out), .en(not_1_out), .Q(PC), .clk(CLK), .clr(RST));
  Hex_Digit_Display hex_digit_display_6 (.value(LedData[11:8]));  // open: dp
  Hex_Digit_Display hex_digit_display_7 (.value(LedData[7:4]));  // open: dp
  // Probe on \总周期数 
  Adder #(.width(32)) adder_1 (.a(PC), .b(32'h4), .out(PC_4));  // open: cin, cout
  Hex_Digit_Display hex_digit_display_8 (.value(LedData[3:0]));  // open: dp
  // RiscV_Probe riscv_probe_1: pin names not known; wires that end beside it: IR
  ROM #(.addrWidth(10), .dataWidth(32), .Select("high")) rom_1 (.addr(PC[11:2]), .data(IR));
  or or_1 (IR1_t, IR1, IRA);
  or or_2 (IR2_t, IR2, IRB);
  \单周期硬布线控制器  \u_单周期硬布线控制器_1  (
    .Funct({IR[30], IR[25], IR[14:12]}), .OP(IR[6:2]), .ALU_OP(\单周期硬布线控制器_1_alu_op ),
    .MemToReg(\单周期硬布线控制器_1_memtoreg [0]), .MemWrite(MemWrite), .ALU_SRC(\单周期硬布线控制器_1_alu_src ),
    .RegWrite(RegWrite), .ecall(ecall), .S_type(\单周期硬布线控制器_1_s_type ), .Jalr(Instr[0]), .Beq(Beq),
    .JAL(Instr[2]), .Bne(Bne), .in_3(IR[21]), .uret(URET), .AUIPC(AUIPC), .lb(lb), .Bge(Bge));
  Multiplexer #(.select(1), .width(5), .disabled("Z"), .enable("false")) multiplexer_2 (
    .in0(IR[19:15]), .in1(5'b10001), .out(multiplexer_2_out), .sel(ecall));
  Multiplexer #(.select(1), .width(5), .disabled("Z"), .enable("false")) multiplexer_3 (
    .in0(IR[24:20]), .in1(5'b01010), .out(multiplexer_3_out), .sel(ecall));
  Multiplexer #(.select(1), .width(12), .disabled("Z"), .enable("false")) multiplexer_4 (
    .in0(IR[31:20]), .in1({IR[31:25], IR[11:7]}), .out(multiplexer_4_out), .sel(\单周期硬布线控制器_1_s_type ));
  assign bit_extender_1_out = {{20{multiplexer_4_out[11]}}, multiplexer_4_out};  // Bit_Extender bit_extender_1
  assign bit_extender_2_out = {{20{IR[31]}}, {IR[31], IR[7], IR[30:25], IR[11:8]}};  // Bit_Extender bit_extender_2
  assign bit_extender_3_out = {{12{IR[31]}}, {IR[31], IR[19:12], IR[20], IR[30:21]}};  // Bit_Extender bit_extender_3
  assign bit_extender_4_out = {{12{IR[31]}}, IR[31:12]};  // Bit_Extender bit_extender_4
  or or_3 (IR3_t, IR3, IRC);
  Regifile regifile_1 (
    .Din(RDin), .Clk(CLK), .R1(R1), .R2(MDin), .WE(RegWrite), .W_num(IR[11:7]), .R1_num(multiplexer_2_out),
    .R2_num(multiplexer_3_out));
  Adder #(.width(32)) adder_2 (.a(bit_extender_1_out), .b(R1), .out(adder_2_out));  // open: cin, cout
  Shifter #(.width(32), .shift("ll")) shifter_1 (.in(bit_extender_2_out), .\dist (5'b00001), .out(shifter_1_out));
  Shifter #(.width(32), .shift("ll")) shifter_2 (.in(bit_extender_3_out), .\dist (5'b00001), .out(shifter_2_out));
  Shifter #(.width(32), .shift("ll")) shifter_3 (.in(bit_extender_4_out), .\dist (5'b01100), .out(shifter_3_out));
  Multiplexer #(.select(1), .width(32), .disabled("Z"), .enable("false")) multiplexer_5 (
    .in0(MDin), .in1(bit_extender_1_out), .out(multiplexer_5_out), .sel(\单周期硬布线控制器_1_alu_src ));
  Adder #(.width(32)) adder_3 (.a(shifter_1_out), .b(PC), .out(adder_3_out));  // open: cin, cout
  Adder #(.width(32)) adder_4 (.a(shifter_2_out), .b(PC), .out(adder_4_out));  // open: cin, cout
  Adder #(.width(32)) adder_5 (.a(shifter_3_out), .b(PC), .out(auipc_res));  // open: cin, cout
  assign and_1_out = adder_2_out & 32'hfffffffe;  // AND_Gate and_1, 32 bits wide
  ALU alu_1 (
    .X(R1), .Y(multiplexer_5_out), .AluOP(\单周期硬布线控制器_1_alu_op ), .Equal(equal), .Result(alu_1_result));  // open: Result_2, out_4, out_6
  Multiplexer #(.select(3), .width(32), .disabled("Z"), .enable("false")) multiplexer_6 (
    .in1(and_1_out), .in2(adder_3_out), .in4(adder_4_out), .out(multiplexer_6_out), .sel(Instr));  // open: in0, in3, in5, in6, in7
  not not_2 (not_2_out, MemWrite);
  D_Flip_Flop #(.trigger("high"), .Pre_Clr_Positions("LEGACY"), .NegatePresetClear("false"), .enable("true"), .NewFFLayout("false")) d_ff_1 (.Q(d_ff_1_q));  // open: clk, D, Qn, preset, en, reset
  // Probe on 13'h139
  RAM #(.addrWidth(10), .dataWidth(32), .bus("separate"), .Select("high")) ram_1 (
    .addr(alu_1_result[11:2]), .din(MDin), .data(ram_1_data), .str(MemWrite), .clk(CLK), .ld(not_2_out));  // open: sel, clr
  Comparator #(.width(13), .mode("twosComplement")) comparator_1 (
    .a(CNT_num), .b(13'h139), .eq(comparator_1_eq), .lt(comparator_1_lt));  // open: gt
  Clock #(.highDuration(1), .lowDuration(1)) clock_1 (.out(clock_1_out));
  Counter #(.width(13), .max('h1fff), .ongoal("stay"), .trigger("rising"), .behavior("old")) counter_1 (
    .count(comparator_1_lt), .Q(CNT_num), .clk(clock_1_out));  // open: load, D, carry, clr, preset
  assign bit_extender_5_out = {{24{ram_1_data[7]}}, ram_1_data[7:0]};  // Bit_Extender bit_extender_5
  assign bit_extender_6_out = {{24{ram_1_data[15]}}, ram_1_data[15:8]};  // Bit_Extender bit_extender_6
  assign bit_extender_7_out = {{24{ram_1_data[23]}}, ram_1_data[23:16]};  // Bit_Extender bit_extender_7
  assign bit_extender_8_out = {{24{ram_1_data[31]}}, ram_1_data[31:24]};  // Bit_Extender bit_extender_8
  Comparator #(.width(32), .mode("unsigned")) comparator_2 (.a(R1), .b(32'h22), .eq(comparator_2_eq));  // open: gt, lt
  nand nand_1 (nand_1_out, d_ff_1_q, comparator_1_eq);
  Multiplexer #(.select(2), .width(32), .disabled("Z"), .enable("false")) multiplexer_7 (
    .in0(bit_extender_5_out), .in1(bit_extender_6_out), .in2(bit_extender_7_out), .in3(bit_extender_8_out),
    .out(multiplexer_7_out), .sel(alu_1_result[1:0]));
  assign CLK = nand_1_out ? clock_1_out : 1'bz;  // Controlled_Buffer controlled_buffer_1
  Pull_Resistor #(.pull(1)) pull_resistor_1 (.node(CLK));
  Multiplexer #(.select(2), .width(32), .disabled("Z"), .enable("false")) multiplexer_8 (
    .in0(alu_1_result), .in1(ram_1_data), .in3(multiplexer_7_out), .out(multiplexer_8_out),
    .sel({lb, \单周期硬布线控制器_1_memtoreg [0]}));  // open: in2
  Multiplexer #(.select(2), .width(32), .disabled("Z"), .enable("false")) multiplexer_9 (
    .in0(multiplexer_8_out), .in1(PC_4), .in2(auipc_res), .out(RDin), .sel({AUIPC, J}));  // open: in3
  and and_2 (and_2_out, ecall, comparator_2_eq);
  and and_3 (and_3_out, ecall, ~comparator_2_eq);  // AND_Gate
  Multiplexer #(.select(1), .width(1), .disabled("Z"), .enable("false")) multiplexer_10 (
    .in0(and_3_out), .in1(1'b0), .out(halt), .sel(Go));
  and and_4 (and_4_out, tunnel, Bge);
  and and_5 (and_5_out, Beq, equal);
  and and_6 (and_6_out, Bne, not_3_out);
  not not_3 (not_3_out, equal);
  or or_4 (J, Instr[2], Instr[0]);
  Comparator #(.width(32), .mode("twosComplement")) comparator_3 (
    .a(R1), .b(MDin), .gt(comparator_3_gt), .eq(comparator_3_eq));  // open: lt
  or or_5 (Instr[1], Beq, Bge, Bne);
  Register #(.width(32), .trigger("rising"), .Select("low")) register_1 (
    .D(MDin), .en(and_2_out), .Q(LedData), .clk(CLK));  // open: clr
  Counter #(.width(16), .max('hffff), .ongoal("stay"), .trigger("rising"), .behavior("old")) counter_2 (
    .count(not_4_out), .Q(\总周期数 ), .clk(CLK));  // open: load, D, carry, clr, preset
  not not_4 (not_4_out, halt);
  or or_6 (PCSrc, and_5_out, and_4_out, and_6_out, J);
  or or_7 (tunnel, comparator_3_gt, comparator_3_eq);

  // Other names for the same wires on the sheet: JALR = Instr[0]; JAL = Instr[2]

  // Notes on the sheet:
  //   中断源
  //   中断等待指示
  //   数码管输出应该用寄存器锁存，否则显示数据只能一闪而过
  //   主电路
  //   数码管输出
  //   指令探针
  //   指令存储器
  //   PC+4
  //   指令字
  //   contents of rom_1 (hex, n*v repeats v):
  //   100493 100006f 100493 200913 300993 100006f 100493 200913 300993 100006f 100493 200913 300993
  //   100006f 100493 200913 300993 404000ef 100413 100493 1f49493 900533 2200893 73 24d493 48463 fedff06f
  //   900533 2200893 73 100493 249493 900533 2200893 73 48463 fedff06f 100493 1f49493 900533 2200893 73
  //   4034d493 900533 2200893 73 4044d493 900533 2200893 73 4044d493 900533 2200893 73 4044d493 900533
  //   2200893 73 4044d493 900533 2200893 73 4044d493 900533 2200893 73 4044d493 900533 2200893 73 4044d493
  //   900533 2200893 73 100413 1f41993 41f9d993 433 c00913 300b13 140413 f47413 800293 100313 499993
  //   89e9b3 1300533 2200893 73 406282b3 fe0294e3 140413 f00f93 1f47433 1c41413 800293 100313 49d993
  //   89e9b3 1300533 2200893 73 406282b3 fe0294e3 1c45413 406b0b33 b0463 f95ff06f 2b3 fff2c293 829293
  //   ff2e293 500533 2200893 73 fff00413 493 84a023 140413 448493 84a023 140413 448493 84a023 140413
  //   448493 84a023 140413 448493 84a023 140413 448493 84a023 140413 448493 84a023 140413 448493 84a023
  //   140413 448493 84a023 140413 448493 84a023 140413 448493 84a023 140413 448493 84a023 140413 448493
  //   84a023 140413 448493 84a023 140413 448493 84a023 140413 448493 84a023 140413 448493 140413 433
  //   3c00493 42983 4aa03 149a2b3 28663 134a023 1442023 ffc48493 fe9412e3 800533 2200893 73 440413 3c00493
  //   fc9416e3 3200893 73 13 430497 900533 2200893 73 430497 900533 2200893 73 430497 900533 2200893 73
  //   430497 900533 2200893 73 430497 900533 2200893 73 430497 900533 2200893 73 430497 900533 2200893 73
  //   430497 900533 2200893 73 a00893 73 fff00293 313 1900413 841413 9700493 940533 2200893 73 5484b3
  //   494b313 fe0306e3 a00893 73 313 1000e13 8400493 849493 8348493 400913 891913 490913 849493 8248493
  //   849493 8148493 891913 490913 891913 490913 932023 12484b3 430313 fffe0e13 fe0e18e3 2000e13 313 30483
  //   900533 2200893 73 130313 fffe0e13 fe0e14e3 a00893 73 f00493 900533 2200893 73 fff48493 fe04d8e3
  //   a00893 73 a00893 73 413 140413 800533 2200893 73 240413 800533 2200893 73 340413 800533 2200893 73
  //   440413 800533 2200893 73 540413 800533 2200893 73 640413 800533 2200893 73 740413 800533 2200893 73
  //   840413 800533 2200893 2200893 73 8067
  //   JAL
  //   JALR
  //   URET
  //   Beq
  //   Bne
  //   MemToReg
  //   MemWrite
  //   AluOP
  //   AluSrcB
  //   RegWrite
  //   S_Tyoe
  //   rs1
  //   rs2
  //   rd
  //   I型
  //   S型
  //   B型
  //   J型
  //   为方便自动评测，需要输出PC，IR，寄存器堆写如数据RDin
  //   RAM写使能MemWrite、RAM写入数据MDin等信号
  //   数据存储器
  //   控制位
  //   暂停节拍，不能为0
  //   戳工具置1进入计数暂停模式，ctrl+k时钟自动运行到对应节拍暂停
  //   ctrl+k关闭时钟连续运行，将控制位置零，进入单步调试模式调试
  //   用这个时钟源需要去掉电路中的其他时钟源
  //   ecall指令相关逻辑
  //   可计数暂停的时钟源
  //   分支跳转相关逻辑
endmodule

// 单周期硬布线控制器
module \单周期硬布线控制器  (
  input  [4:0] OP,
  input  [4:0] Funct,
  input  in_3,
  output [3:0] ALU_OP,
  output uret,
  output MemToReg,
  output ecall,
  output MemWrite,
  output ALU_SRC,
  output RegWrite,
  output S_type,
  output Beq,
  output Bne,
  output Jalr,
  output JAL,
  output AUIPC,
  output lb,
  output Bge
);

  wire \控制信号自动生成_1_ecall ;

  \运算控制器自动生成  \u_运算控制器自动生成_1  (
    .OP2(OP[0]), .OP3(OP[1]), .OP4(OP[2]), .OP5(OP[3]), .OP6(OP[4]), .F12(Funct[0]), .F13(Funct[1]),
    .F14(Funct[2]), .F25(Funct[3]), .F30(Funct[4]), .S0(ALU_OP[0]), .S1(ALU_OP[1]), .S2(ALU_OP[2]),
    .S3(ALU_OP[3]));
  \控制信号自动生成  \u_控制信号自动生成_1  (
    .OP2(OP[0]), .OP3(OP[1]), .OP4(OP[2]), .OP5(OP[3]), .MemToReg(MemToReg), .OP6(OP[4]), .F12(Funct[0]),
    .F13(Funct[1]), .F14(Funct[2]), .F25(Funct[3]), .F30(Funct[4]), .AUIPC(AUIPC), .lb(lb),
    .MemWrite(MemWrite), .Bge(Bge), .ALU_SRC(ALU_SRC), .RegWrite(RegWrite), .ecall(\控制信号自动生成_1_ecall ),
    .S_Type(S_type), .BEQ(Beq), .BNE(Bne), .JALR(Jalr), .JAL(JAL));
  and and_1 (uret, in_3, \控制信号自动生成_1_ecall );
  and and_2 (ecall, ~in_3, \控制信号自动生成_1_ecall );  // AND_Gate

  // Other names for the same wires on the sheet: IR21 = in_3; OP_CODE[4:0] = OP

  // Notes on the sheet:
  //   运算器控制器，根据指令生成运算器功能选择信号
  //   控制信号生成，产生数据通路需要的其他控制信号
endmodule

// 运算器控制器
module \运算控制器自动生成  (
  input  OP2,
  input  OP3,
  input  OP4,
  input  OP5,
  input  OP6,
  input  F12,
  input  F13,
  input  F14,
  input  F25,
  input  F30,
  output S0,
  output S1,
  output S2,
  output S3
);

  wire and_1_out, and_2_out, and_3_out, and_4_out, and_5_out, and_6_out, and_7_out, and_8_out, and_9_out,
       and_10_out, and_11_out, and_12_out, and_13_out, and_14_out, and_15_out, and_16_out, and_17_out,
       and_18_out, and_19_out, and_20_out, and_21_out, and_22_out, and_23_out, and_24_out, and_25_out,
       and_26_out, and_27_out, and_28_out, and_29_out, and_30_out, and_31_out, and_32_out, and_33_out,
       and_34_out, not_1_out, not_2_out, not_3_out, not_4_out, not_5_out, not_6_out, not_7_out, not_8_out,
       not_9_out, not_10_out, not_11_out, not_12_out, not_13_out, not_14_out, not_15_out, not_16_out,
       not_17_out, not_18_out, not_19_out, not_20_out, not_21_out, not_22_out, not_23_out, not_24_out,
       not_25_out, not_26_out, not_27_out, not_28_out, not_29_out, not_30_out, not_31_out, not_32_out,
       not_33_out, not_34_out, not_35_out, not_36_out, not_37_out, not_38_out, not_39_out, not_40_out,
       not_41_out, not_42_out, not_43_out, not_44_out, not_45_out, not_46_out, not_47_out, not_48_out,
       not_49_out, not_50_out, not_51_out, not_52_out, not_53_out, not_54_out, not_55_out, not_56_out,
       not_57_out, not_58_out, not_59_out, not_60_out, not_61_out, not_62_out, not_63_out, not_64_out,
       not_65_out, not_66_out, not_67_out, not_68_out, not_69_out, not_70_out, not_71_out, not_72_out,
       not_73_out, not_74_out, not_75_out, not_76_out, not_77_out, not_78_out, not_79_out, not_80_out,
       not_81_out, not_82_out, not_83_out, not_84_out, not_85_out, not_86_out, not_87_out, not_88_out,
       not_89_out, not_90_out, not_91_out, not_92_out, not_93_out, not_94_out, not_95_out, not_96_out,
       not_97_out, not_98_out, not_99_out, not_100_out, not_101_out, not_102_out, not_103_out, not_104_out,
       not_105_out, not_106_out, not_107_out, not_108_out, not_109_out, not_110_out, not_111_out,
       not_112_out, not_113_out, not_114_out, not_115_out, not_116_out, not_117_out, not_118_out,
       not_119_out, not_120_out, not_121_out, not_122_out, not_123_out, not_124_out, not_125_out,
       not_126_out, not_127_out, not_128_out, not_129_out, not_130_out, not_131_out, not_132_out,
       not_133_out, not_134_out, not_135_out, not_136_out, not_137_out, not_138_out, not_139_out,
       not_140_out, not_141_out, not_142_out, not_143_out, not_144_out, not_145_out, not_146_out,
       not_147_out, not_148_out, not_149_out, not_150_out, not_151_out, not_152_out, not_153_out,
       not_154_out, not_155_out, not_156_out, not_157_out, not_158_out, not_159_out, not_160_out,
       not_161_out, not_162_out, not_163_out, not_164_out, not_165_out, not_166_out, not_167_out,
       not_168_out, not_169_out, not_170_out, not_171_out, not_172_out, not_173_out, not_174_out,
       not_175_out, not_176_out, not_177_out, not_178_out, not_179_out, not_180_out, not_181_out,
       not_182_out, not_183_out, not_184_out, not_185_out, not_186_out, not_187_out, not_188_out,
       not_189_out, not_190_out, not_191_out, not_192_out, not_193_out, not_194_out, not_195_out,
       not_196_out, not_197_out, not_198_out, not_199_out, not_200_out, not_201_out, not_202_out,
       not_203_out, not_204_out, not_205_out, not_206_out, not_207_out, not_208_out, not_209_out, not_210_out;

  not not_1 (not_1_out, F30);
  not not_2 (not_2_out, F25);
  not not_3 (not_3_out, F14);
  not not_4 (not_4_out, F13);
  not not_5 (not_5_out, F12);
  not not_6 (not_6_out, OP6);
  not not_7 (not_7_out, OP3);
  not not_8 (not_8_out, OP2);
  not not_9 (not_9_out, F30);
  not not_10 (not_10_out, F25);
  not not_11 (not_11_out, OP6);
  not not_12 (not_12_out, OP3);
  not not_13 (not_13_out, OP2);
  not not_14 (not_14_out, F30);
  not not_15 (not_15_out, F25);
  not not_16 (not_16_out, F14);
  not not_17 (not_17_out, F12);
  not not_18 (not_18_out, OP6);
  not not_19 (not_19_out, OP3);
  not not_20 (not_20_out, OP2);
  not not_21 (not_21_out, F14);
  not not_22 (not_22_out, F13);
  not not_23 (not_23_out, F12);
  not not_24 (not_24_out, OP6);
  not not_25 (not_25_out, OP5);
  not not_26 (not_26_out, OP3);
  not not_27 (not_27_out, OP2);
  not not_28 (not_28_out, OP6);
  not not_29 (not_29_out, OP5);
  not not_30 (not_30_out, OP3);
  not not_31 (not_31_out, OP2);
  not not_32 (not_32_out, F13);
  not not_33 (not_33_out, F12);
  not not_34 (not_34_out, OP6);
  not not_35 (not_35_out, OP5);
  not not_36 (not_36_out, OP3);
  not not_37 (not_37_out, OP2);
  not not_38 (not_38_out, F14);
  not not_39 (not_39_out, F12);
  not not_40 (not_40_out, OP6);
  not not_41 (not_41_out, OP5);
  not not_42 (not_42_out, OP3);
  not not_43 (not_43_out, OP2);
  not not_44 (not_44_out, F25);
  not not_45 (not_45_out, F13);
  not not_46 (not_46_out, OP6);
  not not_47 (not_47_out, OP5);
  not not_48 (not_48_out, OP3);
  not not_49 (not_49_out, OP2);
  not not_50 (not_50_out, F14);
  not not_51 (not_51_out, F12);
  not not_52 (not_52_out, OP6);
  not not_53 (not_53_out, OP5);
  not not_54 (not_54_out, OP4);
  not not_55 (not_55_out, OP3);
  not not_56 (not_56_out, OP2);
  not not_57 (not_57_out, F14);
  not not_58 (not_58_out, F12);
  not not_59 (not_59_out, OP6);
  not not_60 (not_60_out, OP4);
  not not_61 (not_61_out, OP3);
  not not_62 (not_62_out, OP2);
  not not_63 (not_63_out, F14);
  not not_64 (not_64_out, F13);
  not not_65 (not_65_out, F12);
  not not_66 (not_66_out, OP6);
  not not_67 (not_67_out, OP5);
  not not_68 (not_68_out, OP4);
  not not_69 (not_69_out, OP3);
  not not_70 (not_70_out, OP2);
  not not_71 (not_71_out, F25);
  not not_72 (not_72_out, F14);
  not not_73 (not_73_out, F13);
  not not_74 (not_74_out, F12);
  not not_75 (not_75_out, OP6);
  not not_76 (not_76_out, OP3);
  not not_77 (not_77_out, OP2);
  not not_78 (not_78_out, F30);
  not not_79 (not_79_out, F25);
  not not_80 (not_80_out, OP6);
  not not_81 (not_81_out, OP3);
  not not_82 (not_82_out, OP2);
  not not_83 (not_83_out, F30);
  not not_84 (not_84_out, F25);
  not not_85 (not_85_out, F14);
  not not_86 (not_86_out, F12);
  not not_87 (not_87_out, OP6);
  not not_88 (not_88_out, OP3);
  not not_89 (not_89_out, OP2);
  not not_90 (not_90_out, OP6);
  not not_91 (not_91_out, OP5);
  not not_92 (not_92_out, OP3);
  not not_93 (not_93_out, OP2);
  not not_94 (not_94_out, F14);
  not not_95 (not_95_out, F12);
  not not_96 (not_96_out, OP6);
  not not_97 (not_97_out, OP5);
  not not_98 (not_98_out, OP3);
  not not_99 (not_99_out, OP2);
  not not_100 (not_100_out, F30);
  not not_101 (not_101_out, F25);
  not not_102 (not_102_out, F13);
  not not_103 (not_103_out, OP6);
  not not_104 (not_104_out, OP5);
  not not_105 (not_105_out, OP3);
  not not_106 (not_106_out, OP2);
  not not_107 (not_107_out, F30);
  not not_108 (not_108_out, F25);
  not not_109 (not_109_out, F14);
  not not_110 (not_110_out, F13);
  not not_111 (not_111_out, F12);
  not not_112 (not_112_out, OP6);
  not not_113 (not_113_out, OP3);
  not not_114 (not_114_out, OP2);
  not not_115 (not_115_out, F25);
  not not_116 (not_116_out, F14);
  not not_117 (not_117_out, F13);
  not not_118 (not_118_out, F12);
  not not_119 (not_119_out, OP6);
  not not_120 (not_120_out, OP3);
  not not_121 (not_121_out, OP2);
  not not_122 (not_122_out, F30);
  not not_123 (not_123_out, F25);
  not not_124 (not_124_out, OP6);
  not not_125 (not_125_out, OP3);
  not not_126 (not_126_out, OP2);
  not not_127 (not_127_out, F30);
  not not_128 (not_128_out, F25);
  not not_129 (not_129_out, F14);
  not not_130 (not_130_out, OP6);
  not not_131 (not_131_out, OP3);
  not not_132 (not_132_out, OP2);
  not not_133 (not_133_out, F14);
  not not_134 (not_134_out, F13);
  not not_135 (not_135_out, F12);
  not not_136 (not_136_out, OP6);
  not not_137 (not_137_out, OP5);
  not not_138 (not_138_out, OP3);
  not not_139 (not_139_out, OP2);
  not not_140 (not_140_out, OP6);
  not not_141 (not_141_out, OP5);
  not not_142 (not_142_out, OP3);
  not not_143 (not_143_out, OP2);
  not not_144 (not_144_out, F14);
  not not_145 (not_145_out, F12);
  not not_146 (not_146_out, OP6);
  not not_147 (not_147_out, OP5);
  not not_148 (not_148_out, OP4);
  not not_149 (not_149_out, OP3);
  not not_150 (not_150_out, OP2);
  not not_151 (not_151_out, F14);
  not not_152 (not_152_out, F12);
  not not_153 (not_153_out, OP6);
  not not_154 (not_154_out, OP4);
  not not_155 (not_155_out, OP3);
  not not_156 (not_156_out, OP2);
  not not_157 (not_157_out, F14);
  not not_158 (not_158_out, OP6);
  not not_159 (not_159_out, OP5);
  not not_160 (not_160_out, OP3);
  not not_161 (not_161_out, OP2);
  not not_162 (not_162_out, F14);
  not not_163 (not_163_out, F13);
  not not_164 (not_164_out, F12);
  not not_165 (not_165_out, OP6);
  not not_166 (not_166_out, OP5);
  not not_167 (not_167_out, OP4);
  not not_168 (not_168_out, OP3);
  not not_169 (not_169_out, OP2);
  not not_170 (not_170_out, F30);
  not not_171 (not_171_out, F25);
  not not_172 (not_172_out, F12);
  not not_173 (not_173_out, OP6);
  not not_174 (not_174_out, OP3);
  not not_175 (not_175_out, OP2);
  not not_176 (not_176_out, F30);
  not not_177 (not_177_out, F25);
  not not_178 (not_178_out, F14);
  not not_179 (not_179_out, F12);
  not not_180 (not_180_out, OP6);
  not not_181 (not_181_out, OP3);
  not not_182 (not_182_out, OP2);
  not not_183 (not_183_out, F30);
  not not_184 (not_184_out, F25);
  not not_185 (not_185_out, F14);
  not not_186 (not_186_out, OP6);
  not not_187 (not_187_out, OP3);
  not not_188 (not_188_out, OP2);
  not not_189 (not_189_out, F12);
  not not_190 (not_190_out, OP6);
  not not_191 (not_191_out, OP5);
  not not_192 (not_192_out, OP3);
  not not_193 (not_193_out, OP2);
  not not_194 (not_194_out, F13);
  not not_195 (not_195_out, F12);
  not not_196 (not_196_out, OP6);
  not not_197 (not_197_out, OP5);
  not not_198 (not_198_out, OP3);
  not not_199 (not_199_out, OP2);
  not not_200 (not_200_out, F14);
  not not_201 (not_201_out, F12);
  not not_202 (not_202_out, OP6);
  not not_203 (not_203_out, OP5);
  not not_204 (not_204_out, OP3);
  not not_205 (not_205_out, OP2);
  not not_206 (not_206_out, F14);
  not not_207 (not_207_out, OP6);
  not not_208 (not_208_out, OP5);
  not not_209 (not_209_out, OP3);
  not not_210 (not_210_out, OP2);
  and and_1 (and_1_out, not_1_out, not_2_out, not_3_out, not_4_out, not_5_out, not_6_out, OP5, OP4, not_7_out, not_8_out);
  and and_2 (and_2_out, not_9_out, not_10_out, F14, F13, F12, not_11_out, OP5, OP4, not_12_out, not_13_out);
  and and_3 (and_3_out, not_14_out, not_15_out, not_16_out, F13, not_17_out, not_18_out, OP5, OP4, not_19_out, not_20_out);
  and and_4 (and_4_out, not_21_out, not_22_out, not_23_out, not_24_out, not_25_out, OP4, not_26_out, not_27_out);
  and and_5 (and_5_out, F14, F13, F12, not_28_out, not_29_out, OP4, not_30_out, not_31_out);
  and and_6 (and_6_out, F14, not_32_out, not_33_out, not_34_out, not_35_out, OP4, not_36_out, not_37_out);
  and and_7 (and_7_out, not_38_out, F13, not_39_out, not_40_out, not_41_out, OP4, not_42_out, not_43_out);
  and and_8 (and_8_out, F30, not_44_out, F14, not_45_out, F12, not_46_out, not_47_out, OP4, not_48_out, not_49_out);
  and and_9 (and_9_out, not_50_out, F13, not_51_out, not_52_out, not_53_out, not_54_out, not_55_out, not_56_out);
  and and_10 (and_10_out, not_57_out, F13, not_58_out, not_59_out, OP5, not_60_out, not_61_out, not_62_out);
  and and_11 (and_11_out, not_63_out, not_64_out, not_65_out, not_66_out, not_67_out, not_68_out, not_69_out, not_70_out);
  and and_12 (and_12_out, F30, not_71_out, not_72_out, not_73_out, not_74_out, not_75_out, OP5, OP4, not_76_out, not_77_out);
  and and_13 (and_13_out, not_78_out, not_79_out, F14, F13, F12, not_80_out, OP5, OP4, not_81_out, not_82_out);
  and and_14 (and_14_out, not_83_out, not_84_out, not_85_out, F13, not_86_out, not_87_out, OP5, OP4, not_88_out, not_89_out);
  and and_15 (and_15_out, F14, F13, F12, not_90_out, not_91_out, OP4, not_92_out, not_93_out);
  and and_16 (and_16_out, not_94_out, F13, not_95_out, not_96_out, not_97_out, OP4, not_98_out, not_99_out);
  and and_17 (and_17_out, not_100_out, not_101_out, F14, not_102_out, F12, not_103_out, not_104_out, OP4, not_105_out, not_106_out);
  and and_18 (and_18_out, not_107_out, not_108_out, not_109_out, not_110_out, not_111_out, not_112_out, OP5, OP4, not_113_out, not_114_out);
  and and_19 (and_19_out, F30, not_115_out, not_116_out, not_117_out, not_118_out, not_119_out, OP5, OP4, not_120_out, not_121_out);
  and and_20 (and_20_out, not_122_out, not_123_out, F14, F13, F12, not_124_out, OP5, OP4, not_125_out, not_126_out);
  and and_21 (and_21_out, not_127_out, not_128_out, not_129_out, F13, F12, not_130_out, OP5, OP4, not_131_out, not_132_out);
  and and_22 (and_22_out, not_133_out, not_134_out, not_135_out, not_136_out, not_137_out, OP4, not_138_out, not_139_out);
  and and_23 (and_23_out, F14, F13, F12, not_140_out, not_141_out, OP4, not_142_out, not_143_out);
  and and_24 (and_24_out, not_144_out, F13, not_145_out, not_146_out, not_147_out, not_148_out, not_149_out, not_150_out);
  and and_25 (and_25_out, not_151_out, F13, not_152_out, not_153_out, OP5, not_154_out, not_155_out, not_156_out);
  and and_26 (and_26_out, not_157_out, F13, F12, not_158_out, not_159_out, OP4, not_160_out, not_161_out);
  and and_27 (and_27_out, not_162_out, not_163_out, not_164_out, not_165_out, not_166_out, not_167_out, not_168_out, not_169_out);
  and and_28 (and_28_out, not_170_out, not_171_out, F14, F13, not_172_out, not_173_out, OP5, OP4, not_174_out, not_175_out);
  and and_29 (and_29_out, not_176_out, not_177_out, not_178_out, F13, not_179_out, not_180_out, OP5, OP4, not_181_out, not_182_out);
  and and_30 (and_30_out, not_183_out, not_184_out, not_185_out, F13, F12, not_186_out, OP5, OP4, not_187_out, not_188_out);
  and and_31 (and_31_out, F14, F13, not_189_out, not_190_out, not_191_out, OP4, not_192_out, not_193_out);
  and and_32 (and_32_out, F14, not_194_out, not_195_out, not_196_out, not_197_out, OP4, not_198_out, not_199_out);
  and and_33 (and_33_out, not_200_out, F13, not_201_out, not_202_out, not_203_out, OP4, not_204_out, not_205_out);
  and and_34 (and_34_out, not_206_out, F13, F12, not_207_out, not_208_out, OP4, not_209_out, not_210_out);
  or or_1 (S0, and_1_out, and_2_out, and_3_out, and_4_out, and_5_out, and_6_out, and_7_out, and_8_out, and_9_out, and_10_out, and_11_out);
  or or_2 (S1, and_12_out, and_13_out, and_14_out, and_15_out, and_16_out, and_17_out);
  or or_3 (S2, and_18_out, and_19_out, and_20_out, and_21_out, and_22_out, and_23_out, and_24_out, and_25_out, and_26_out, and_27_out);
  or or_4 (S3, and_28_out, and_29_out, and_30_out, and_31_out, and_32_out, and_33_out, and_34_out);
endmodule

// 控制信号生成
module \控制信号自动生成  (
  input  OP2,
  input  OP3,
  input  OP4,
  input  OP5,
  input  OP6,
  input  F12,
  input  F13,
  input  F14,
  input  F25,
  input  F30,
  output MemToReg,
  output AUIPC,
  output lb,
  output MemWrite,
  output Bge,
  output ALU_SRC,
  output RegWrite,
  output ecall,
  output S_Type,
  output BEQ,
  output BNE,
  output JALR,
  output JAL
);

  wire and_1_out, and_2_out, and_7_out, and_8_out, and_9_out, and_10_out, and_11_out, and_12_out, and_13_out,
       and_14_out, and_15_out, and_16_out, and_17_out, and_18_out, and_19_out, and_20_out, and_21_out,
       and_22_out, and_23_out, and_24_out, and_25_out, and_26_out, and_27_out, and_28_out, and_29_out,
       and_30_out, and_31_out, and_32_out, and_33_out, and_34_out, and_35_out, and_36_out, and_37_out,
       and_38_out, and_39_out, not_1_out, not_2_out, not_3_out, not_4_out, not_5_out, not_6_out, not_7_out,
       not_8_out, not_9_out, not_10_out, not_11_out, not_12_out, not_13_out, not_14_out, not_15_out,
       not_16_out, not_17_out, not_18_out, not_19_out, not_20_out, not_21_out, not_22_out, not_23_out,
       not_24_out, not_25_out, not_26_out, not_27_out, not_28_out, not_29_out, not_30_out, not_31_out,
       not_32_out, not_33_out, not_34_out, not_35_out, not_36_out, not_37_out, not_38_out, not_39_out,
       not_40_out, not_41_out, not_42_out, not_43_out, not_44_out, not_45_out, not_46_out, not_47_out,
       not_48_out, not_49_out, not_50_out, not_51_out, not_52_out, not_53_out, not_54_out, not_55_out,
       not_56_out, not_57_out, not_58_out, not_59_out, not_60_out, not_61_out, not_62_out, not_63_out,
       not_64_out, not_65_out, not_66_out, not_67_out, not_68_out, not_69_out, not_70_out, not_71_out,
       not_72_out, not_73_out, not_74_out, not_75_out, not_76_out, not_77_out, not_78_out, not_79_out,
       not_80_out, not_81_out, not_82_out, not_83_out, not_84_out, not_85_out, not_86_out, not_87_out,
       not_88_out, not_89_out, not_90_out, not_91_out, not_92_out, not_93_out, not_94_out, not_95_out,
       not_96_out, not_97_out, not_98_out, not_99_out, not_100_out, not_101_out, not_102_out, not_103_out,
       not_104_out, not_105_out, not_106_out, not_107_out, not_108_out, not_109_out, not_110_out,
       not_111_out, not_112_out, not_113_out, not_114_out, not_115_out, not_116_out, not_117_out,
       not_118_out, not_119_out, not_120_out, not_121_out, not_122_out, not_123_out, not_124_out,
       not_125_out, not_126_out, not_127_out, not_128_out, not_129_out, not_130_out, not_131_out,
       not_132_out, not_133_out, not_134_out, not_135_out, not_136_out, not_137_out, not_138_out,
       not_139_out, not_140_out, not_141_out, not_142_out, not_143_out, not_144_out, not_145_out,
       not_146_out, not_147_out, not_148_out, not_149_out, not_150_out, not_151_out, not_152_out,
       not_153_out, not_154_out, not_155_out, not_156_out, not_157_out, not_158_out, not_159_out,
       not_160_out, not_161_out, not_162_out, not_163_out, not_164_out, not_165_out, not_166_out,
       not_167_out, not_168_out, not_169_out, not_170_out, not_171_out, not_172_out, not_173_out,
       not_174_out, not_175_out, not_176_out, not_177_out, not_178_out, not_179_out, not_180_out,
       not_181_out, not_182_out, not_183_out, not_184_out, not_185_out, not_186_out, not_187_out,
       not_188_out, not_189_out, not_190_out, not_191_out, not_192_out, not_193_out, not_194_out,
       not_195_out, not_196_out, not_197_out, not_198_out, not_199_out, not_200_out, not_201_out,
       not_202_out, not_203_out, not_204_out, not_205_out, not_206_out, not_207_out, not_208_out,
       not_209_out, not_210_out, not_211_out, not_212_out, not_213_out, not_214_out, not_215_out,
       not_216_out, not_217_out, not_218_out, not_219_out, not_220_out, not_221_out, not_222_out,
       not_223_out, not_224_out, not_225_out, not_226_out, not_227_out, not_228_out, not_229_out,
       not_230_out, not_231_out, not_232_out, not_233_out, not_234_out, not_235_out, not_236_out,
       not_237_out, not_238_out, not_239_out, not_240_out, not_241_out, not_242_out, not_243_out,
       not_244_out, not_245_out, not_246_out, not_247_out, not_248_out, not_249_out, not_250_out,
       not_251_out, not_252_out, not_253_out, not_254_out, not_255_out, not_256_out, not_257_out,
       not_258_out, not_259_out, not_260_out, not_261_out, not_262_out, not_263_out;

  not not_1 (not_1_out, F14);
  not not_2 (not_2_out, F12);
  not not_3 (not_3_out, OP6);
  not not_4 (not_4_out, OP5);
  not not_5 (not_5_out, OP4);
  not not_6 (not_6_out, OP3);
  not not_7 (not_7_out, OP2);
  not not_8 (not_8_out, F14);
  not not_9 (not_9_out, F13);
  not not_10 (not_10_out, F12);
  not not_11 (not_11_out, OP6);
  not not_12 (not_12_out, OP5);
  not not_13 (not_13_out, OP4);
  not not_14 (not_14_out, OP3);
  not not_15 (not_15_out, OP2);
  not not_16 (not_16_out, OP6);
  not not_17 (not_17_out, OP5);
  not not_18 (not_18_out, OP3);
  not not_19 (not_19_out, F14);
  not not_20 (not_20_out, F13);
  not not_21 (not_21_out, F12);
  not not_22 (not_22_out, OP6);
  not not_23 (not_23_out, OP5);
  not not_24 (not_24_out, OP4);
  not not_25 (not_25_out, OP3);
  not not_26 (not_26_out, OP2);
  not not_27 (not_27_out, F14);
  not not_28 (not_28_out, F12);
  not not_29 (not_29_out, OP6);
  not not_30 (not_30_out, OP4);
  not not_31 (not_31_out, OP3);
  not not_32 (not_32_out, OP2);
  not not_33 (not_33_out, F13);
  not not_34 (not_34_out, OP4);
  not not_35 (not_35_out, OP3);
  not not_36 (not_36_out, OP2);
  not not_37 (not_37_out, F14);
  not not_38 (not_38_out, F13);
  not not_39 (not_39_out, F12);
  not not_40 (not_40_out, OP6);
  not not_41 (not_41_out, OP5);
  not not_42 (not_42_out, OP3);
  not not_43 (not_43_out, OP2);
  not not_44 (not_44_out, OP6);
  not not_45 (not_45_out, OP5);
  not not_46 (not_46_out, OP3);
  not not_47 (not_47_out, OP2);
  not not_48 (not_48_out, F12);
  not not_49 (not_49_out, OP6);
  not not_50 (not_50_out, OP5);
  not not_51 (not_51_out, OP3);
  not not_52 (not_52_out, OP2);
  not not_53 (not_53_out, F13);
  not not_54 (not_54_out, F12);
  not not_55 (not_55_out, OP6);
  not not_56 (not_56_out, OP5);
  not not_57 (not_57_out, OP3);
  not not_58 (not_58_out, OP2);
  not not_59 (not_59_out, F14);
  not not_60 (not_60_out, F12);
  not not_61 (not_61_out, OP6);
  not not_62 (not_62_out, OP5);
  not not_63 (not_63_out, OP3);
  not not_64 (not_64_out, OP2);
  not not_65 (not_65_out, F30);
  not not_66 (not_66_out, F25);
  not not_67 (not_67_out, F14);
  not not_68 (not_68_out, F13);
  not not_69 (not_69_out, OP6);
  not not_70 (not_70_out, OP5);
  not not_71 (not_71_out, OP3);
  not not_72 (not_72_out, OP2);
  not not_73 (not_73_out, F30);
  not not_74 (not_74_out, F25);
  not not_75 (not_75_out, F13);
  not not_76 (not_76_out, OP6);
  not not_77 (not_77_out, OP5);
  not not_78 (not_78_out, OP3);
  not not_79 (not_79_out, OP2);
  not not_80 (not_80_out, F25);
  not not_81 (not_81_out, F13);
  not not_82 (not_82_out, OP6);
  not not_83 (not_83_out, OP5);
  not not_84 (not_84_out, OP3);
  not not_85 (not_85_out, OP2);
  not not_86 (not_86_out, F14);
  not not_87 (not_87_out, F12);
  not not_88 (not_88_out, OP6);
  not not_89 (not_89_out, OP5);
  not not_90 (not_90_out, OP4);
  not not_91 (not_91_out, OP3);
  not not_92 (not_92_out, OP2);
  not not_93 (not_93_out, F14);
  not not_94 (not_94_out, F12);
  not not_95 (not_95_out, OP6);
  not not_96 (not_96_out, OP4);
  not not_97 (not_97_out, OP3);
  not not_98 (not_98_out, OP2);
  not not_99 (not_99_out, F14);
  not not_100 (not_100_out, F13);
  not not_101 (not_101_out, F12);
  not not_102 (not_102_out, OP4);
  not not_103 (not_103_out, OP3);
  not not_104 (not_104_out, F14);
  not not_105 (not_105_out, OP6);
  not not_106 (not_106_out, OP5);
  not not_107 (not_107_out, OP3);
  not not_108 (not_108_out, OP2);
  not not_109 (not_109_out, F14);
  not not_110 (not_110_out, F13);
  not not_111 (not_111_out, F12);
  not not_112 (not_112_out, OP6);
  not not_113 (not_113_out, OP5);
  not not_114 (not_114_out, OP4);
  not not_115 (not_115_out, OP3);
  not not_116 (not_116_out, OP2);
  not not_117 (not_117_out, F30);
  not not_118 (not_118_out, F25);
  not not_119 (not_119_out, F14);
  not not_120 (not_120_out, F13);
  not not_121 (not_121_out, F12);
  not not_122 (not_122_out, OP6);
  not not_123 (not_123_out, OP3);
  not not_124 (not_124_out, OP2);
  not not_125 (not_125_out, F25);
  not not_126 (not_126_out, F14);
  not not_127 (not_127_out, F13);
  not not_128 (not_128_out, F12);
  not not_129 (not_129_out, OP6);
  not not_130 (not_130_out, OP3);
  not not_131 (not_131_out, OP2);
  not not_132 (not_132_out, F30);
  not not_133 (not_133_out, F25);
  not not_134 (not_134_out, OP6);
  not not_135 (not_135_out, OP3);
  not not_136 (not_136_out, OP2);
  not not_137 (not_137_out, F30);
  not not_138 (not_138_out, F25);
  not not_139 (not_139_out, F12);
  not not_140 (not_140_out, OP6);
  not not_141 (not_141_out, OP3);
  not not_142 (not_142_out, OP2);
  not not_143 (not_143_out, F30);
  not not_144 (not_144_out, F25);
  not not_145 (not_145_out, F14);
  not not_146 (not_146_out, F12);
  not not_147 (not_147_out, OP6);
  not not_148 (not_148_out, OP3);
  not not_149 (not_149_out, OP2);
  not not_150 (not_150_out, F30);
  not not_151 (not_151_out, F25);
  not not_152 (not_152_out, F14);
  not not_153 (not_153_out, OP6);
  not not_154 (not_154_out, OP3);
  not not_155 (not_155_out, OP2);
  not not_156 (not_156_out, F14);
  not not_157 (not_157_out, F13);
  not not_158 (not_158_out, F12);
  not not_159 (not_159_out, OP6);
  not not_160 (not_160_out, OP5);
  not not_161 (not_161_out, OP3);
  not not_162 (not_162_out, OP2);
  not not_163 (not_163_out, OP6);
  not not_164 (not_164_out, OP5);
  not not_165 (not_165_out, OP3);
  not not_166 (not_166_out, OP2);
  not not_167 (not_167_out, F12);
  not not_168 (not_168_out, OP6);
  not not_169 (not_169_out, OP5);
  not not_170 (not_170_out, OP3);
  not not_171 (not_171_out, OP2);
  not not_172 (not_172_out, F13);
  not not_173 (not_173_out, F12);
  not not_174 (not_174_out, OP6);
  not not_175 (not_175_out, OP5);
  not not_176 (not_176_out, OP3);
  not not_177 (not_177_out, OP2);
  not not_178 (not_178_out, F14);
  not not_179 (not_179_out, F12);
  not not_180 (not_180_out, OP6);
  not not_181 (not_181_out, OP5);
  not not_182 (not_182_out, OP3);
  not not_183 (not_183_out, OP2);
  not not_184 (not_184_out, F30);
  not not_185 (not_185_out, F25);
  not not_186 (not_186_out, F14);
  not not_187 (not_187_out, F13);
  not not_188 (not_188_out, OP6);
  not not_189 (not_189_out, OP5);
  not not_190 (not_190_out, OP3);
  not not_191 (not_191_out, OP2);
  not not_192 (not_192_out, F30);
  not not_193 (not_193_out, F25);
  not not_194 (not_194_out, F13);
  not not_195 (not_195_out, OP6);
  not not_196 (not_196_out, OP5);
  not not_197 (not_197_out, OP3);
  not not_198 (not_198_out, OP2);
  not not_199 (not_199_out, F25);
  not not_200 (not_200_out, F13);
  not not_201 (not_201_out, OP6);
  not not_202 (not_202_out, OP5);
  not not_203 (not_203_out, OP3);
  not not_204 (not_204_out, OP2);
  not not_205 (not_205_out, F14);
  not not_206 (not_206_out, F12);
  not not_207 (not_207_out, OP6);
  not not_208 (not_208_out, OP5);
  not not_209 (not_209_out, OP4);
  not not_210 (not_210_out, OP3);
  not not_211 (not_211_out, OP2);
  not not_212 (not_212_out, OP4);
  not not_213 (not_213_out, F14);
  not not_214 (not_214_out, F13);
  not not_215 (not_215_out, F12);
  not not_216 (not_216_out, OP4);
  not not_217 (not_217_out, OP3);
  not not_218 (not_218_out, OP6);
  not not_219 (not_219_out, OP5);
  not not_220 (not_220_out, OP3);
  not not_221 (not_221_out, F14);
  not not_222 (not_222_out, OP6);
  not not_223 (not_223_out, OP5);
  not not_224 (not_224_out, OP3);
  not not_225 (not_225_out, OP2);
  not not_226 (not_226_out, F14);
  not not_227 (not_227_out, F13);
  not not_228 (not_228_out, F12);
  not not_229 (not_229_out, OP6);
  not not_230 (not_230_out, OP5);
  not not_231 (not_231_out, OP4);
  not not_232 (not_232_out, OP3);
  not not_233 (not_233_out, OP2);
  not not_234 (not_234_out, F30);
  not not_235 (not_235_out, F25);
  not not_236 (not_236_out, F14);
  not not_237 (not_237_out, F13);
  not not_238 (not_238_out, F12);
  not not_239 (not_239_out, OP3);
  not not_240 (not_240_out, OP2);
  not not_241 (not_241_out, F14);
  not not_242 (not_242_out, F12);
  not not_243 (not_243_out, OP6);
  not not_244 (not_244_out, OP4);
  not not_245 (not_245_out, OP3);
  not not_246 (not_246_out, OP2);
  not not_247 (not_247_out, F14);
  not not_248 (not_248_out, F13);
  not not_249 (not_249_out, F12);
  not not_250 (not_250_out, OP4);
  not not_251 (not_251_out, OP3);
  not not_252 (not_252_out, OP2);
  not not_253 (not_253_out, F14);
  not not_254 (not_254_out, F13);
  not not_255 (not_255_out, OP4);
  not not_256 (not_256_out, OP3);
  not not_257 (not_257_out, OP2);
  not not_258 (not_258_out, F14);
  not not_259 (not_259_out, F13);
  not not_260 (not_260_out, F12);
  not not_261 (not_261_out, OP4);
  not not_262 (not_262_out, OP3);
  not not_263 (not_263_out, OP4);
  and and_1 (and_1_out, not_1_out, F13, not_2_out, not_3_out, not_4_out, not_5_out, not_6_out, not_7_out);
  and and_2 (and_2_out, not_8_out, not_9_out, not_10_out, not_11_out, not_12_out, not_13_out, not_14_out, not_15_out);
  and and_3 (AUIPC, not_16_out, not_17_out, OP4, not_18_out, OP2);
  and and_4 (lb, not_19_out, not_20_out, not_21_out, not_22_out, not_23_out, not_24_out, not_25_out, not_26_out);
  and and_5 (MemWrite, not_27_out, F13, not_28_out, not_29_out, OP5, not_30_out, not_31_out, not_32_out);
  and and_6 (Bge, F14, not_33_out, F12, OP6, OP5, not_34_out, not_35_out, not_36_out);
  and and_7 (and_7_out, not_37_out, not_38_out, not_39_out, not_40_out, not_41_out, OP4, not_42_out, not_43_out);
  and and_8 (and_8_out, F14, F13, F12, not_44_out, not_45_out, OP4, not_46_out, not_47_out);
  and and_9 (and_9_out, F14, F13, not_48_out, not_49_out, not_50_out, OP4, not_51_out, not_52_out);
  and and_10 (and_10_out, F14, not_53_out, not_54_out, not_55_out, not_56_out, OP4, not_57_out, not_58_out);
  and and_11 (and_11_out, not_59_out, F13, not_60_out, not_61_out, not_62_out, OP4, not_63_out, not_64_out);
  and and_12 (and_12_out, not_65_out, not_66_out, not_67_out, not_68_out, F12, not_69_out, not_70_out, OP4, not_71_out, not_72_out);
  and and_13 (and_13_out, not_73_out, not_74_out, F14, not_75_out, F12, not_76_out, not_77_out, OP4, not_78_out, not_79_out);
  and and_14 (and_14_out, F30, not_80_out, F14, not_81_out, F12, not_82_out, not_83_out, OP4, not_84_out, not_85_out);
  and and_15 (and_15_out, not_86_out, F13, not_87_out, not_88_out, not_89_out, not_90_out, not_91_out, not_92_out);
  and and_16 (and_16_out, not_93_out, F13, not_94_out, not_95_out, OP5, not_96_out, not_97_out, not_98_out);
  and and_17 (and_17_out, not_99_out, not_100_out, not_101_out, OP6, OP5, not_102_out, not_103_out, OP2);
  and and_18 (and_18_out, not_104_out, F13, F12, not_105_out, not_106_out, OP4, not_107_out, not_108_out);
  and and_19 (and_19_out, not_109_out, not_110_out, not_111_out, not_112_out, not_113_out, not_114_out, not_115_out, not_116_out);
  and and_20 (and_20_out, not_117_out, not_118_out, not_119_out, not_120_out, not_121_out, not_122_out, OP5, OP4, not_123_out, not_124_out);
  and and_21 (and_21_out, F30, not_125_out, not_126_out, not_127_out, not_128_out, not_129_out, OP5, OP4, not_130_out, not_131_out);
  and and_22 (and_22_out, not_132_out, not_133_out, F14, F13, F12, not_134_out, OP5, OP4, not_135_out, not_136_out);
  and and_23 (and_23_out, not_137_out, not_138_out, F14, F13, not_139_out, not_140_out, OP5, OP4, not_141_out, not_142_out);
  and and_24 (and_24_out, not_143_out, not_144_out, not_145_out, F13, not_146_out, not_147_out, OP5, OP4, not_148_out, not_149_out);
  and and_25 (and_25_out, not_150_out, not_151_out, not_152_out, F13, F12, not_153_out, OP5, OP4, not_154_out, not_155_out);
  and and_26 (and_26_out, not_156_out, not_157_out, not_158_out, not_159_out, not_160_out, OP4, not_161_out, not_162_out);
  and and_27 (and_27_out, F14, F13, F12, not_163_out, not_164_out, OP4, not_165_out, not_166_out);
  and and_28 (and_28_out, F14, F13, not_167_out, not_168_out, not_169_out, OP4, not_170_out, not_171_out);
  and and_29 (and_29_out, F14, not_172_out, not_173_out, not_174_out, not_175_out, OP4, not_176_out, not_177_out);
  and and_30 (and_30_out, not_178_out, F13, not_179_out, not_180_out, not_181_out, OP4, not_182_out, not_183_out);
  and and_31 (and_31_out, not_184_out, not_185_out, not_186_out, not_187_out, F12, not_188_out, not_189_out, OP4, not_190_out, not_191_out);
  and and_32 (and_32_out, not_192_out, not_193_out, F14, not_194_out, F12, not_195_out, not_196_out, OP4, not_197_out, not_198_out);
  and and_33 (and_33_out, F30, not_199_out, F14, not_200_out, F12, not_201_out, not_202_out, OP4, not_203_out, not_204_out);
  and and_34 (and_34_out, not_205_out, F13, not_206_out, not_207_out, not_208_out, not_209_out, not_210_out, not_211_out);
  and and_35 (and_35_out, OP6, OP5, not_212_out, OP3, OP2);
  and and_36 (and_36_out, not_213_out, not_214_out, not_215_out, OP6, OP5, not_216_out, not_217_out, OP2);
  and and_37 (and_37_out, not_218_out, not_219_out, OP4, not_220_out, OP2);
  and and_38 (and_38_out, not_221_out, F13, F12, not_222_out, not_223_out, OP4, not_224_out, not_225_out);
  and and_39 (and_39_out, not_226_out, not_227_out, not_228_out, not_229_out, not_230_out, not_231_out, not_232_out, not_233_out);
  and and_40 (ecall, not_234_out, not_235_out, not_236_out, not_237_out, not_238_out, OP6, OP5, OP4, not_239_out, not_240_out);
  and and_41 (S_Type, not_241_out, F13, not_242_out, not_243_out, OP5, not_244_out, not_245_out, not_246_out);
  and and_42 (BEQ, not_247_out, not_248_out, not_249_out, OP6, OP5, not_250_out, not_251_out, not_252_out);
  and and_43 (BNE, not_253_out, not_254_out, F12, OP6, OP5, not_255_out, not_256_out, not_257_out);
  and and_44 (JALR, not_258_out, not_259_out, not_260_out, OP6, OP5, not_261_out, not_262_out, OP2);
  and and_45 (JAL, OP6, OP5, not_263_out, OP3, OP2);
  or or_1 (MemToReg, and_1_out, and_2_out);
  or or_2 (ALU_SRC, and_7_out, and_8_out, and_9_out, and_10_out, and_11_out, and_12_out, and_13_out, and_14_out, and_15_out, and_16_out, and_17_out, and_18_out, and_19_out);
  or or_3 (RegWrite, and_20_out, and_21_out, and_22_out, and_23_out, and_24_out, and_25_out, and_26_out, and_27_out, and_28_out, and_29_out, and_30_out, and_31_out, and_32_out, and_33_out, and_34_out, and_35_out, and_36_out, and_37_out, and_38_out, and_39_out);
endmodule

// ALU
module ALU (
  input  [31:0] X,
  input  [31:0] Y,
  input  [3:0] AluOP,
  output out_4,
  output Equal,
  output out_6,
  output [31:0] Result,
  output [31:0] Result_2
);

  wire [0:0] comparator_1_lt, comparator_2_lt;
  wire [31:0] adder_1_out, AND_out, divider_1_out, divider_1_rem, multiplier_1_cout, multiplier_1_out,
       NOR_out, OR_out, shifter_1_out, shifter_2_out, shifter_3_out, subtractor_1_out, XOR_out;

  assign AND_out = X & Y;  // AND_Gate AND, 32 bits wide
  assign OR_out = X | Y;  // OR_Gate OR, 32 bits wide
  Shifter #(.width(32), .shift("ll")) shifter_1 (.in(X), .\dist (Y[4:0]), .out(shifter_1_out));
  Shifter #(.width(32), .shift("ar")) shifter_2 (.in(X), .\dist (Y[4:0]), .out(shifter_2_out));
  Shifter #(.width(32), .shift("lr")) shifter_3 (.in(X), .\dist (Y[4:0]), .out(shifter_3_out));
  Multiplier #(.width(32)) multiplier_1 (.a(X), .b(Y), .out(multiplier_1_out), .cout(multiplier_1_cout));  // open: cin
  Divider #(.width(32)) divider_1 (.a(X), .b(Y), .out(divider_1_out), .rem(divider_1_rem));  // open: upper
  Adder #(.width(32)) adder_1 (.a(X), .b(Y), .out(adder_1_out));  // open: cin, cout
  Subtractor #(.width(32)) subtractor_1 (.a(X), .b(Y), .out(subtractor_1_out));  // open: bin, bout
  assign XOR_out = X ^ Y;  // XOR_Gate XOR, 32 bits wide
  assign NOR_out = ~(X | Y);  // NOR_Gate NOR, 32 bits wide
  Comparator #(.width(32), .mode("twosComplement")) comparator_1 (
    .a(X), .b(Y), .eq(Equal), .lt(comparator_1_lt[0]));  // open: gt
  Comparator #(.width(32), .mode("unsigned")) comparator_2 (.a(X), .b(Y), .lt(comparator_2_lt[0]));  // open: gt, eq
  Multiplexer #(.select(4), .width(32), .disabled("Z"), .enable("false")) multiplexer_1 (
    .in0(shifter_1_out), .in1(shifter_2_out), .in2(shifter_3_out), .in3(multiplier_1_out),
    .in4(divider_1_out), .in5(adder_1_out), .in6(subtractor_1_out), .in7(AND_out), .in8(OR_out),
    .in9(XOR_out), .in10(NOR_out), .in11({{31{1'b0}}, comparator_1_lt[0]}),
    .in12({{31{1'b0}}, comparator_2_lt[0]}), .in13({32{1'b0}}), .in14({32{1'b0}}), .in15({32{1'b0}}),
    .out(Result), .sel(AluOP));
  Multiplexer #(.select(4), .width(32), .disabled("Z"), .enable("false")) multiplexer_2 (
    .in0({32{1'b0}}), .in1({32{1'b0}}), .in2({32{1'b0}}), .in3(multiplier_1_cout), .in4(divider_1_rem),
    .in5({32{1'b0}}), .in6({32{1'b0}}), .in7({32{1'b0}}), .in8({32{1'b0}}), .in9({32{1'b0}}),
    .in10({32{1'b0}}), .in11({32{1'b0}}), .in12({32{1'b0}}), .in13({32{1'b0}}), .in14({32{1'b0}}),
    .in15({32{1'b0}}), .out(Result_2), .sel(AluOP));
  Multiplexer #(.select(4), .width(1), .disabled("Z"), .enable("false")) multiplexer_3 (
    .in0(1'b0), .in1(1'b0), .in2(1'b0), .in3(1'b0), .in4(1'b0), .in5(1'b0), .in6(1'b0), .in7(1'b0),
    .in8(1'b0), .in9(1'b0), .in10(1'b0), .in11(comparator_1_lt[0]), .in12(comparator_2_lt[0]), .in13(1'b0),
    .in14(1'b0), .in15(1'b0), .out(out_6), .sel(AluOP));
  not not_1 (out_4, out_6);

  // Other names for the same wires on the sheet: Result2[31:0] = Result_2; S[3:0] = AluOP; tunnel = out_6;
  //   tunnel_t = out_4

  // Notes on the sheet:
  //   不要改变此引脚区域内容，也不要改变ALU封装形式
  //   输入引脚
  //   输出引脚
endmodule

module Regifile (
  input  [31:0] Din,
  input  Clk,
  input  WE,
  input  [4:0] R1_num,
  input  [4:0] W_num,
  input  [4:0] R2_num,
  output [31:0] R1,
  output [31:0] R2
);

  // RegisterFile registerfile_1: pin names not known; wires that end beside it: Din, Clk, WE, W_num, R1_num, R2_num, R1, R2
endmodule

module \理想流水线  (
  output RegWrite,
  output MemWrite,
  output [31:0] IF_PC,
  output [31:0] ID_PC,
  output [31:0] EX_PC,
  output [31:0] M_PC,
  output [31:0] WB_PC,
  output [31:0] RDin,
  output [31:0] MDin,
  output [31:0] LedData
);

  wire and_2_out, and_3_out, and_4_out, and_5_out, Beq, Bne, CLK, clock_1_out, comparator_1_eq,
       comparator_1_lt, comparator_2_eq, d_ff_1_q, ecall, equal, \ex_mem流水寄存器_1_p16 , \ex_mem流水寄存器_1_p17 ,
       \ex_mem流水寄存器_1_p19 , \ex_mem流水寄存器_1_p20 , \ex_mem流水寄存器_1_p21 , \ex_mem流水寄存器_1_p25 ,
       \ex_mem流水寄存器_1_p26 , Go, halt, \id_ex流水寄存器_1_alusrcbout , \id_ex流水寄存器_1_ecallout ,
       \id_ex流水寄存器_1_memtoregout , \id_ex流水寄存器_1_memwriteout , \id_ex流水寄存器_1_regwrite_2 , IR1, IR2, IR3,
       \mem_wb流水寄存器_1_p15 , \mem_wb流水寄存器_1_p16 , nand_1_out, not_1_out, not_2_out, not_3_out, not_4_out,
       or_1_out, or_2_out, PCSrc, RST, URET, W1, W2, W3, \单周期硬布线控制器_1_alu_src , \单周期硬布线控制器_1_beq ,
       \单周期硬布线控制器_1_bne , \单周期硬布线控制器_1_ecall , \单周期硬布线控制器_1_jal , \单周期硬布线控制器_1_jalr , \单周期硬布线控制器_1_memtoreg ,
       \单周期硬布线控制器_1_memwrite , \单周期硬布线控制器_1_regwrite , \单周期硬布线控制器_1_s_type , \单周期硬布线控制器_1_uret ;
  wire [2:0] Instr;
  wire [3:0] \id_ex流水寄存器_1_aluopout , \单周期硬布线控制器_1_alu_op ;
  wire [4:0] \id_ex流水寄存器_1_rdout , multiplexer_2_out, multiplexer_3_out, Rd;
  wire [11:0] multiplexer_4_out;
  wire [12:0] CNT_num;
  wire [15:0] \LoadUse次数 , \总周期数 , \插入气泡数 , \无条件分支数 , \条件分支成功数 ;
  wire [31:0] adder_1_out, adder_2_out, adder_3_out, adder_4_out, alu_1_result, and_1_out,
       bit_extender_1_out, bit_extender_2_out, bit_extender_3_out, BranchAddr, EX_IR, \ex_mem流水寄存器_1_p22 ,
       \id_ex流水寄存器_1_bout , \id_ex流水寄存器_1_i_sout , \id_ex流水寄存器_1_iout , \id_ex流水寄存器_1_pc_4out ,
       \id_ex流水寄存器_1_r1out , ID_IR, \if_id流水寄存器_1_pc_4out , IF_IR, MEM_IR, \mem_wb流水寄存器_1_p20 ,
       \mem_wb流水寄存器_1_p21 , \mem_wb流水寄存器_1_p23 , multiplexer_1_out, multiplexer_5_out, multiplexer_7_out, R1,
       ram_1_data, regifile_1_r1, regifile_1_r2, shifter_1_out, shifter_2_out, WB_IR, WriteData;

  Button \u_总复位  (.out(RST));
  Button _1 (.out(IR1));
  Button _2 (.out(IR2));
  Button _3 (.out(IR3));
  // Probe on \总周期数 
  // Probe on \总周期数 
  Button \u_继续运行  (.out(Go));
  LED #(.active("true")) led_1 (.in(W1));
  LED #(.active("true")) led_2 (.in(W2));
  LED #(.active("true")) led_3 (.in(W3));
  Hex_Digit_Display hex_digit_display_1 (.value(LedData[31:28]));  // open: dp
  // Probe on IF_PC[19:0]
  // RiscV_Probe riscv_probe_1: pin names not known; wires that end beside it: IF_IR
  Multiplexer #(.select(1), .width(32), .disabled("Z"), .enable("false")) multiplexer_1 (
    .in0(adder_1_out), .in1(BranchAddr), .out(multiplexer_1_out), .sel(PCSrc));
  Hex_Digit_Display hex_digit_display_2 (.value(LedData[23:20]));  // open: dp
  Hex_Digit_Display hex_digit_display_3 (.value(LedData[27:24]));  // open: dp
  // Probe on ID_PC[19:0]
  // RiscV_Probe riscv_probe_2: pin names not known; wires that end beside it: ID_IR
  not not_1 (not_1_out, halt);
  Hex_Digit_Display hex_digit_display_4 (.value(LedData[15:12]));  // open: dp
  Hex_Digit_Display hex_digit_display_5 (.value(LedData[19:16]));  // open: dp
  Register #(.width(32), .trigger("rising"), .Select("low")) PC (
    .D(multiplexer_1_out), .en(not_1_out), .Q(IF_PC), .clk(CLK), .clr(RST));
  Hex_Digit_Display hex_digit_display_6 (.value(LedData[11:8]));  // open: dp
  Hex_Digit_Display hex_digit_display_7 (.value(LedData[7:4]));  // open: dp
  // Probe on EX_PC[19:0]
  // RiscV_Probe riscv_probe_3: pin names not known; wires that end beside it: EX_IR
  Hex_Digit_Display hex_digit_display_8 (.value(LedData[3:0]));  // open: dp
  Adder #(.width(32)) adder_1 (.a(IF_PC), .b(32'h4), .out(adder_1_out));  // open: cin, cout
  // Probe on \总周期数 
  // Probe on M_PC[19:0]
  // RiscV_Probe riscv_probe_4: pin names not known; wires that end beside it: MEM_IR
  ROM #(.addrWidth(10), .dataWidth(32), .Select("high")) rom_1 (.addr(IF_PC[11:2]), .data(IF_IR));
  // Probe on \总周期数 
  // Probe on \无条件分支数 
  // Probe on \条件分支成功数 
  // Probe on \插入气泡数 
  // Probe on \LoadUse次数 
  \IF_ID流水寄存器  \if_id流水寄存器_1  (
    .IR(IF_IR), .PC(IF_PC), .PC_4(adder_1_out), .CLK(CLK), .IRout(ID_IR), .PCout(ID_PC),
    .PC_4out(\if_id流水寄存器_1_pc_4out ), .\使能端_低电平有效_stall_高电平有效 (halt), .IntR(RST), .IntRout(RST));  // open: 同步清零_气泡_高电平有效
  // Probe on IF_PC[11:0]
  // Probe on WB_PC[19:0]
  // RiscV_Probe riscv_probe_5: pin names not known; wires that end beside it: RST, WB_IR
  // Probe on EX_PC[11:0]
  // Probe on ID_PC[11:0]
  \单周期硬布线控制器  \u_单周期硬布线控制器_1  (
    .Funct({ID_IR[30], ID_IR[25], ID_IR[14:12]}), .OP(ID_IR[6:2]), .ALU_OP(\单周期硬布线控制器_1_alu_op ),
    .MemToReg(\单周期硬布线控制器_1_memtoreg ), .MemWrite(\单周期硬布线控制器_1_memwrite ), .ALU_SRC(\单周期硬布线控制器_1_alu_src ),
    .RegWrite(\单周期硬布线控制器_1_regwrite ), .ecall(\单周期硬布线控制器_1_ecall ), .S_type(\单周期硬布线控制器_1_s_type ),
    .Jalr(\单周期硬布线控制器_1_jalr ), .Beq(\单周期硬布线控制器_1_beq ), .JAL(\单周期硬布线控制器_1_jal ), .Bne(\单周期硬布线控制器_1_bne ),
    .in_3(ID_IR[21]), .uret(\单周期硬布线控制器_1_uret ));  // open: AUIPC, lb, Bge
  Multiplexer #(.select(1), .width(5), .disabled("Z"), .enable("false")) multiplexer_2 (
    .in0(ID_IR[19:15]), .in1(5'b10001), .out(multiplexer_2_out), .sel(\单周期硬布线控制器_1_ecall ));
  Multiplexer #(.select(1), .width(5), .disabled("Z"), .enable("false")) multiplexer_3 (
    .in0(ID_IR[24:20]), .in1(5'b01010), .out(multiplexer_3_out), .sel(\单周期硬布线控制器_1_ecall ));
  // Probe on M_PC[11:0]
  D_Flip_Flop #(.trigger("high"), .Pre_Clr_Positions("LEGACY"), .NegatePresetClear("false"), .enable("true"), .NewFFLayout("false")) d_ff_1 (.Q(d_ff_1_q));  // open: clk, D, Qn, preset, en, reset
  // Probe on 13'hc
  Multiplexer #(.select(1), .width(12), .disabled("Z"), .enable("false")) multiplexer_4 (
    .in0(ID_IR[31:20]), .in1({ID_IR[31:25], ID_IR[11:7]}), .out(multiplexer_4_out), .sel(\单周期硬布线控制器_1_s_type ));
  // Probe on WB_PC[11:0]
  Comparator #(.width(13), .mode("twosComplement")) comparator_1 (
    .a(CNT_num), .b(13'hc), .eq(comparator_1_eq), .lt(comparator_1_lt));  // open: gt
  Clock #(.highDuration(1), .lowDuration(1)) clock_1 (.out(clock_1_out));
  assign bit_extender_1_out = {{20{multiplexer_4_out[11]}}, multiplexer_4_out};  // Bit_Extender bit_extender_1
  assign bit_extender_2_out = {{20{ID_IR[31]}}, {ID_IR[31], ID_IR[7], ID_IR[30:25], ID_IR[11:8]}};  // Bit_Extender bit_extender_2
  assign bit_extender_3_out = {{12{ID_IR[31]}}, {ID_IR[31], ID_IR[19:12], ID_IR[20], ID_IR[30:21]}};  // Bit_Extender bit_extender_3
  nand nand_1 (nand_1_out, d_ff_1_q, comparator_1_eq);
  Counter #(.width(13), .max('h1fff), .ongoal("stay"), .trigger("rising"), .behavior("old")) counter_1 (
    .count(comparator_1_lt), .Q(CNT_num), .clk(clock_1_out));  // open: load, D, carry, clr, preset
  Regifile regifile_1 (
    .Din(RDin), .Clk(CLK), .R1(regifile_1_r1), .R2(regifile_1_r2), .WE(RegWrite), .W_num(Rd),
    .R1_num(multiplexer_2_out), .R2_num(multiplexer_3_out));
  \ID_EX流水寄存器  \id_ex流水寄存器_1  (
    .JAL(\单周期硬布线控制器_1_jal ), .JALR(\单周期硬布线控制器_1_jalr ), .URET(\单周期硬布线控制器_1_uret ), .Beq(\单周期硬布线控制器_1_beq ),
    .Bne(\单周期硬布线控制器_1_bne ), .MemToReg(\单周期硬布线控制器_1_memtoreg ), .AluOp(\单周期硬布线控制器_1_alu_op ),
    .AluSrcB(\单周期硬布线控制器_1_alu_src ), .RegWrite(\单周期硬布线控制器_1_regwrite ), .I_S(bit_extender_1_out),
    .B(bit_extender_2_out), .I(bit_extender_3_out), .CLK(CLK), .JALout(Instr[2]), .JALRout(Instr[0]),
    .URETout(URET), .Beqout(Beq), .Bneout(Bne), .MemToRegout(\id_ex流水寄存器_1_memtoregout ),
    .AluOpout(\id_ex流水寄存器_1_aluopout ), .AluSrcBout(\id_ex流水寄存器_1_alusrcbout ),
    .RegWrite_2(\id_ex流水寄存器_1_regwrite_2 ), .I_Sout(\id_ex流水寄存器_1_i_sout ), .Bout(\id_ex流水寄存器_1_bout ),
    .Iout(\id_ex流水寄存器_1_iout ), .\使能端_低电平有效_stall_高电平有效 (halt), .R1(regifile_1_r1),
    .R1out(\id_ex流水寄存器_1_r1out ), .R2(regifile_1_r2), .R2out(WriteData), .MemWrite(\单周期硬布线控制器_1_memwrite ),
    .MemWriteout(\id_ex流水寄存器_1_memwriteout ), .PC(ID_PC), .PCout(EX_PC), .PC_4(\if_id流水寄存器_1_pc_4out ),
    .PC_4out(\id_ex流水寄存器_1_pc_4out ), .Rd(ID_IR[11:7]), .Rdout(\id_ex流水寄存器_1_rdout ), .IR(ID_IR),
    .IRout(EX_IR), .ecall(\单周期硬布线控制器_1_ecall ), .ecallout(\id_ex流水寄存器_1_ecallout ), .IntR(RST), .IntRout(RST));  // open: 同步清零_气泡_高电平有效, R1Src, R1Srcout, R2Src, ecallout_2, AUIPC, AUIPCout, lb, lbout, Bge, Bgeout, U, Uout
  assign CLK = nand_1_out ? clock_1_out : 1'bz;  // Controlled_Buffer controlled_buffer_1
  Pull_Resistor #(.pull(1)) pull_resistor_1 (.node(CLK));
  Adder #(.width(32)) adder_2 (
    .a(\id_ex流水寄存器_1_i_sout ), .b(\id_ex流水寄存器_1_r1out ), .out(adder_2_out));  // open: cin, cout
  Shifter #(.width(32), .shift("ll")) shifter_1 (.in(\id_ex流水寄存器_1_bout ), .\dist (5'b00001), .out(shifter_1_out));
  Shifter #(.width(32), .shift("ll")) shifter_2 (.in(\id_ex流水寄存器_1_iout ), .\dist (5'b00001), .out(shifter_2_out));
  Multiplexer #(.select(1), .width(32), .disabled("Z"), .enable("false")) multiplexer_5 (
    .in0(WriteData), .in1(\id_ex流水寄存器_1_i_sout ), .out(multiplexer_5_out), .sel(\id_ex流水寄存器_1_alusrcbout ));
  Adder #(.width(32)) adder_3 (.a(shifter_1_out), .b(EX_PC), .out(adder_3_out));  // open: cin, cout
  Adder #(.width(32)) adder_4 (.a(shifter_2_out), .b(EX_PC), .out(adder_4_out));  // open: cin, cout
  assign and_1_out = adder_2_out & 32'hfffffffe;  // AND_Gate and_1, 32 bits wide
  or or_1 (or_1_out, Instr[2], Instr[0]);
  ALU alu_1 (
    .X(\id_ex流水寄存器_1_r1out ), .Y(multiplexer_5_out), .AluOP(\id_ex流水寄存器_1_aluopout ), .Equal(equal),
    .Result(alu_1_result));  // open: Result_2, out_4, out_6
  Multiplexer #(.select(3), .width(32), .disabled("Z"), .enable("false")) multiplexer_6 (
    .in1(and_1_out), .in2(adder_3_out), .in4(adder_4_out), .out(BranchAddr), .sel(Instr));  // open: in0, in3, in5, in6, in7
  // EX_MEM流水寄存器 ex_mem流水寄存器_1: pin names not known; wires that end beside it: or_1_out, \id_ex流水寄存器_1_memtoregout , \id_ex流水寄存器_1_memwriteout , \id_ex流水寄存器_1_regwrite_2 , \id_ex流水寄存器_1_ecallout , \id_ex流水寄存器_1_r1out , alu_1_result, WriteData, EX_PC, \id_ex流水寄存器_1_pc_4out , \id_ex流水寄存器_1_rdout , EX_IR, halt, RST, CLK, \ex_mem流水寄存器_1_p16 , \ex_mem流水寄存器_1_p17 , MemWrite, \ex_mem流水寄存器_1_p19 , \ex_mem流水寄存器_1_p20 , \ex_mem流水寄存器_1_p21 , \ex_mem流水寄存器_1_p22 , MDin, M_PC, \ex_mem流水寄存器_1_p25 , \ex_mem流水寄存器_1_p26 , MEM_IR
  not not_2 (not_2_out, MemWrite);
  RAM #(.addrWidth(10), .dataWidth(32), .bus("separate"), .Select("high")) ram_1 (
    .addr(\ex_mem流水寄存器_1_p22 [11:2]), .din(MDin), .data(ram_1_data), .str(MemWrite), .clk(CLK), .ld(not_2_out));  // open: sel, clr
  // MEM_WB流水寄存器 mem_wb流水寄存器_1: pin names not known; wires that end beside it: \ex_mem流水寄存器_1_p16 , \ex_mem流水寄存器_1_p17 , \ex_mem流水寄存器_1_p19 , \ex_mem流水寄存器_1_p20 , \ex_mem流水寄存器_1_p21 , \ex_mem流水寄存器_1_p22 , ram_1_data, M_PC, \ex_mem流水寄存器_1_p25 , \ex_mem流水寄存器_1_p26 , MEM_IR, halt, RST, CLK, \mem_wb流水寄存器_1_p15 , \mem_wb流水寄存器_1_p16 , RegWrite, ecall, R1, \mem_wb流水寄存器_1_p20 , \mem_wb流水寄存器_1_p21 , WB_PC, \mem_wb流水寄存器_1_p23 , Rd, WB_IR
  Multiplexer #(.select(1), .width(32), .disabled("Z"), .enable("false")) multiplexer_7 (
    .in0(\mem_wb流水寄存器_1_p20 ), .in1(\mem_wb流水寄存器_1_p21 ), .out(multiplexer_7_out), .sel(\mem_wb流水寄存器_1_p16 ));
  Multiplexer #(.select(1), .width(32), .disabled("Z"), .enable("false")) multiplexer_8 (
    .in0(multiplexer_7_out), .in1(\mem_wb流水寄存器_1_p23 ), .out(RDin), .sel(\mem_wb流水寄存器_1_p15 ));
  not not_3 (not_3_out, equal);
  Comparator #(.width(32), .mode("unsigned")) comparator_2 (.a(R1), .b(32'h22), .eq(comparator_2_eq));  // open: gt, lt
  and and_2 (and_2_out, Beq, equal);
  and and_3 (and_3_out, Bne, not_3_out);
  or or_2 (or_2_out, Instr[2], Instr[0]);
  or or_3 (Instr[1], Beq, Bne);
  and and_4 (and_4_out, ecall, comparator_2_eq);
  and and_5 (and_5_out, ecall, ~comparator_2_eq);  // AND_Gate
  Multiplexer #(.select(1), .width(1), .disabled("Z"), .enable("false")) multiplexer_9 (
    .in0(and_5_out), .in1(1'b0), .out(halt), .sel(Go));
  or or_4 (PCSrc, and_2_out, and_3_out, or_2_out);
  not not_4 (not_4_out, halt);
  Register #(.width(32), .trigger("rising"), .Select("low")) register_1 (
    .D(WriteData), .en(and_4_out), .Q(LedData), .clk(CLK));  // open: clr
  Counter #(.width(16), .max('hffff), .ongoal("stay"), .trigger("rising"), .behavior("old")) counter_2 (
    .count(not_4_out), .Q(\总周期数 ), .clk(CLK));  // open: load, D, carry, clr, preset

  // Other names for the same wires on the sheet: JALR = Instr[0]; JAL = Instr[2]; MEM_PC[31:0] = M_PC

  // Notes on the sheet:
  //   中断源
  //   时空图监测，可删除
  //   中断等待指示
  //   数码管输出
  //   指令存储器
  //   IR
  //   contents of rom_1 (hex, n*v repeats v):
  //   413 493 913 993 46413 14e493 296913 39e993 842023 942223 1242423 1342623 a00893 493 913 993 73
  //   PC
  //   PC+4
  //   JAL
  //   JALR
  //   URET
  //   rd
  //   IR
  //   控制位
  //   Beq
  //   Bne
  //   AluOP
  //   AluSrcB
  //   RegWrite
  //   S_Tyoe
  //   I型
  //   S型
  //   B型
  //   J型
  //   流水调试日志用
  //   暂停节拍，不能为0
  //   MemToReg
  //   MemWrite
  //   rs1
  //   rs2
  //   戳工具置1进入计数暂停模式，ctrl+k时钟自动运行到对应节拍暂停
  //   ctrl+k关闭时钟连续运行，将控制位置零，进入单步调试模式调试
  //   用这个时钟源需要去掉电路中的其他时钟源
  //   可计数暂停的时钟源
  //   为方便自动评测，需要输出流水线各段保存的PC值，注意是PC不是PC+4，另外ID段寄存器写入信息，Mem段内存写入信息也要输出
  //   AluResult
  //   WriteData
  //   数据存储器
  //   J
  //   MemToReg
  //   PC+4
endmodule

module \气泡流水线  (
  output RegWrite,
  output MemWrite,
  output [31:0] IF_PC,
  output [31:0] ID_PC,
  output [31:0] EX_PC,
  output [31:0] M_PC,
  output [31:0] WB_PC,
  output [31:0] RDin,
  output [31:0] MDin,
  output [31:0] LedData
);

  wire AluSrcB, and_1_out, and_2_out, and_3_out, and_4_out, and_5_out, and_6_out, and_8_out, and_9_out,
       and_10_out, and_11_out, and_12_out, and_13_out, and_14_out, and_15_out, and_16_out, Beq, Bge, Bne,
       CLK, clock_1_out, clock_2_out, comparator_1_eq, comparator_2_eq, comparator_2_gt, comparator_3_eq,
       comparator_3_lt, comparator_4_eq, comparator_5_eq, comparator_6_eq, comparator_7_eq, comparator_8_eq,
       comparator_9_eq, d_ff_1_q, DataHazzard, ecall, ecall_id, equal, \ex_mem流水寄存器_1_auipcout ,
       \ex_mem流水寄存器_1_ecallout , \ex_mem流水寄存器_1_jout , \ex_mem流水寄存器_1_lbout , \ex_mem流水寄存器_1_memtoregout ,
       Go, halt, \id_ex流水寄存器_1_p27 , \id_ex流水寄存器_1_p30 , \id_ex流水寄存器_1_p31 , \id_ex流水寄存器_1_p38 ,
       \id_ex流水寄存器_1_p39 , \id_ex流水寄存器_1_p41 , \id_ex流水寄存器_1_p43 , IR1, IR2, IR3, JAL_id, nand_1_out,
       not_1_out, not_2_out, not_3_out, not_4_out, not_6_out, not_7_out, not_8_out, not_9_out, not_10_out,
       or_1_out, or_5_out, or_6_out, or_7_out, or_8_out, or_10_out, or_11_out, PCSrc, RegWrite_ex,
       RegWrite_mem, Rs1used, Rs2used, RST, tunnel, URET, W1, W2, W3, \单周期硬布线控制器_1_auipc , \单周期硬布线控制器_1_beq ,
       \单周期硬布线控制器_1_bge , \单周期硬布线控制器_1_bne , \单周期硬布线控制器_1_jalr , \单周期硬布线控制器_1_lb , \单周期硬布线控制器_1_memtoreg ,
       \单周期硬布线控制器_1_memwrite , \单周期硬布线控制器_1_regwrite , \单周期硬布线控制器_1_s_type , \单周期硬布线控制器_1_uret ;
  wire [1:0] \mem_wb流水寄存器_1_jout , \mem_wb流水寄存器_1_memtoregout , \mem_wb流水寄存器_1_selout ;
  wire [2:0] Instr;
  wire [3:0] \id_ex流水寄存器_1_p40 , \单周期硬布线控制器_1_alu_op ;
  wire [4:0] multiplexer_3_out, multiplexer_4_out, multiplexer_8_out, Rd, rd_ex, rd_mem;
  wire [11:0] multiplexer_5_out;
  wire [12:0] CNT_num;
  wire [15:0] \LoadUse次数 , \总周期数 , \插入气泡数 , \无条件分支数 , \条件分支成功数 ;
  wire [31:0] adder_1_out, adder_2_out, adder_3_out, adder_4_out, adder_5_out, alu_1_result, and_7_out,
       bit_extender_1_out, bit_extender_2_out, bit_extender_3_out, bit_extender_4_out, bit_extender_5_out,
       bit_extender_6_out, bit_extender_7_out, bit_extender_8_out, BranchAddr, EX_IR,
       \ex_mem流水寄存器_1_aluresultout , \ex_mem流水寄存器_1_auipc_out , \ex_mem流水寄存器_1_pc_4out ,
       \ex_mem流水寄存器_1_r1out , \id_ex流水寄存器_1_p47 , \id_ex流水寄存器_1_p50 , \id_ex流水寄存器_1_p51 , \id_ex流水寄存器_1_p52 ,
       \id_ex流水寄存器_1_p53 , ID_IR, \if_id流水寄存器_1_pc_4out , IF_IR, MEM_IR, \mem_wb流水寄存器_1_aluresultout ,
       \mem_wb流水寄存器_1_auipc_out , \mem_wb流水寄存器_1_pc_4out , \mem_wb流水寄存器_1_writedataout , multiplexer_1_out,
       multiplexer_6_out, multiplexer_9_out, multiplexer_10_out, R1, R1_ex, R2, R2_ex, ram_1_data,
       regifile_1_r1, regifile_1_r2, shifter_1_out, shifter_2_out, shifter_3_out, WB_IR;

  Button \u_总复位  (.out(RST));
  Button _1 (.out(IR1));
  Button _2 (.out(IR2));
  Button _3 (.out(IR3));
  // Probe on \总周期数 
  // Probe on \总周期数 
  Button \u_继续运行  (.out(Go));
  LED #(.active("true")) led_1 (.in(W1));
  LED #(.active("true")) led_2 (.in(W2));
  LED #(.active("true")) led_3 (.in(W3));
  Hex_Digit_Display hex_digit_display_1 (.value(LedData[31:28]));  // open: dp
  // Probe on IF_PC[19:0]
  // RiscV_Probe riscv_probe_1: pin names not known; wires that end beside it: IF_IR
  Hex_Digit_Display hex_digit_display_2 (.value(LedData[23:20]));  // open: dp
  Hex_Digit_Display hex_digit_display_3 (.value(LedData[27:24]));  // open: dp
  // Probe on ID_PC[19:0]
  // RiscV_Probe riscv_probe_2: pin names not known; wires that end beside it: ID_IR
  and and_1 (and_1_out, tunnel, Bge);
  and and_2 (and_2_out, Beq, equal);
  and and_3 (and_3_out, Bne, not_1_out);
  not not_1 (not_1_out, equal);
  or or_1 (or_1_out, Instr[2], Instr[0]);
  Hex_Digit_Display hex_digit_display_4 (.value(LedData[15:12]));  // open: dp
  Hex_Digit_Display hex_digit_display_5 (.value(LedData[19:16]));  // open: dp
  Comparator #(.width(32), .mode("unsigned")) comparator_1 (.a(R1), .b(32'h22), .eq(comparator_1_eq));  // open: gt, lt
  Hex_Digit_Display hex_digit_display_6 (.value(LedData[7:4]));  // open: dp
  Hex_Digit_Display hex_digit_display_7 (.value(LedData[11:8]));  // open: dp
  Clock #(.highDuration(1), .lowDuration(1)) clock_1 (.out(clock_1_out));
  // Probe on EX_PC[19:0]
  // RiscV_Probe riscv_probe_3: pin names not known; wires that end beside it: clock_1_out, EX_IR, CLK
  Multiplexer #(.select(1), .width(32), .disabled("Z"), .enable("false")) multiplexer_1 (
    .in0(adder_1_out), .in1(BranchAddr), .out(multiplexer_1_out), .sel(PCSrc));
  and and_4 (and_4_out, not_2_out, not_3_out);
  not not_2 (not_2_out, DataHazzard);
  not not_3 (not_3_out, halt);
  or or_2 (PCSrc, and_1_out, and_2_out, and_3_out, or_1_out);
  or or_3 (Instr[1], Beq, Bge, Bne);
  and and_5 (and_5_out, ecall, comparator_1_eq);
  and and_6 (and_6_out, ecall, ~comparator_1_eq);  // AND_Gate
  Hex_Digit_Display hex_digit_display_8 (.value(LedData[3:0]));  // open: dp
  Register #(.width(32), .trigger("rising"), .Select("low")) PC (
    .D(multiplexer_1_out), .en(and_4_out), .Q(IF_PC), .clk(CLK), .clr(RST));
  Multiplexer #(.select(1), .width(1), .disabled("Z"), .enable("false")) multiplexer_2 (
    .in0(and_6_out), .in1(1'b0), .out(halt), .sel(Go));
  // Probe on \总周期数 
  // Probe on M_PC[19:0]
  // RiscV_Probe riscv_probe_4: pin names not known; wires that end beside it: MEM_IR
  // Probe on \总周期数 
  // Probe on \无条件分支数 
  // Probe on \条件分支成功数 
  // Probe on \插入气泡数 
  // Probe on \LoadUse次数 
  Adder #(.width(32)) adder_1 (.a(IF_PC), .b(32'h4), .out(adder_1_out));  // open: cin, cout
  Comparator #(.width(32), .mode("twosComplement")) comparator_2 (
    .a(R1_ex), .b(R2_ex), .gt(comparator_2_gt), .eq(comparator_2_eq));  // open: lt
  // Probe on IF_PC[11:0]
  // Probe on WB_PC[19:0]
  // RiscV_Probe riscv_probe_5: pin names not known; wires that end beside it: WB_IR
  or or_4 (tunnel, comparator_2_gt, comparator_2_eq);
  not not_4 (not_4_out, halt);
  // Probe on ID_PC[11:0]
  // Probe on EX_PC[11:0]
  or or_5 (or_5_out, RST, PCSrc);
  ROM #(.addrWidth(10), .dataWidth(32), .Select("high")) rom_1 (.addr(IF_PC[11:2]), .data(IF_IR));
  \IF_ID流水寄存器  \if_id流水寄存器_1  (
    .IR(IF_IR), .PC(IF_PC), .PC_4(adder_1_out), .CLK(CLK), .IRout(ID_IR), .PCout(ID_PC),
    .PC_4out(\if_id流水寄存器_1_pc_4out ), .\同步清零_气泡_高电平有效 (or_5_out), .\使能端_低电平有效_stall_高电平有效 (or_6_out));  // open: IntR, IntRout
  or or_6 (or_6_out, halt, DataHazzard);
  Register #(.width(32), .trigger("rising"), .Select("low")) register_1 (
    .D(R2), .en(and_5_out), .Q(LedData), .clk(CLK));  // open: clr
  Counter #(.width(16), .max('hffff), .ongoal("stay"), .trigger("rising"), .behavior("old")) counter_1 (
    .count(not_4_out), .Q(\总周期数 ), .clk(CLK));  // open: load, D, carry, clr, preset
  // Probe on M_PC[11:0]
  D_Flip_Flop #(.trigger("high"), .Pre_Clr_Positions("LEGACY"), .NegatePresetClear("false"), .enable("true"), .NewFFLayout("false")) d_ff_1 (.Q(d_ff_1_q));  // open: clk, D, Qn, preset, en, reset
  // Probe on 13'hc
  // Probe on WB_PC[11:0]
  Comparator #(.width(13), .mode("twosComplement")) comparator_3 (
    .a(CNT_num), .b(13'hc), .eq(comparator_3_eq), .lt(comparator_3_lt));  // open: gt
  Clock #(.highDuration(1), .lowDuration(1)) clock_2 (.out(clock_2_out));
  nand nand_1 (nand_1_out, d_ff_1_q, comparator_3_eq);
  Counter #(.width(13), .max('h1fff), .ongoal("stay"), .trigger("rising"), .behavior("old")) counter_2 (
    .count(comparator_3_lt), .Q(CNT_num), .clk(clock_2_out));  // open: load, D, carry, clr, preset
  \单周期硬布线控制器  \u_单周期硬布线控制器_1  (
    .Funct({ID_IR[30], ID_IR[25], ID_IR[14:12]}), .OP(ID_IR[6:2]), .ALU_OP(\单周期硬布线控制器_1_alu_op ),
    .MemToReg(\单周期硬布线控制器_1_memtoreg ), .MemWrite(\单周期硬布线控制器_1_memwrite ), .ALU_SRC(AluSrcB),
    .RegWrite(\单周期硬布线控制器_1_regwrite ), .ecall(ecall_id), .S_type(\单周期硬布线控制器_1_s_type ),
    .Jalr(\单周期硬布线控制器_1_jalr ), .Beq(\单周期硬布线控制器_1_beq ), .JAL(JAL_id), .Bne(\单周期硬布线控制器_1_bne ),
    .in_3(ID_IR[21]), .uret(\单周期硬布线控制器_1_uret ), .AUIPC(\单周期硬布线控制器_1_auipc ), .lb(\单周期硬布线控制器_1_lb ),
    .Bge(\单周期硬布线控制器_1_bge ));
  Multiplexer #(.select(1), .width(5), .disabled("Z"), .enable("false")) multiplexer_3 (
    .in0(ID_IR[19:15]), .in1(5'b10001), .out(multiplexer_3_out), .sel(ecall_id));
  Multiplexer #(.select(1), .width(5), .disabled("Z"), .enable("false")) multiplexer_4 (
    .in0(ID_IR[24:20]), .in1(5'b01010), .out(multiplexer_4_out), .sel(ecall_id));
  Multiplexer #(.select(1), .width(12), .disabled("Z"), .enable("false")) multiplexer_5 (
    .in0(ID_IR[31:20]), .in1({ID_IR[31:25], ID_IR[11:7]}), .out(multiplexer_5_out), .sel(\单周期硬布线控制器_1_s_type ));
  assign CLK = nand_1_out ? clock_2_out : 1'bz;  // Controlled_Buffer controlled_buffer_1
  assign bit_extender_1_out = {{20{multiplexer_5_out[11]}}, multiplexer_5_out};  // Bit_Extender bit_extender_1
  assign bit_extender_2_out = {{20{ID_IR[31]}}, {ID_IR[31], ID_IR[7], ID_IR[30:25], ID_IR[11:8]}};  // Bit_Extender bit_extender_2
  assign bit_extender_3_out = {{12{ID_IR[31]}}, {ID_IR[31], ID_IR[19:12], ID_IR[20], ID_IR[30:21]}};  // Bit_Extender bit_extender_3
  assign bit_extender_4_out = {{12{ID_IR[31]}}, ID_IR[31:12]};  // Bit_Extender bit_extender_4
  Pull_Resistor #(.pull(1)) pull_resistor_1 (.node(CLK));
  or or_7 (or_7_out, RST, DataHazzard, PCSrc);
  Regifile regifile_1 (
    .Din(RDin), .Clk(CLK), .R1(regifile_1_r1), .R2(regifile_1_r2), .WE(RegWrite), .W_num(Rd),
    .R1_num(multiplexer_3_out), .R2_num(multiplexer_4_out));
  not not_5 (Rs1used, JAL_id);
  nor nor_1 (Rs2used, ecall_id, JAL_id, AluSrcB);
  // ID_EX流水寄存器 id_ex流水寄存器_1: pin names not known; wires that end beside it: \单周期硬布线控制器_1_lb , \单周期硬布线控制器_1_auipc , \单周期硬布线控制器_1_uret , \单周期硬布线控制器_1_jalr , JAL_id, \单周期硬布线控制器_1_beq , \单周期硬布线控制器_1_bge , \单周期硬布线控制器_1_bne , \单周期硬布线控制器_1_memtoreg , \单周期硬布线控制器_1_memwrite , \单周期硬布线控制器_1_alu_op , AluSrcB, \单周期硬布线控制器_1_regwrite , ecall_id, regifile_1_r1, regifile_1_r2, ID_PC, \if_id流水寄存器_1_pc_4out , ID_IR[11:7], ID_IR, bit_extender_1_out, bit_extender_2_out, bit_extender_3_out, bit_extender_4_out, halt, or_7_out, \id_ex流水寄存器_1_p27 , \id_ex流水寄存器_1_p27 , CLK, \id_ex流水寄存器_1_p30 , \id_ex流水寄存器_1_p31 , URET, Instr[0], Instr[2], Beq, Bge, Bne, \id_ex流水寄存器_1_p38 , \id_ex流水寄存器_1_p39 , \id_ex流水寄存器_1_p40 , \id_ex流水寄存器_1_p41 , RegWrite_ex, \id_ex流水寄存器_1_p43 , R1_ex, R2_ex, EX_PC, \id_ex流水寄存器_1_p47 , rd_ex, EX_IR, \id_ex流水寄存器_1_p50 , \id_ex流水寄存器_1_p51 , \id_ex流水寄存器_1_p52 , \id_ex流水寄存器_1_p53 
  Adder #(.width(32)) adder_2 (.a(\id_ex流水寄存器_1_p50 ), .b(R1_ex), .out(adder_2_out));  // open: cin, cout
  Shifter #(.width(32), .shift("ll")) shifter_1 (.in(\id_ex流水寄存器_1_p51 ), .\dist (5'b00001), .out(shifter_1_out));
  Shifter #(.width(32), .shift("ll")) shifter_2 (.in(\id_ex流水寄存器_1_p52 ), .\dist (5'b00001), .out(shifter_2_out));
  Shifter #(.width(32), .shift("ll")) shifter_3 (.in(\id_ex流水寄存器_1_p53 ), .\dist (5'b01100), .out(shifter_3_out));
  Multiplexer #(.select(1), .width(32), .disabled("Z"), .enable("false")) multiplexer_6 (
    .in0(R2_ex), .in1(\id_ex流水寄存器_1_p50 ), .out(multiplexer_6_out), .sel(\id_ex流水寄存器_1_p41 ));
  assign and_7_out = adder_2_out & 32'hfffffffe;  // AND_Gate and_7, 32 bits wide
  Adder #(.width(32)) adder_3 (.a(shifter_1_out), .b(EX_PC), .out(adder_3_out));  // open: cin, cout
  Adder #(.width(32)) adder_4 (.a(shifter_2_out), .b(EX_PC), .out(adder_4_out));  // open: cin, cout
  Adder #(.width(32)) adder_5 (.a(shifter_3_out), .b(EX_PC), .out(adder_5_out));  // open: cin, cout
  or or_8 (or_8_out, Instr[2], Instr[0]);
  ALU alu_1 (
    .X(R1_ex), .Y(multiplexer_6_out), .AluOP(\id_ex流水寄存器_1_p40 ), .Equal(equal), .Result(alu_1_result));  // open: Result_2, out_4, out_6
  Multiplexer #(.select(3), .width(32), .disabled("Z"), .enable("false")) multiplexer_7 (
    .in1(and_7_out), .in2(adder_3_out), .in4(adder_4_out), .out(BranchAddr), .sel(Instr));  // open: in0, in3, in5, in6, in7
  Multiplexer #(.select(1), .width(5), .disabled("Z"), .enable("false")) multiplexer_8 (
    .in0(ID_IR[19:15]), .in1(5'b10001), .out(multiplexer_8_out), .sel(ecall_id));
  \EX_MEM流水寄存器  \ex_mem流水寄存器_1  (
    .MemToReg(\id_ex流水寄存器_1_p38 ), .MemWrite(\id_ex流水寄存器_1_p39 ), .RegWrite(RegWrite_ex),
    .AluResult(alu_1_result), .Rd(rd_ex), .CLK(CLK), .MemToRegout(\ex_mem流水寄存器_1_memtoregout ),
    .MemWriteout(MemWrite), .RegWriteout(RegWrite_mem), .AluResultout(\ex_mem流水寄存器_1_aluresultout ),
    .Rdout(rd_mem), .\同步清零_气泡_高电平有效 (RST), .\使能端_低电平有效_stall_高电平有效 (halt), .WriteData(R2_ex),
    .WriteDataout(MDin), .PC_4(\id_ex流水寄存器_1_p47 ), .PC_4out(\ex_mem流水寄存器_1_pc_4out ),
    .J(\id_ex流水寄存器_1_p30 ), .Jout(\ex_mem流水寄存器_1_jout ), .IR(EX_IR), .IRout(MEM_IR), .PC(EX_PC),
    .PCout(M_PC), .ecall(\id_ex流水寄存器_1_p43 ), .ecallout(\ex_mem流水寄存器_1_ecallout ), .R1(R1_ex),
    .R1out(\ex_mem流水寄存器_1_r1out ), .AUIPC(\id_ex流水寄存器_1_p31 ), .AUIPCout(\ex_mem流水寄存器_1_auipcout ),
    .lb(or_8_out), .lbout(\ex_mem流水寄存器_1_lbout ), .auipc_res(adder_5_out),
    .auipc_out(\ex_mem流水寄存器_1_auipc_out ));
  Comparator #(.width(5), .mode("unsigned")) comparator_4 (
    .a(rd_ex), .b(multiplexer_8_out), .eq(comparator_4_eq));  // open: gt, lt
  Comparator #(.width(5), .mode("unsigned")) comparator_5 (
    .a(rd_ex), .b(ID_IR[24:20]), .eq(comparator_5_eq));  // open: gt, lt
  Comparator #(.width(5), .mode("unsigned")) comparator_6 (
    .a(rd_mem), .b(multiplexer_8_out), .eq(comparator_6_eq));  // open: gt, lt
  Comparator #(.width(5), .mode("unsigned")) comparator_7 (
    .a(rd_mem), .b(ID_IR[24:20]), .eq(comparator_7_eq));  // open: gt, lt
  Comparator #(.width(5), .mode("unsigned")) comparator_8 (
    .a(multiplexer_8_out), .b({5{1'b0}}), .eq(comparator_8_eq));  // open: gt, lt
  not not_6 (not_6_out, comparator_8_eq);
  Comparator #(.width(5), .mode("unsigned")) comparator_9 (
    .a(ID_IR[24:20]), .b({5{1'b0}}), .eq(comparator_9_eq));  // open: gt, lt
  not not_7 (not_7_out, comparator_9_eq);
  not not_8 (not_8_out, MemWrite);
  RAM #(.addrWidth(10), .dataWidth(32), .bus("separate"), .Select("high")) ram_1 (
    .addr(\ex_mem流水寄存器_1_aluresultout [11:2]), .din(MDin), .data(ram_1_data), .str(MemWrite), .clk(CLK),
    .ld(not_8_out));  // open: sel, clr
  and and_8 (and_8_out, Rs1used, comparator_4_eq, not_6_out, RegWrite_ex);
  and and_9 (and_9_out, Rs2used, comparator_5_eq, not_7_out, RegWrite_ex);
  and and_10 (and_10_out, Rs1used, comparator_6_eq, not_6_out, RegWrite_mem);
  and and_11 (and_11_out, Rs2used, comparator_7_eq, not_7_out, RegWrite_mem);
  \MEM_WB流水寄存器  \mem_wb流水寄存器_1  (
    .J(\ex_mem流水寄存器_1_lbout ), .MemToReg(\ex_mem流水寄存器_1_memtoregout ), .RegWrite(RegWrite_mem),
    .AluResult(\ex_mem流水寄存器_1_aluresultout ), .WriteData(ram_1_data), .PC_4(\ex_mem流水寄存器_1_pc_4out ),
    .Rd(rd_mem), .CLK(CLK), .Jout(\mem_wb流水寄存器_1_jout [0]), .MemToRegout(\mem_wb流水寄存器_1_memtoregout [0]),
    .RegWriteout(RegWrite), .AluResultout(\mem_wb流水寄存器_1_aluresultout ),
    .WriteDataout(\mem_wb流水寄存器_1_writedataout ), .PC_4out(\mem_wb流水寄存器_1_pc_4out ), .Rdout(Rd),
    .\同步清零_气泡_高电平有效 (RST), .\使能端_低电平有效_stall_高电平有效 (halt), .IR(MEM_IR), .IRout(WB_IR), .PCout(WB_PC),
    .PC(M_PC), .ecall(\ex_mem流水寄存器_1_ecallout ), .ecallout(ecall), .R1(\ex_mem流水寄存器_1_r1out ), .R1out(R1),
    .R2(MDin), .R2out(R2), .AUIPC(\ex_mem流水寄存器_1_auipcout ), .AUIPCout(\mem_wb流水寄存器_1_jout [1]),
    .lb(\ex_mem流水寄存器_1_jout ), .lbout(\mem_wb流水寄存器_1_memtoregout [1]),
    .sel(\ex_mem流水寄存器_1_aluresultout [1:0]), .selout(\mem_wb流水寄存器_1_selout ),
    .auipc_2(\ex_mem流水寄存器_1_auipc_out ), .auipc_out(\mem_wb流水寄存器_1_auipc_out ));
  or or_9 (DataHazzard, and_8_out, and_9_out, and_10_out, and_11_out);
  assign bit_extender_5_out = {{24{\mem_wb流水寄存器_1_writedataout [7]}}, \mem_wb流水寄存器_1_writedataout [7:0]};  // Bit_Extender bit_extender_5
  assign bit_extender_6_out = {{24{\mem_wb流水寄存器_1_writedataout [15]}}, \mem_wb流水寄存器_1_writedataout [15:8]};  // Bit_Extender bit_extender_6
  assign bit_extender_7_out = {{24{\mem_wb流水寄存器_1_writedataout [23]}}, \mem_wb流水寄存器_1_writedataout [23:16]};  // Bit_Extender bit_extender_7
  assign bit_extender_8_out = {{24{\mem_wb流水寄存器_1_writedataout [31]}}, \mem_wb流水寄存器_1_writedataout [31:24]};  // Bit_Extender bit_extender_8
  Multiplexer #(.select(2), .width(32), .disabled("Z"), .enable("false")) multiplexer_9 (
    .in0(bit_extender_5_out), .in1(bit_extender_6_out), .in2(bit_extender_7_out), .in3(bit_extender_8_out),
    .out(multiplexer_9_out), .sel(\mem_wb流水寄存器_1_selout ));
  Multiplexer #(.select(2), .width(32), .disabled("Z"), .enable("false")) multiplexer_10 (
    .in0(\mem_wb流水寄存器_1_aluresultout ), .in1(\mem_wb流水寄存器_1_writedataout ), .in3(multiplexer_9_out),
    .out(multiplexer_10_out), .sel(\mem_wb流水寄存器_1_memtoregout ));  // open: in2
  Multiplexer #(.select(2), .width(32), .disabled("Z"), .enable("false")) multiplexer_11 (
    .in0(multiplexer_10_out), .in1(\mem_wb流水寄存器_1_pc_4out ), .in2(\mem_wb流水寄存器_1_auipc_out ), .out(RDin),
    .sel(\mem_wb流水寄存器_1_jout ));  // open: in3
  not not_9 (not_9_out, equal);
  and and_12 (and_12_out, Beq, equal);
  and and_13 (and_13_out, Bne, not_9_out);
  not not_10 (not_10_out, halt);
  or or_10 (or_10_out, Instr[0], Instr[2]);
  or or_11 (or_11_out, and_12_out, and_13_out);
  and and_14 (and_14_out, or_10_out, not_10_out);
  and and_15 (and_15_out, or_11_out, not_10_out);
  and and_16 (and_16_out, DataHazzard, not_10_out);
  Counter #(.width(16), .max('hffff), .ongoal("stay"), .trigger("rising"), .behavior("old")) counter_3 (
    .count(and_14_out), .Q(\无条件分支数 ), .clk(CLK));  // open: load, D, carry, clr, preset
  Counter #(.width(16), .max('hffff), .ongoal("stay"), .trigger("rising"), .behavior("old")) counter_4 (
    .count(and_15_out), .Q(\条件分支成功数 ), .clk(CLK));  // open: load, D, carry, clr, preset
  Counter #(.width(16), .max('hffff), .ongoal("stay"), .trigger("rising"), .behavior("old")) counter_5 (
    .count(and_16_out), .Q(\插入气泡数 ), .clk(CLK));  // open: load, D, carry, clr, preset

  // Other names for the same wires on the sheet: JALR = Instr[0]; JAL = Instr[2]; MEM_PC[31:0] = M_PC;
  //   stall = DataHazzard

  // Notes on the sheet:
  //   中断源
  //   时空图监测，可删除
  //   中断等待指示
  //   数码管输出
  //   指令存储器
  //   PC
  //   PC+4
  //   控制位
  //   IF/ID
  //   IR
  //   contents of rom_1 (hex, n*v repeats v):
  //   100493 100006f 100493 200913 300993 100006f 100493 200913 300993 100006f 100493 200913 300993
  //   100006f 100493 200913 300993 404000ef 100413 100493 1f49493 900533 2200893 73 24d493 48463 fedff06f
  //   900533 2200893 73 100493 249493 900533 2200893 73 48463 fedff06f 100493 1f49493 900533 2200893 73
  //   4034d493 900533 2200893 73 4044d493 900533 2200893 73 4044d493 900533 2200893 73 4044d493 900533
  //   2200893 73 4044d493 900533 2200893 73 4044d493 900533 2200893 73 4044d493 900533 2200893 73 4044d493
  //   900533 2200893 73 100413 1f41993 41f9d993 433 c00913 300b13 140413 f47413 800293 100313 499993
  //   89e9b3 1300533 2200893 73 406282b3 fe0294e3 140413 f00f93 1f47433 1c41413 800293 100313 49d993
  //   89e9b3 1300533 2200893 73 406282b3 fe0294e3 1c45413 406b0b33 b0463 f95ff06f 2b3 fff2c293 829293
  //   ff2e293 500533 2200893 73 fff00413 493 84a023 140413 448493 84a023 140413 448493 84a023 140413
  //   448493 84a023 140413 448493 84a023 140413 448493 84a023 140413 448493 84a023 140413 448493 84a023
  //   140413 448493 84a023 140413 448493 84a023 140413 448493 84a023 140413 448493 84a023 140413 448493
  //   84a023 140413 448493 84a023 140413 448493 84a023 140413 448493 84a023 140413 448493 140413 433
  //   3c00493 42983 4aa03 149a2b3 28663 134a023 1442023 ffc48493 fe9412e3 800533 2200893 73 440413 3c00493
  //   fc9416e3 3200893 73 13 430497 900533 2200893 73 430497 900533 2200893 73 430497 900533 2200893 73
  //   430497 900533 2200893 73 430497 900533 2200893 73 430497 900533 2200893 73 430497 900533 2200893 73
  //   430497 900533 2200893 73 a00893 73 fff00293 313 1900413 841413 9700493 940533 2200893 73 5484b3
  //   494b313 fe0306e3 a00893 73 313 1000e13 8400493 849493 8348493 400913 891913 490913 849493 8248493
  //   849493 8148493 891913 490913 891913 490913 932023 12484b3 430313 fffe0e13 fe0e18e3 2000e13 313 30483
  //   900533 2200893 73 130313 fffe0e13 fe0e14e3 a00893 73 f00493 900533 2200893 73 fff48493 fe04d8e3
  //   a00893 73 a00893 73 413 140413 800533 2200893 73 240413 800533 2200893 73 340413 800533 2200893 73
  //   440413 800533 2200893 73 540413 800533 2200893 73 640413 800533 2200893 73 740413 800533 2200893 73
  //   840413 800533 2200893 2200893 73 8067
  //   流水调试日志用
  //   暂停节拍，不能为0
  //   戳工具置1进入计数暂停模式，ctrl+k时钟自动运行到对应节拍暂停
  //   ctrl+k关闭时钟连续运行，将控制位置零，进入单步调试模式调试
  //   rd
  //   IR
  //   I型
  //   S型
  //   B型
  //   J型
  //   Beq
  //   Bne
  //   MemToReg
  //   MemWrite
  //   AluOP
  //   AluSrcB
  //   RegWrite
  //   S_Tyoe
  //   rs1
  //   rs2
  //   可计数暂停的时钟源
  //   ID/EX
  //   为方便自动评测，需要输出流水线各段保存的PC值，注意是PC不是PC+4，另外ID段寄存器写入信息，Mem段内存写入信息也要输出
  //   AluResult
  //   WriteData
  //   EX/MEM
  //   数据存储器
  //   MEM/WB
endmodule
module \重定向中断流水线  (
  output RegWrite,
  output MemWrite,
  output [31:0] IF_PC,
  output [31:0] ID_PC,
  output [31:0] EX_PC,
  output [31:0] M_PC,
  output [31:0] WB_PC,
  output [31:0] RDin,
  output [31:0] MDin,
  output [31:0] LedData
);

  wire AluSrcB, and_1_out, and_2_out, and_3_out, and_4_out, and_5_out, and_6_out, and_7_out, and_8_out,
       and_9_out, and_10_out, and_11_out, and_12_out, and_13_out, and_14_out, and_15_out, and_20_out,
       and_21_out, and_22_out, and_23_out, and_24_out, and_25_out, and_26_out, and_28_out, and_29_out,
       and_30_out, AUIPC_mem, Beq, Bge, Bne, CLK, clock_1_out, Clr1, Clr2, Clr3, comparator_1_eq,
       comparator_2_eq, comparator_3_eq, comparator_4_eq, comparator_5_eq, comparator_6_eq, comparator_6_gt,
       comparator_7_eq, comparator_7_lt, comparator_8_eq, comparator_9_eq, comparator_10_eq,
       comparator_11_eq, comparator_12_eq, comparator_13_eq, comparator_14_eq, comparator_15_eq,
       comparator_16_eq, comparator_17_eq, comparator_18_eq, comparator_19_eq, d_ff_1_q, DataHazzard, ecall,
       ecall_id, equal, \ex_mem流水寄存器_1_ecallout , \ex_mem流水寄存器_1_jout , \ex_mem流水寄存器_1_lbout ,
       \ex_mem流水寄存器_1_memtoregout , Go, halt, \id_ex流水寄存器_1_alusrcbout , \id_ex流水寄存器_1_auipcout ,
       \id_ex流水寄存器_1_ecallout , \id_ex流水寄存器_1_lbout , \id_ex流水寄存器_1_memwriteout , \if_id流水寄存器_1_introut ,
       Intout, IntR, IntR_ex, IntRe, IR1, IR1_2_q, IR1_3_q, IR1_4_q, IR1_q, IR2, IR2_2_q, IR2_q, IR3, IRA,
       IRa_t, IRB, IRb_t, IRC, IRc_t, JAL_id, LoadUse, MemToReg_ex, nand_1_out, not_1_out, not_2_out,
       not_3_out, not_4_out, not_6_out, not_7_out, not_8_out, not_9_out, not_10_out, not_11_out, not_13_out,
       not_14_out, not_15_out, not_16_out, not_17_out, not_18_out, or_1_out, or_2_out, or_3_out, or_8_out,
       or_14_out, or_15_out, or_16_out, or_19_out, or_20_out, or_21_out, or_22_out, or_23_out, PCSrc,
       register_3_q, RegWrite_ex, RegWrite_mem, Rs1used, Rs2used, RST, S_Type, tunnel, URET, W1, W2, W3,
       \单周期硬布线控制器_1_auipc , \单周期硬布线控制器_1_beq , \单周期硬布线控制器_1_bge , \单周期硬布线控制器_1_bne , \单周期硬布线控制器_1_jalr ,
       \单周期硬布线控制器_1_lb , \单周期硬布线控制器_1_memtoreg , \单周期硬布线控制器_1_memwrite , \单周期硬布线控制器_1_regwrite ,
       \单周期硬布线控制器_1_uret ;
  wire [0:0] and_27_out;
  wire [1:0] \id_ex流水寄存器_1_ecallout_2 , \id_ex流水寄存器_1_r1srcout , \mem_wb流水寄存器_1_jout ,
       \mem_wb流水寄存器_1_memtoregout , \mem_wb流水寄存器_1_selout , priority_encoder_1_out, R1Src, R2Src,
       register_2_q;
  wire [2:0] Instr;
  wire [3:0] \id_ex流水寄存器_1_aluopout , \单周期硬布线控制器_1_alu_op ;
  wire [4:0] multiplexer_2_out, multiplexer_3_out, multiplexer_5_out, multiplexer_6_out, multiplexer_9_out,
       multiplexer_10_out, Rd, rd_ex, rd_mem;
  wire [11:0] multiplexer_11_out;
  wire [12:0] CNT_num;
  wire [15:0] \LoadUse次数 , \总周期数 , \插入气泡数 , \无条件分支数 , \条件分支成功数 ;
  wire [31:0] adder_1_out, adder_2_out, adder_3_out, adder_4_out, adder_5_out, Ain, alu_1_result, AluResult,
       AluResult_in, and_31_out, Bin, bit_extender_1_out, bit_extender_2_out, bit_extender_3_out,
       bit_extender_4_out, bit_extender_5_out, bit_extender_6_out, bit_extender_7_out, bit_extender_8_out,
       BranchAddr, EX_IR, \ex_mem流水寄存器_1_auipc_out , \ex_mem流水寄存器_1_r1out , \id_ex流水寄存器_1_bout ,
       \id_ex流水寄存器_1_i_sout , \id_ex流水寄存器_1_iout , \id_ex流水寄存器_1_pc_4out , \id_ex流水寄存器_1_r1out ,
       \id_ex流水寄存器_1_r2out , \id_ex流水寄存器_1_uout , ID_IR, \if_id流水寄存器_1_pc_4out , IF_IR, IntPrc, MEM_IR,
       \mem_wb流水寄存器_1_aluresultout , \mem_wb流水寄存器_1_auipc_out , \mem_wb流水寄存器_1_pc_4out ,
       \mem_wb流水寄存器_1_writedataout , mEPCout, multiplexer_7_out, multiplexer_14_out, multiplexer_17_out,
       multiplexer_18_out, PC_next, PC_q, R1, R2, ram_1_data, regifile_1_r1, regifile_1_r2, shifter_1_out,
       shifter_2_out, shifter_3_out, WB_IR;

  Button \u_总复位  (.out(RST));
  Button _1 (.out(IR1));
  Button _2 (.out(IR2));
  Button _3 (.out(IR3));
  // Probe on \总周期数 
  // Probe on \总周期数 
  Button \u_继续运行  (.out(Go));
  LED #(.active("true")) led_1 (.in(W1));
  LED #(.active("true")) led_2 (.in(W2));
  LED #(.active("true")) led_3 (.in(W3));
  Hex_Digit_Display hex_digit_display_1 (.value(LedData[31:28]));  // open: dp
  // Probe on IF_PC[19:0]
  // RiscV_Probe riscv_probe_1: pin names not known; wires that end beside it: IF_IR
  Hex_Digit_Display hex_digit_display_2 (.value(LedData[27:24]));  // open: dp
  Hex_Digit_Display hex_digit_display_3 (.value(LedData[23:20]));  // open: dp
  // Probe on ID_PC[19:0]
  // RiscV_Probe riscv_probe_2: pin names not known; wires that end beside it: ID_IR
  not not_1 (not_1_out, equal);
  not not_2 (not_2_out, equal);
  Hex_Digit_Display hex_digit_display_4 (.value(LedData[19:16]));  // open: dp
  Hex_Digit_Display hex_digit_display_5 (.value(LedData[15:12]));  // open: dp
  and and_1 (and_1_out, Bge, tunnel);
  and and_2 (and_2_out, Beq, equal);
  and and_3 (and_3_out, Bne, not_1_out);
  or or_1 (or_1_out, Instr[2], Instr[0]);
  Comparator #(.width(32), .mode("unsigned")) comparator_1 (.a(R1), .b(32'h22), .eq(comparator_1_eq));  // open: gt, lt
  and and_4 (and_4_out, Beq, equal);
  and and_5 (and_5_out, Bne, not_2_out);
  not not_3 (not_3_out, halt);
  Hex_Digit_Display hex_digit_display_6 (.value(LedData[7:4]));  // open: dp
  Hex_Digit_Display hex_digit_display_7 (.value(LedData[11:8]));  // open: dp
  // Probe on EX_PC[19:0]
  // RiscV_Probe riscv_probe_3: pin names not known; wires that end beside it: EX_IR
  or or_2 (or_2_out, Instr[0], Instr[2]);
  or or_3 (or_3_out, and_4_out, and_5_out);
  Hex_Digit_Display hex_digit_display_8 (.value(LedData[3:0]));  // open: dp
  Comparator #(.width(16), .mode("twosComplement")) comparator_2 (
    .a(16'h23b), .b(\总周期数 ), .eq(comparator_2_eq));  // open: gt, lt
  Comparator #(.width(16), .mode("twosComplement")) comparator_3 (
    .a(\总周期数 ), .b(16'h1), .eq(comparator_3_eq));  // open: gt, lt
  Comparator #(.width(16), .mode("twosComplement")) comparator_4 (
    .a(\总周期数 ), .b(16'h4), .eq(comparator_4_eq));  // open: gt, lt
  Comparator #(.width(16), .mode("twosComplement")) comparator_5 (
    .a(\总周期数 ), .b(16'h7), .eq(comparator_5_eq));  // open: gt, lt
  or or_4 (IRA, IR1, IRa_t);
  or or_5 (IRB, IR2, IRb_t);
  or or_6 (IRC, IR3, IRc_t);
  or or_7 (PCSrc, and_1_out, and_2_out, and_3_out, or_1_out);
  and and_6 (and_6_out, ecall, comparator_1_eq);
  and and_7 (and_7_out, ecall, ~comparator_1_eq);  // AND_Gate
  and and_8 (and_8_out, or_2_out, not_3_out);
  and and_9 (and_9_out, or_3_out, not_3_out);
  and and_10 (and_10_out, LoadUse, not_3_out);
  and and_11 (and_11_out, LoadUse, not_3_out);
  // Probe on \总周期数 
  // Probe on M_PC[19:0]
  // RiscV_Probe riscv_probe_4: pin names not known; wires that end beside it: MEM_IR
  or or_8 (or_8_out, comparator_2_eq, comparator_3_eq);
  assign IRa_t = or_8_out ? ~CLK : 1'bz;  // Controlled_Inverter controlled_inverter_1
  assign IRb_t = comparator_4_eq ? ~CLK : 1'bz;  // Controlled_Inverter controlled_inverter_2
  assign IRc_t = comparator_5_eq ? ~CLK : 1'bz;  // Controlled_Inverter controlled_inverter_3
  Multiplexer #(.select(1), .width(1), .disabled("Z"), .enable("false")) multiplexer_1 (
    .in0(and_7_out), .in1(1'b0), .out(halt), .sel(Go));
  Counter #(.width(16), .max('hffff), .ongoal("stay"), .trigger("rising"), .behavior("old")) counter_1 (
    .count(and_8_out), .Q(\无条件分支数 ), .clk(CLK));  // open: load, D, carry, clr, preset
  Counter #(.width(16), .max('hffff), .ongoal("stay"), .trigger("rising"), .behavior("old")) counter_2 (
    .count(and_9_out), .Q(\条件分支成功数 ), .clk(CLK));  // open: load, D, carry, clr, preset
  Counter #(.width(16), .max('hffff), .ongoal("stay"), .trigger("rising"), .behavior("old")) counter_3 (
    .count(and_10_out), .Q(\插入气泡数 ), .clk(CLK));  // open: load, D, carry, clr, preset
  Counter #(.width(16), .max('hffff), .ongoal("stay"), .trigger("rising"), .behavior("old")) counter_4 (
    .count(and_11_out), .Q(\LoadUse次数 ), .clk(CLK));  // open: load, D, carry, clr, preset
  // Probe on \总周期数 
  // Probe on \无条件分支数 
  // Probe on \条件分支成功数 
  // Probe on \LoadUse次数 
  // Probe on \插入气泡数 
  Pull_Resistor #(.pull(0)) pull_resistor_1 (.node(IRa_t));
  Pull_Resistor #(.pull(0)) pull_resistor_2 (.node(IRb_t));
  Pull_Resistor #(.pull(0)) pull_resistor_3 (.node(IRc_t));
  // Probe on IF_PC[11:0]
  // Probe on WB_PC[19:0]
  // RiscV_Probe riscv_probe_5: pin names not known; wires that end beside it: WB_IR
  Comparator #(.width(32), .mode("twosComplement")) comparator_6 (
    .a(Ain), .b(Bin), .gt(comparator_6_gt), .eq(comparator_6_eq));  // open: lt
  or or_9 (Instr[1], Beq, Bge, Bne);
  // Probe on ID_PC[11:0]
  // Probe on EX_PC[11:0]
  or or_10 (tunnel, comparator_6_gt, comparator_6_eq);
  Register #(.width(32), .trigger("rising"), .Select("low")) register_1 (
    .D(R2), .en(and_6_out), .Q(LedData), .clk(CLK));  // open: clr
  Counter #(.width(16), .max('hffff), .ongoal("stay"), .trigger("rising"), .behavior("old")) counter_5 (
    .count(not_4_out), .Q(\总周期数 ), .clk(CLK));  // open: load, D, carry, clr, preset
  not not_4 (not_4_out, halt);
  // Probe on M_PC[11:0]
  D_Flip_Flop #(.trigger("high"), .Pre_Clr_Positions("LEGACY"), .NegatePresetClear("false"), .enable("true"), .NewFFLayout("false")) d_ff_1 (.Q(d_ff_1_q));  // open: clk, D, Qn, preset, en, reset
  // Probe on 13'hb4
  D_Flip_Flop #(.trigger("rising"), .Pre_Clr_Positions("LEGACY"), .NegatePresetClear("false"), .enable("true"), .NewFFLayout("false")) u_IR1 (
    .clk(IR1), .D(1'b1), .Q(IR1_q), .reset(IR1_4_q));  // open: Qn, preset, en
  or or_11 (W1, IR1_4_q, IR1_q);
  D_Flip_Flop #(.trigger("rising"), .Pre_Clr_Positions("LEGACY"), .NegatePresetClear("false"), .enable("true"), .NewFFLayout("false")) IR1_2 (
    .clk(IR2), .D(1'b1), .Q(IR1_2_q), .reset(IR2_q));  // open: Qn, preset, en
  or or_12 (W2, IR2_q, IR1_2_q);
  D_Flip_Flop #(.trigger("rising"), .Pre_Clr_Positions("LEGACY"), .NegatePresetClear("false"), .enable("true"), .NewFFLayout("false")) IR1_3 (
    .clk(IR3), .D(1'b1), .Q(IR1_3_q), .reset(IR2_2_q));  // open: Qn, preset, en
  or or_13 (W3, IR2_2_q, IR1_3_q);
  // Probe on WB_PC[11:0]
  Comparator #(.width(13), .mode("twosComplement")) comparator_7 (
    .a(CNT_num), .b(13'hb4), .eq(comparator_7_eq), .lt(comparator_7_lt));  // open: gt
  Clock #(.highDuration(1), .lowDuration(1)) clock_1 (.out(clock_1_out));
  nand nand_1 (nand_1_out, d_ff_1_q, comparator_7_eq);
  Counter #(.width(13), .max('h1fff), .ongoal("stay"), .trigger("rising"), .behavior("old")) counter_6 (
    .count(comparator_7_lt), .Q(CNT_num), .clk(clock_1_out));  // open: load, D, carry, clr, preset
  or or_14 (or_14_out, IR1_q, IR1_4_q);
  or or_15 (or_15_out, IR1_2_q, IR2_q);
  or or_16 (or_16_out, IR1_3_q, IR2_2_q);
  assign CLK = nand_1_out ? clock_1_out : 1'bz;  // Controlled_Buffer controlled_buffer_1
  and and_12 (and_12_out, or_14_out, ~Clr1);  // AND_Gate
  and and_13 (and_13_out, or_15_out, ~Clr2);  // AND_Gate
  and and_14 (and_14_out, or_16_out, ~Clr3);  // AND_Gate
  Pull_Resistor #(.pull(1)) pull_resistor_4 (.node(CLK));
  and and_15 (and_15_out, AluSrcB, ~S_Type);  // AND_Gate
  D_Flip_Flop #(.trigger("rising"), .Pre_Clr_Positions("LEGACY"), .NegatePresetClear("false"), .enable("true"), .NewFFLayout("false")) IR1_4 (
    .clk(CLK), .D(and_12_out), .Q(IR1_4_q));  // open: Qn, preset, en, reset
  D_Flip_Flop #(.trigger("rising"), .Pre_Clr_Positions("LEGACY"), .NegatePresetClear("false"), .enable("true"), .NewFFLayout("false")) u_IR2 (
    .clk(CLK), .D(and_13_out), .Q(IR2_q));  // open: Qn, preset, en, reset
  D_Flip_Flop #(.trigger("rising"), .Pre_Clr_Positions("LEGACY"), .NegatePresetClear("false"), .enable("true"), .NewFFLayout("false")) IR2_2 (
    .clk(CLK), .D(and_14_out), .Q(IR2_2_q));  // open: Qn, preset, en, reset
  not not_5 (Rs1used, JAL_id);
  nor nor_1 (Rs2used, JAL_id, and_15_out);
  Multiplexer #(.select(1), .width(5), .disabled("Z"), .enable("false")) multiplexer_2 (
    .in0(ID_IR[19:15]), .in1(5'b10001), .out(multiplexer_2_out), .sel(ecall_id));
  Multiplexer #(.select(1), .width(5), .disabled("Z"), .enable("false")) multiplexer_3 (
    .in0(ID_IR[24:20]), .in1(5'b01010), .out(multiplexer_3_out), .sel(ecall_id));
  Comparator #(.width(5), .mode("unsigned")) comparator_8 (
    .a(rd_mem), .b(multiplexer_2_out), .eq(comparator_8_eq));  // open: gt, lt
  Comparator #(.width(5), .mode("unsigned")) comparator_9 (
    .a(rd_mem), .b(multiplexer_3_out), .eq(comparator_9_eq));  // open: gt, lt
  Comparator #(.width(5), .mode("unsigned")) comparator_10 (
    .a(rd_ex), .b(multiplexer_2_out), .eq(comparator_10_eq));  // open: gt, lt
  Comparator #(.width(5), .mode("unsigned")) comparator_11 (
    .a(rd_ex), .b(multiplexer_3_out), .eq(comparator_11_eq));  // open: gt, lt
  Comparator #(.width(5), .mode("unsigned")) comparator_12 (
    .a(multiplexer_2_out), .b({5{1'b0}}), .eq(comparator_12_eq));  // open: gt, lt
  Comparator #(.width(5), .mode("unsigned")) comparator_13 (
    .a(multiplexer_3_out), .b({5{1'b0}}), .eq(comparator_13_eq));  // open: gt, lt
  Priority_Encoder #(.select(2), .disabled("Z")) priority_encoder_1 (
    .in0(IR1_4_q), .in1(IR2_q), .in2(IR2_2_q), .out(priority_encoder_1_out), .gs(Intout), .en_in(1'b1));  // open: in3, en_out
  not not_6 (not_6_out, comparator_12_eq);
  not not_7 (not_7_out, comparator_13_eq);
  Multiplexer #(.select(2), .width(32), .disabled("Z"), .enable("false")) multiplexer_4 (
    .in0(32'h30ac), .in1(32'h3150), .in2(32'h31f4), .out(IntPrc), .sel(priority_encoder_1_out));  // open: in3
  and and_16 (R1Src[0], RegWrite_mem, comparator_8_eq, not_8_out, not_6_out, Rs1used);
  and and_17 (R1Src[1], RegWrite_ex, comparator_10_eq, not_6_out, Rs1used);
  and and_18 (R2Src[0], RegWrite_mem, comparator_9_eq, not_9_out, not_7_out, Rs2used);
  and and_19 (R2Src[1], comparator_11_eq, RegWrite_ex, not_7_out, Rs2used);
  and and_20 (and_20_out, Rs1used, not_6_out, comparator_10_eq, MemToReg_ex);
  and and_21 (and_21_out, Rs2used, not_7_out, comparator_11_eq, MemToReg_ex);
  Register #(.width(2), .trigger("falling"), .Select("low")) register_2 (
    .D(priority_encoder_1_out), .en(IntR), .Q(register_2_q), .clk(CLK));  // open: clr
  and and_22 (and_22_out, Intout, IntRe);
  Multiplexer #(.select(1), .width(5), .disabled("Z"), .enable("false")) multiplexer_5 (
    .in0(ID_IR[19:15]), .in1(5'b10001), .out(multiplexer_5_out), .sel(ecall_id));
  Multiplexer #(.select(1), .width(5), .disabled("Z"), .enable("false")) multiplexer_6 (
    .in0(ID_IR[24:20]), .in1(5'b01010), .out(multiplexer_6_out), .sel(ecall_id));
  not not_8 (not_8_out, R1Src[1]);
  not not_9 (not_9_out, R2Src[1]);
  Decoder #(.select(2), .tristate("false"), .disabled(0), .enable("true")) decoder_1 (
    .out0(Clr1), .out1(Clr2), .out2(Clr3), .sel(register_2_q), .en(URET));  // open: out3
  Register #(.width(1), .trigger("rising"), .Select("low")) \u_中断使能寄存器IE  (
    .D(and_22_out), .Q(IntR), .clk(CLK));  // open: en, clr
  or or_17 (LoadUse, and_20_out, and_21_out);
  Comparator #(.width(5), .mode("unsigned")) comparator_14 (
    .a(rd_ex), .b(multiplexer_5_out), .eq(comparator_14_eq));  // open: gt, lt
  Comparator #(.width(5), .mode("unsigned")) comparator_15 (
    .a(rd_ex), .b(multiplexer_6_out), .eq(comparator_15_eq));  // open: gt, lt
  Comparator #(.width(5), .mode("unsigned")) comparator_16 (
    .a(rd_mem), .b(multiplexer_5_out), .eq(comparator_16_eq));  // open: gt, lt
  Comparator #(.width(5), .mode("unsigned")) comparator_17 (
    .a(rd_mem), .b(multiplexer_6_out), .eq(comparator_17_eq));  // open: gt, lt
  Comparator #(.width(5), .mode("unsigned")) comparator_18 (
    .a(multiplexer_5_out), .b({5{1'b0}}), .eq(comparator_18_eq));  // open: gt, lt
  Comparator #(.width(5), .mode("unsigned")) comparator_19 (
    .a(multiplexer_6_out), .b({5{1'b0}}), .eq(comparator_19_eq));  // open: gt, lt
  not not_10 (not_10_out, comparator_18_eq);
  not not_11 (not_11_out, comparator_19_eq);
  Register #(.width(32), .trigger("rising"), .Select("low")) mEPC (
    .D(PC_next), .en(IntR_ex), .Q(mEPCout), .clk(CLK));  // open: clr
  and and_23 (and_23_out, Rs1used, comparator_14_eq, not_10_out, RegWrite_ex);
  and and_24 (and_24_out, Rs2used, comparator_15_eq, not_11_out, RegWrite_ex);
  and and_25 (and_25_out, Rs1used, comparator_16_eq, not_10_out, RegWrite_mem);
  and and_26 (and_26_out, Rs2used, comparator_17_eq, not_11_out, RegWrite_mem);
  Register #(.width(1), .trigger("rising"), .Select("low")) register_3 (
    .D(1'b0), .en(URET), .Q(register_3_q), .clk(CLK), .preset(IntR));  // open: clr, cs
  not not_12 (IntRe, register_3_q);
  or or_18 (DataHazzard, and_23_out, and_24_out, and_25_out, and_26_out);
  not not_13 (not_13_out, IntR);
  and and_27 (and_27_out[0], not_13_out, PCSrc);
  Multiplexer #(.select(2), .width(32), .disabled("Z"), .enable("false")) multiplexer_7 (
    .in0(adder_1_out), .in1(BranchAddr), .in2(mEPCout), .in3(mEPCout), .out(multiplexer_7_out),
    .sel({URET, and_27_out[0]}));
  and and_28 (and_28_out, not_14_out, not_15_out);
  not not_14 (not_14_out, LoadUse);
  not not_15 (not_15_out, halt);
  Register #(.width(32), .trigger("rising"), .Select("low")) PC (
    .D(multiplexer_7_out), .en(and_28_out), .Q(PC_q), .clk(CLK), .clr(RST));
  Multiplexer #(.select(1), .width(32), .disabled("Z"), .enable("false")) multiplexer_8 (
    .in0(PC_q), .in1(IntPrc), .out(IF_PC), .sel(IntR));
  Adder #(.width(32)) adder_1 (.a(IF_PC), .b(32'h4), .out(adder_1_out));  // open: cin, cout
  and and_29 (and_29_out, not_16_out, or_20_out);
  not not_16 (not_16_out, IntR);
  ROM #(.addrWidth(10), .dataWidth(32), .Select("high")) rom_1 (.addr(IF_PC[11:2]), .data(IF_IR));
  or or_19 (or_19_out, halt, LoadUse);
  or or_20 (or_20_out, RST, PCSrc);
  \IF_ID流水寄存器  \if_id流水寄存器_1  (
    .IR(IF_IR), .PC(IF_PC), .PC_4(adder_1_out), .CLK(CLK), .IRout(ID_IR), .PCout(ID_PC),
    .PC_4out(\if_id流水寄存器_1_pc_4out ), .\同步清零_气泡_高电平有效 (and_29_out), .\使能端_低电平有效_stall_高电平有效 (or_19_out),
    .IntR(IntR), .IntRout(\if_id流水寄存器_1_introut ));
  \单周期硬布线控制器  \u_单周期硬布线控制器_1  (
    .Funct({ID_IR[30], ID_IR[25], ID_IR[14:12]}), .OP(ID_IR[6:2]), .ALU_OP(\单周期硬布线控制器_1_alu_op ),
    .MemToReg(\单周期硬布线控制器_1_memtoreg ), .MemWrite(\单周期硬布线控制器_1_memwrite ), .ALU_SRC(AluSrcB),
    .RegWrite(\单周期硬布线控制器_1_regwrite ), .ecall(ecall_id), .S_type(S_Type), .Jalr(\单周期硬布线控制器_1_jalr ),
    .Beq(\单周期硬布线控制器_1_beq ), .JAL(JAL_id), .Bne(\单周期硬布线控制器_1_bne ), .in_3(ID_IR[21]),
    .uret(\单周期硬布线控制器_1_uret ), .AUIPC(\单周期硬布线控制器_1_auipc ), .lb(\单周期硬布线控制器_1_lb ), .Bge(\单周期硬布线控制器_1_bge ));
  Multiplexer #(.select(1), .width(5), .disabled("Z"), .enable("false")) multiplexer_9 (
    .in0(ID_IR[19:15]), .in1(5'b10001), .out(multiplexer_9_out), .sel(ecall_id));
  Multiplexer #(.select(1), .width(5), .disabled("Z"), .enable("false")) multiplexer_10 (
    .in0(ID_IR[24:20]), .in1(5'b01010), .out(multiplexer_10_out), .sel(ecall_id));
  Multiplexer #(.select(1), .width(12), .disabled("Z"), .enable("false")) multiplexer_11 (
    .in0(ID_IR[31:20]), .in1({ID_IR[31:25], ID_IR[11:7]}), .out(multiplexer_11_out), .sel(S_Type));
  assign bit_extender_1_out = {{20{multiplexer_11_out[11]}}, multiplexer_11_out};  // Bit_Extender bit_extender_1
  assign bit_extender_2_out = {{20{ID_IR[31]}}, {ID_IR[31], ID_IR[7], ID_IR[30:25], ID_IR[11:8]}};  // Bit_Extender bit_extender_2
  assign bit_extender_3_out = {{12{ID_IR[31]}}, {ID_IR[31], ID_IR[19:12], ID_IR[20], ID_IR[30:21]}};  // Bit_Extender bit_extender_3
  assign bit_extender_4_out = {{12{ID_IR[31]}}, ID_IR[31:12]};  // Bit_Extender bit_extender_4
  not not_17 (not_17_out, \if_id流水寄存器_1_introut );
  Regifile regifile_1 (
    .Din(RDin), .Clk(CLK), .R1(regifile_1_r1), .R2(regifile_1_r2), .WE(RegWrite), .W_num(Rd),
    .R1_num(multiplexer_9_out), .R2_num(multiplexer_10_out));
  or or_21 (or_21_out, IntR_ex, RST, URET, PCSrc, LoadUse);
  and and_30 (and_30_out, not_17_out, or_21_out);
  \ID_EX流水寄存器  \id_ex流水寄存器_1  (
    .JAL(JAL_id), .JALR(\单周期硬布线控制器_1_jalr ), .URET(\单周期硬布线控制器_1_uret ), .Beq(\单周期硬布线控制器_1_beq ),
    .Bne(\单周期硬布线控制器_1_bne ), .MemToReg(\单周期硬布线控制器_1_memtoreg ), .AluOp(\单周期硬布线控制器_1_alu_op ),
    .AluSrcB(AluSrcB), .RegWrite(\单周期硬布线控制器_1_regwrite ), .I_S(bit_extender_1_out), .B(bit_extender_2_out),
    .I(bit_extender_3_out), .CLK(CLK), .JALout(Instr[2]), .JALRout(Instr[0]), .URETout(URET), .Beqout(Beq),
    .Bneout(Bne), .MemToRegout(MemToReg_ex), .AluOpout(\id_ex流水寄存器_1_aluopout ),
    .AluSrcBout(\id_ex流水寄存器_1_alusrcbout ), .RegWrite_2(RegWrite_ex), .I_Sout(\id_ex流水寄存器_1_i_sout ),
    .Bout(\id_ex流水寄存器_1_bout ), .Iout(\id_ex流水寄存器_1_iout ), .\同步清零_气泡_高电平有效 (and_30_out),
    .\使能端_低电平有效_stall_高电平有效 (halt), .R1(regifile_1_r1), .R1out(\id_ex流水寄存器_1_r1out ), .R2(regifile_1_r2),
    .R2out(\id_ex流水寄存器_1_r2out ), .MemWrite(\单周期硬布线控制器_1_memwrite ),
    .MemWriteout(\id_ex流水寄存器_1_memwriteout ), .PC(ID_PC), .PCout(EX_PC), .PC_4(\if_id流水寄存器_1_pc_4out ),
    .PC_4out(\id_ex流水寄存器_1_pc_4out ), .Rd(ID_IR[11:7]), .Rdout(rd_ex), .IR(ID_IR), .IRout(EX_IR),
    .ecall(ecall_id), .ecallout(\id_ex流水寄存器_1_ecallout ), .R1Src(R1Src), .R1Srcout(\id_ex流水寄存器_1_r1srcout ),
    .R2Src(R2Src), .ecallout_2(\id_ex流水寄存器_1_ecallout_2 ), .AUIPC(\单周期硬布线控制器_1_auipc ),
    .AUIPCout(\id_ex流水寄存器_1_auipcout ), .lb(\单周期硬布线控制器_1_lb ), .lbout(\id_ex流水寄存器_1_lbout ),
    .Bge(\单周期硬布线控制器_1_bge ), .Bgeout(Bge), .U(bit_extender_4_out), .Uout(\id_ex流水寄存器_1_uout ),
    .IntR(\if_id流水寄存器_1_introut ), .IntRout(IntR_ex));
  Multiplexer #(.select(2), .width(32), .disabled("Z"), .enable("false")) multiplexer_12 (
    .in0(\id_ex流水寄存器_1_r1out ), .in1(RDin), .in2(AluResult_in), .out(Ain), .sel(\id_ex流水寄存器_1_r1srcout ));  // open: in3
  Multiplexer #(.select(2), .width(32), .disabled("Z"), .enable("false")) multiplexer_13 (
    .in0(\id_ex流水寄存器_1_r2out ), .in1(RDin), .in2(AluResult_in), .out(Bin), .sel(\id_ex流水寄存器_1_ecallout_2 ));  // open: in3
  Multiplexer #(.select(1), .width(32), .disabled("Z"), .enable("false")) multiplexer_14 (
    .in0(Bin), .in1(\id_ex流水寄存器_1_i_sout ), .out(multiplexer_14_out), .sel(\id_ex流水寄存器_1_alusrcbout ));
  Adder #(.width(32)) adder_2 (.a(\id_ex流水寄存器_1_i_sout ), .b(Ain), .out(adder_2_out));  // open: cin, cout
  Shifter #(.width(32), .shift("ll")) shifter_1 (.in(\id_ex流水寄存器_1_bout ), .\dist (5'b00001), .out(shifter_1_out));
  Shifter #(.width(32), .shift("ll")) shifter_2 (.in(\id_ex流水寄存器_1_iout ), .\dist (5'b00001), .out(shifter_2_out));
  Shifter #(.width(32), .shift("ll")) shifter_3 (.in(\id_ex流水寄存器_1_uout ), .\dist (5'b01100), .out(shifter_3_out));
  or or_22 (or_22_out, Instr[2], Instr[0]);
  ALU alu_1 (
    .X(Ain), .Y(multiplexer_14_out), .AluOP(\id_ex流水寄存器_1_aluopout ), .Equal(equal), .Result(alu_1_result));  // open: Result_2, out_4, out_6
  assign and_31_out = adder_2_out & 32'hfffffffe;  // AND_Gate and_31, 32 bits wide
  Adder #(.width(32)) adder_3 (.a(shifter_1_out), .b(EX_PC), .out(adder_3_out));  // open: cin, cout
  Adder #(.width(32)) adder_4 (.a(shifter_2_out), .b(EX_PC), .out(adder_4_out));  // open: cin, cout
  Adder #(.width(32)) adder_5 (.a(shifter_3_out), .b(EX_PC), .out(adder_5_out));  // open: cin, cout
  Multiplexer #(.select(3), .width(32), .disabled("Z"), .enable("false")) multiplexer_15 (
    .in1(and_31_out), .in2(adder_3_out), .in4(adder_4_out), .out(BranchAddr), .sel(Instr));  // open: in0, in3, in5, in6, in7
  or or_23 (or_23_out, IntR_ex, RST);
  \EX_MEM流水寄存器  \ex_mem流水寄存器_1  (
    .MemToReg(MemToReg_ex), .MemWrite(\id_ex流水寄存器_1_memwriteout ), .RegWrite(RegWrite_ex),
    .AluResult(alu_1_result), .Rd(rd_ex), .CLK(CLK), .MemToRegout(\ex_mem流水寄存器_1_memtoregout ),
    .MemWriteout(MemWrite), .RegWriteout(RegWrite_mem), .AluResultout(AluResult), .Rdout(rd_mem),
    .\同步清零_气泡_高电平有效 (or_23_out), .\使能端_低电平有效_stall_高电平有效 (halt), .WriteData(Bin), .WriteDataout(MDin),
    .PC_4(\id_ex流水寄存器_1_pc_4out ), .PC_4out(PC_next), .J(\id_ex流水寄存器_1_lbout ), .Jout(\ex_mem流水寄存器_1_jout ),
    .IR(EX_IR), .IRout(MEM_IR), .PC(EX_PC), .PCout(M_PC), .ecall(\id_ex流水寄存器_1_ecallout ),
    .ecallout(\ex_mem流水寄存器_1_ecallout ), .R1(Ain), .R1out(\ex_mem流水寄存器_1_r1out ),
    .AUIPC(\id_ex流水寄存器_1_auipcout ), .AUIPCout(AUIPC_mem), .lb(or_22_out), .lbout(\ex_mem流水寄存器_1_lbout ),
    .auipc_res(adder_5_out), .auipc_out(\ex_mem流水寄存器_1_auipc_out ));
  Multiplexer #(.select(1), .width(32), .disabled("Z"), .enable("false")) multiplexer_16 (
    .in0(AluResult), .in1(\ex_mem流水寄存器_1_auipc_out ), .out(AluResult_in), .sel(AUIPC_mem));
  RAM #(.addrWidth(10), .dataWidth(32), .bus("separate"), .Select("high")) ram_1 (
    .addr(AluResult[11:2]), .din(MDin), .data(ram_1_data), .str(MemWrite), .clk(CLK), .ld(not_18_out));  // open: sel, clr
  not not_18 (not_18_out, MemWrite);
  \MEM_WB流水寄存器  \mem_wb流水寄存器_1  (
    .J(\ex_mem流水寄存器_1_lbout ), .MemToReg(\ex_mem流水寄存器_1_memtoregout ), .RegWrite(RegWrite_mem),
    .AluResult(AluResult), .WriteData(ram_1_data), .PC_4(PC_next), .Rd(rd_mem), .CLK(CLK),
    .Jout(\mem_wb流水寄存器_1_jout [0]), .MemToRegout(\mem_wb流水寄存器_1_memtoregout [0]), .RegWriteout(RegWrite),
    .AluResultout(\mem_wb流水寄存器_1_aluresultout ), .WriteDataout(\mem_wb流水寄存器_1_writedataout ),
    .PC_4out(\mem_wb流水寄存器_1_pc_4out ), .Rdout(Rd), .\同步清零_气泡_高电平有效 (RST), .\使能端_低电平有效_stall_高电平有效 (halt),
    .IR(MEM_IR), .IRout(WB_IR), .PCout(WB_PC), .PC(M_PC), .ecall(\ex_mem流水寄存器_1_ecallout ), .ecallout(ecall),
    .R1(\ex_mem流水寄存器_1_r1out ), .R1out(R1), .R2(MDin), .R2out(R2), .AUIPC(AUIPC_mem),
    .AUIPCout(\mem_wb流水寄存器_1_jout [1]), .lb(\ex_mem流水寄存器_1_jout ), .lbout(\mem_wb流水寄存器_1_memtoregout [1]),
    .sel(AluResult[1:0]), .selout(\mem_wb流水寄存器_1_selout ), .auipc_2(\ex_mem流水寄存器_1_auipc_out ),
    .auipc_out(\mem_wb流水寄存器_1_auipc_out ));
  assign bit_extender_5_out = {{24{\mem_wb流水寄存器_1_writedataout [7]}}, \mem_wb流水寄存器_1_writedataout [7:0]};  // Bit_Extender bit_extender_5
  assign bit_extender_6_out = {{24{\mem_wb流水寄存器_1_writedataout [15]}}, \mem_wb流水寄存器_1_writedataout [15:8]};  // Bit_Extender bit_extender_6
  assign bit_extender_7_out = {{24{\mem_wb流水寄存器_1_writedataout [23]}}, \mem_wb流水寄存器_1_writedataout [23:16]};  // Bit_Extender bit_extender_7
  assign bit_extender_8_out = {{24{\mem_wb流水寄存器_1_writedataout [31]}}, \mem_wb流水寄存器_1_writedataout [31:24]};  // Bit_Extender bit_extender_8
  Multiplexer #(.select(2), .width(32), .disabled("Z"), .enable("false")) multiplexer_17 (
    .in0(bit_extender_5_out), .in1(bit_extender_6_out), .in2(bit_extender_7_out), .in3(bit_extender_8_out),
    .out(multiplexer_17_out), .sel(\mem_wb流水寄存器_1_selout ));
  Multiplexer #(.select(2), .width(32), .disabled("Z"), .enable("false")) multiplexer_18 (
    .in0(\mem_wb流水寄存器_1_aluresultout ), .in1(\mem_wb流水寄存器_1_writedataout ), .in3(multiplexer_17_out),
    .out(multiplexer_18_out), .sel(\mem_wb流水寄存器_1_memtoregout ));  // open: in2
  Multiplexer #(.select(2), .width(32), .disabled("Z"), .enable("false")) multiplexer_19 (
    .in0(multiplexer_18_out), .in1(\mem_wb流水寄存器_1_pc_4out ), .in2(\mem_wb流水寄存器_1_auipc_out ), .out(RDin),
    .sel(\mem_wb流水寄存器_1_jout ));  // open: in3

  // Other names for the same wires on the sheet: JALR = Instr[0]; JAL = Instr[2]; MEM_PC[31:0] = M_PC;
  //   stall = LoadUse

  // Notes on the sheet:
  //   中断源
  //   时空图监测，可删除
  //   中断等待指示
  //   计数逻辑
  //   数码管输出
  //   单级中断测试信号模拟器
  //   控制位
  //   流水调试日志用
  //   暂停节拍，不能为0
  //   戳工具置1进入计数暂停模式，ctrl+k时钟自动运行到对应节拍暂停
  //   ctrl+k关闭时钟连续运行，将控制位置零，进入单步调试模式调试
  //   中断信号采样逻辑
  //   可计数暂停的时钟源
  //   气泡流水线数据冲突逻辑
  //   重定向流水线数据冲突逻辑
  //   为方便自动评测，需要输出流水线各段保存的PC值，注意是PC不是PC+4，另外ID段寄存器写入信息，Mem段内存写入信息也要输出
  //   rs：mem段数据相关
  //   rs：ex段数据相关
  //   rt：mem段数据相关
  //   rt：ex段数据相关
  //   指令存储器
  //   PC
  //   PC+4
  //   IF/ID
  //   IR
  //   contents of rom_1 (hex, n*v repeats v):
  //   100493 100006f 100493 200913 300993 100006f 100493 200913 300993 100006f 100493 200913 300993
  //   100006f 100493 200913 300993 29c000ef 100413 100493 1f49493 900533 2200893 73 24d493 48463 fedff06f
  //   900533 2200893 73 100493 249493 900533 2200893 73 48463 fedff06f 100493 1f49493 900533 2200893 73
  //   4034d493 900533 2200893 73 4044d493 900533 2200893 73 4044d493 900533 2200893 73 4044d493 900533
  //   2200893 73 4044d493 900533 2200893 73 4044d493 900533 2200893 73 4044d493 900533 2200893 73 4044d493
  //   900533 2200893 73 100413 1f41993 41f9d993 433 c00913 300b13 140413 f47413 800293 100313 499993
  //   89e9b3 1300533 2200893 73 406282b3 fe0294e3 140413 f00f93 1f47433 1c41413 800293 100313 49d993
  //   89e9b3 1300533 2200893 73 406282b3 fe0294e3 1c45413 406b0b33 b0463 f95ff06f 2b3 fff2c293 829293
  //   ff2e293 500533 2200893 73 fff00413 493 84a023 140413 448493 84a023 140413 448493 84a023 140413
  //   448493 84a023 140413 448493 84a023 140413 448493 84a023 140413 448493 84a023 140413 448493 84a023
  //   140413 448493 84a023 140413 448493 84a023 140413 448493 84a023 140413 448493 84a023 140413 448493
  //   84a023 140413 448493 84a023 140413 448493 84a023 140413 448493 84a023 140413 448493 140413 433
  //   3c00493 42983 4aa03 149a2b3 28663 134a023 1442023 ffc48493 fe9412e3 800533 2200893 73 440413 3c00493
  //   fc9416e3 a00893 73 413 140413 800533 2200893 73 240413 800533 2200893 73 340413 800533 2200893 73
  //   440413 800533 2200893 73 540413 800533 2200893 73 640413 800533 2200893 73 740413 800533 2200893 73
  //   840413 800533 2200893 2200893 73 8067
  //   JAL
  //   JALR
  //   URET
  //   AUIPC
  //   lb
  //   rd
  //   IR
  //   I型
  //   S型
  //   Beq
  //   Bne
  //   MemToReg
  //   MemWrite
  //   AluOP
  //   AluSrcB
  //   RegWrite
  //   S_Tyoe
  //   rs1
  //   rs2
  //   B型
  //   J型
  //   ID/EX
  //   AluResult
  //   WriteData
  //   EX/MEM
  //   数据存储器
  //   MEM/WB
  //   lb
  //   AUIPC
  //   MemToReg
  //   PC+4
  //   J
endmodule

module \单周期_单级中断  (
  input  IR1,
  input  IR2,
  input  IR3,
  output RegWrite,
  output MemWrite,
  output [31:0] PC,
  output [31:0] IR,
  output [31:0] RDin,
  output [31:0] MDin,
  output [31:0] LedData
);

  wire and_1_out, and_2_out, and_3_out, and_4_out, and_5_out, and_6_out, and_7_out, and_8_out, and_10_out,
       AUIPC, Beq, Bge, Bne, CLK, Clr1, Clr2, Clr3, comparator_1_eq, comparator_2_eq, comparator_3_eq,
       comparator_4_eq, comparator_5_eq, comparator_5_gt, comparator_6_eq, ecall, equal, Go, halt, Intout,
       IntR, IntRe, IR1_2_q, IR1_3_q, IR1_4_q, IR1_q, IR1_t, IR2_2_q, IR2_q, IR2_t, IR3_t, IRA, IRB, IRC, J,
       lb, not_1_out, not_2_out, not_3_out, not_4_out, or_1_out, or_10_out, or_11_out, or_12_out, PCSrc,
       register_3_q, RST, tunnel, URET, W1, W2, W3, \单周期硬布线控制器_1_alu_src , \单周期硬布线控制器_1_s_type ;
  wire [0:0] \单周期硬布线控制器_1_memtoreg ;
  wire [1:0] priority_encoder_1_out, register_2_q;
  wire [2:0] Instr;
  wire [3:0] \单周期硬布线控制器_1_alu_op ;
  wire [4:0] multiplexer_3_out, multiplexer_4_out;
  wire [11:0] multiplexer_5_out;
  wire [15:0] \总周期数 ;
  wire [31:0] adder_2_out, adder_3_out, adder_4_out, alu_1_result, and_9_out, auipc_res, bit_extender_1_out,
       bit_extender_2_out, bit_extender_3_out, bit_extender_4_out, bit_extender_5_out, bit_extender_6_out,
       bit_extender_7_out, bit_extender_8_out, IntPrc, mEPCout, multiplexer_1_out, multiplexer_7_out,
       multiplexer_8_out, multiplexer_10_out, multiplexer_12_out, PC_4, PC_next, R1, ram_1_data,
       shifter_1_out, shifter_2_out, shifter_3_out;

  Clock #(.highDuration(1), .lowDuration(1)) clock_1 (.out(CLK));
  Button _1 ();  // open: out
  Button _2 ();  // open: out
  Button _3 ();  // open: out
  Button \u_继续运行  (.out(Go));
  LED #(.active("true")) led_1 (.in(W1));
  LED #(.active("true")) led_2 (.in(W2));
  LED #(.active("true")) led_3 (.in(W3));
  Hex_Digit_Display hex_digit_display_1 (.value(LedData[31:28]));  // open: dp
  // RiscV_Probe riscv_probe_1: pin names not known; wires that end beside it: IR
  Hex_Digit_Display hex_digit_display_2 (.value(LedData[27:24]));  // open: dp
  Hex_Digit_Display hex_digit_display_3 (.value(LedData[23:20]));  // open: dp
  Comparator #(.width(16), .mode("twosComplement")) comparator_1 (
    .a(16'h23b), .b(\总周期数 ), .eq(comparator_1_eq));  // open: gt, lt
  or or_1 (or_1_out, comparator_1_eq, comparator_2_eq);
  Comparator #(.width(16), .mode("twosComplement")) comparator_2 (
    .a(\总周期数 ), .b(16'h1), .eq(comparator_2_eq));  // open: gt, lt
  Comparator #(.width(16), .mode("twosComplement")) comparator_3 (
    .a(\总周期数 ), .b(16'h4), .eq(comparator_3_eq));  // open: gt, lt
  Comparator #(.width(16), .mode("twosComplement")) comparator_4 (
    .a(\总周期数 ), .b(16'h7), .eq(comparator_4_eq));  // open: gt, lt
  Multiplexer #(.select(2), .width(32), .disabled("Z"), .enable("false")) multiplexer_1 (
    .in0(PC_4), .in1(multiplexer_8_out), .in2(mEPCout), .in3(mEPCout), .out(multiplexer_1_out),
    .sel({URET, PCSrc}));
  not not_1 (not_1_out, halt);
  not not_2 (not_2_out, equal);
  Hex_Digit_Display hex_digit_display_4 (.value(LedData[19:16]));  // open: dp
  Hex_Digit_Display hex_digit_display_5 (.value(LedData[15:12]));  // open: dp
  Pull_Resistor #(.pull(0)) pull_resistor_1 (.node(IRA));
  assign IRA = or_1_out ? ~CLK : 1'bz;  // Controlled_Inverter controlled_inverter_1
  Pull_Resistor #(.pull(0)) pull_resistor_2 (.node(IRB));
  assign IRB = comparator_3_eq ? ~CLK : 1'bz;  // Controlled_Inverter controlled_inverter_2
  Pull_Resistor #(.pull(0)) pull_resistor_3 (.node(IRC));
  assign IRC = comparator_4_eq ? ~CLK : 1'bz;  // Controlled_Inverter controlled_inverter_3
  Register #(.width(32), .trigger("rising"), .Select("low")) u_PC (
    .D(multiplexer_1_out), .en(not_1_out), .Q(PC_next), .clk(CLK), .clr(RST));
  and and_1 (and_1_out, tunnel, Bge);
  and and_2 (and_2_out, Beq, equal);
  and and_3 (and_3_out, Bne, not_2_out);
  or or_2 (J, Instr[2], Instr[0]);
  or or_3 (Instr[1], Beq, Bge, Bne);
  Hex_Digit_Display hex_digit_display_6 (.value(LedData[7:4]));  // open: dp
  Hex_Digit_Display hex_digit_display_7 (.value(LedData[11:8]));  // open: dp
  // Probe on \总周期数 
  Multiplexer #(.select(1), .width(32), .disabled("Z"), .enable("false")) multiplexer_2 (
    .in0(PC_next), .in1(IntPrc), .out(PC), .sel(IntR));
  Hex_Digit_Display hex_digit_display_8 (.value(LedData[3:0]));  // open: dp
  or or_4 (PCSrc, and_2_out, and_1_out, and_3_out, J);
  Adder #(.width(32)) adder_1 (.a(PC), .b(32'h4), .out(PC_4));  // open: cin, cout
  or or_5 (IR1_t, IR1, IRA);
  or or_6 (W1, IR1_4_q, IR1_q);
  or or_7 (W2, IR2_q, IR1_2_q);
  or or_8 (W3, IR2_2_q, IR1_3_q);
  // RiscV_Probe riscv_probe_2: pin names not known; wires that end beside it: IR
  ROM #(.addrWidth(10), .dataWidth(32), .Select("high")) rom_1 (.addr(PC[11:2]), .data(IR));
  or or_9 (IR2_t, IR2, IRB);
  D_Flip_Flop #(.trigger("rising"), .Pre_Clr_Positions("LEGACY"), .NegatePresetClear("false"), .enable("true"), .NewFFLayout("false")) u_IR1 (
    .clk(IRA), .D(1'b1), .Q(IR1_q), .reset(IR1_4_q));  // open: Qn, preset, en
  D_Flip_Flop #(.trigger("rising"), .Pre_Clr_Positions("LEGACY"), .NegatePresetClear("false"), .enable("true"), .NewFFLayout("false")) IR1_2 (
    .clk(IRB), .D(1'b1), .Q(IR1_2_q), .reset(IR2_q));  // open: Qn, preset, en
  D_Flip_Flop #(.trigger("rising"), .Pre_Clr_Positions("LEGACY"), .NegatePresetClear("false"), .enable("true"), .NewFFLayout("false")) IR1_3 (
    .clk(IRC), .D(1'b1), .Q(IR1_3_q), .reset(IR2_2_q));  // open: Qn, preset, en
  or or_10 (or_10_out, IR1_q, IR1_4_q);
  or or_11 (or_11_out, IR1_2_q, IR2_q);
  or or_12 (or_12_out, IR1_3_q, IR2_2_q);
  \单周期硬布线控制器  \u_单周期硬布线控制器_1  (
    .Funct({IR[30], IR[25], IR[14:12]}), .OP(IR[6:2]), .ALU_OP(\单周期硬布线控制器_1_alu_op ),
    .MemToReg(\单周期硬布线控制器_1_memtoreg [0]), .MemWrite(MemWrite), .ALU_SRC(\单周期硬布线控制器_1_alu_src ),
    .RegWrite(RegWrite), .ecall(ecall), .S_type(\单周期硬布线控制器_1_s_type ), .Jalr(Instr[0]), .Beq(Beq),
    .JAL(Instr[2]), .Bne(Bne), .in_3(IR[21]), .uret(URET), .AUIPC(AUIPC), .lb(lb), .Bge(Bge));
  Multiplexer #(.select(1), .width(5), .disabled("Z"), .enable("false")) multiplexer_3 (
    .in0(IR[19:15]), .in1(5'b10001), .out(multiplexer_3_out), .sel(ecall));
  Multiplexer #(.select(1), .width(5), .disabled("Z"), .enable("false")) multiplexer_4 (
    .in0(IR[24:20]), .in1(5'b01010), .out(multiplexer_4_out), .sel(ecall));
  Comparator #(.width(32), .mode("twosComplement")) comparator_5 (
    .a(R1), .b(MDin), .gt(comparator_5_gt), .eq(comparator_5_eq));  // open: lt
  Comparator #(.width(32), .mode("unsigned")) comparator_6 (.a(R1), .b(32'h22), .eq(comparator_6_eq));  // open: gt, lt
  or or_13 (IR3_t, IR3, IRC);
  and and_4 (and_4_out, or_10_out, ~Clr1);  // AND_Gate
  and and_5 (and_5_out, or_11_out, ~Clr2);  // AND_Gate
  and and_6 (and_6_out, or_12_out, ~Clr3);  // AND_Gate
  Multiplexer #(.select(1), .width(12), .disabled("Z"), .enable("false")) multiplexer_5 (
    .in0(IR[31:20]), .in1({IR[31:25], IR[11:7]}), .out(multiplexer_5_out), .sel(\单周期硬布线控制器_1_s_type ));
  assign bit_extender_1_out = {{20{IR[31]}}, {IR[31], IR[7], IR[30:25], IR[11:8]}};  // Bit_Extender bit_extender_1
  assign bit_extender_2_out = {{12{IR[31]}}, {IR[31], IR[19:12], IR[20], IR[30:21]}};  // Bit_Extender bit_extender_2
  assign bit_extender_3_out = {{12{IR[31]}}, IR[31:12]};  // Bit_Extender bit_extender_3
  or or_14 (tunnel, comparator_5_gt, comparator_5_eq);
  and and_7 (and_7_out, ecall, comparator_6_eq);
  and and_8 (and_8_out, ecall, ~comparator_6_eq);  // AND_Gate
  assign bit_extender_4_out = {{20{multiplexer_5_out[11]}}, multiplexer_5_out};  // Bit_Extender bit_extender_4
  Multiplexer #(.select(1), .width(1), .disabled("Z"), .enable("false")) multiplexer_6 (
    .in0(and_8_out), .in1(1'b0), .out(halt), .sel(Go));
  D_Flip_Flop #(.trigger("rising"), .Pre_Clr_Positions("LEGACY"), .NegatePresetClear("false"), .enable("true"), .NewFFLayout("false")) IR1_4 (
    .clk(CLK), .D(and_4_out), .Q(IR1_4_q));  // open: Qn, preset, en, reset
  D_Flip_Flop #(.trigger("rising"), .Pre_Clr_Positions("LEGACY"), .NegatePresetClear("false"), .enable("true"), .NewFFLayout("false")) u_IR2 (
    .clk(CLK), .D(and_5_out), .Q(IR2_q));  // open: Qn, preset, en, reset
  D_Flip_Flop #(.trigger("rising"), .Pre_Clr_Positions("LEGACY"), .NegatePresetClear("false"), .enable("true"), .NewFFLayout("false")) IR2_2 (
    .clk(CLK), .D(and_6_out), .Q(IR2_2_q));  // open: Qn, preset, en, reset
  Regifile regifile_1 (
    .Din(RDin), .Clk(CLK), .R1(R1), .R2(MDin), .WE(RegWrite), .W_num(IR[11:7]), .R1_num(multiplexer_3_out),
    .R2_num(multiplexer_4_out));
  Adder #(.width(32)) adder_2 (.a(bit_extender_4_out), .b(R1), .out(adder_2_out));  // open: cin, cout
  Shifter #(.width(32), .shift("ll")) shifter_1 (.in(bit_extender_1_out), .\dist (5'b00001), .out(shifter_1_out));
  Shifter #(.width(32), .shift("ll")) shifter_2 (.in(bit_extender_2_out), .\dist (5'b00001), .out(shifter_2_out));
  Shifter #(.width(32), .shift("ll")) shifter_3 (.in(bit_extender_3_out), .\dist (5'b01100), .out(shifter_3_out));
  Multiplexer #(.select(1), .width(32), .disabled("Z"), .enable("false")) multiplexer_7 (
    .in0(MDin), .in1(bit_extender_4_out), .out(multiplexer_7_out), .sel(\单周期硬布线控制器_1_alu_src ));
  Adder #(.width(32)) adder_3 (.a(shifter_1_out), .b(PC), .out(adder_3_out));  // open: cin, cout
  Adder #(.width(32)) adder_4 (.a(shifter_2_out), .b(PC), .out(adder_4_out));  // open: cin, cout
  Adder #(.width(32)) adder_5 (.a(shifter_3_out), .b(PC), .out(auipc_res));  // open: cin, cout
  assign and_9_out = adder_2_out & 32'hfffffffe;  // AND_Gate and_9, 32 bits wide
  not not_3 (not_3_out, halt);
  and and_10 (and_10_out, Intout, IntRe);
  ALU alu_1 (
    .X(R1), .Y(multiplexer_7_out), .AluOP(\单周期硬布线控制器_1_alu_op ), .Equal(equal), .Result(alu_1_result));  // open: Result_2, out_4, out_6
  Register #(.width(32), .trigger("rising"), .Select("low")) register_1 (
    .D(MDin), .en(and_7_out), .Q(LedData), .clk(CLK));  // open: clr
  Counter #(.width(16), .max('hffff), .ongoal("stay"), .trigger("rising"), .behavior("old")) counter_1 (
    .count(not_3_out), .Q(\总周期数 ), .clk(CLK));  // open: load, D, carry, clr, preset
  Priority_Encoder #(.select(2), .disabled("Z")) priority_encoder_1 (
    .in0(IR1_4_q), .in1(IR2_q), .in2(IR2_2_q), .out(priority_encoder_1_out), .gs(Intout), .en_in(1'b1));  // open: in3, en_out
  Register #(.width(1), .trigger("rising"), .Select("low")) \u_中断使能寄存器IE  (
    .D(and_10_out), .Q(IntR), .clk(CLK));  // open: en, clr
  Multiplexer #(.select(3), .width(32), .disabled("Z"), .enable("false")) multiplexer_8 (
    .in1(and_9_out), .in2(adder_3_out), .in4(adder_4_out), .out(multiplexer_8_out), .sel(Instr));  // open: in0, in3, in5, in6, in7
  Multiplexer #(.select(2), .width(32), .disabled("Z"), .enable("false")) multiplexer_9 (
    .in0(32'h30ac), .in1(32'h3150), .in2(32'h31f4), .out(IntPrc), .sel(priority_encoder_1_out));  // open: in3
  not not_4 (not_4_out, MemWrite);
  Register #(.width(2), .trigger("falling"), .Select("low")) register_2 (
    .D(priority_encoder_1_out), .en(IntR), .Q(register_2_q), .clk(CLK));  // open: clr
  RAM #(.addrWidth(10), .dataWidth(32), .bus("separate"), .Select("high")) ram_1 (
    .addr(alu_1_result[11:2]), .din(MDin), .data(ram_1_data), .str(MemWrite), .clk(CLK), .ld(not_4_out));  // open: sel, clr
  Register #(.width(32), .trigger("rising"), .Select("low")) mEPC (
    .D(PC_next), .en(IntR), .Q(mEPCout), .clk(CLK));  // open: clr
  Decoder #(.select(2), .tristate("false"), .disabled(0), .enable("true")) decoder_1 (
    .out0(Clr1), .out1(Clr2), .out2(Clr3), .sel(register_2_q), .en(URET));  // open: out3
  assign bit_extender_5_out = {{24{ram_1_data[7]}}, ram_1_data[7:0]};  // Bit_Extender bit_extender_5
  assign bit_extender_6_out = {{24{ram_1_data[15]}}, ram_1_data[15:8]};  // Bit_Extender bit_extender_6
  assign bit_extender_7_out = {{24{ram_1_data[23]}}, ram_1_data[23:16]};  // Bit_Extender bit_extender_7
  assign bit_extender_8_out = {{24{ram_1_data[31]}}, ram_1_data[31:24]};  // Bit_Extender bit_extender_8
  Multiplexer #(.select(2), .width(32), .disabled("Z"), .enable("false")) multiplexer_10 (
    .in0(bit_extender_5_out), .in1(bit_extender_6_out), .in2(bit_extender_7_out), .in3(bit_extender_8_out),
    .out(multiplexer_10_out), .sel(alu_1_result[1:0]));
  Register #(.width(1), .trigger("rising"), .Select("low")) register_3 (
    .D(1'b0), .en(URET), .Q(register_3_q), .clk(CLK), .preset(IntR));  // open: clr, cs
  Multiplexer #(.select(2), .width(32), .disabled("Z"), .enable("false")) multiplexer_11 (
    .in0(multiplexer_12_out), .in1(PC_4), .in2(auipc_res), .out(RDin), .sel({AUIPC, J}));  // open: in3
  not not_5 (IntRe, register_3_q);
  Multiplexer #(.select(2), .width(32), .disabled("Z"), .enable("false")) multiplexer_12 (
    .in0(alu_1_result), .in1(ram_1_data), .in3(multiplexer_10_out), .out(multiplexer_12_out),
    .sel({lb, \单周期硬布线控制器_1_memtoreg [0]}));  // open: in2

  // Other names for the same wires on the sheet: JALR = Instr[0]; JAL = Instr[2]

  // Notes on the sheet:
  //   中断源
  //   中断等待指示
  //   总复位信号应将除ROM以外所有存储组件全部清零
  //   单级中断测试信号模拟器
  //   指令探针
  //   指令存储器
  //   数码管输出
  //   数码管输出应该用寄存器锁存，否则显示数据只能一闪而过
  //   指令探针
  //   指令存储器
  //   contents of rom_1 (hex, n*v repeats v):
  //   7d000113 100413 1f41993 41f9d993 433 c00913 800b13 140413 f47413 800293 100313 499993 89e9b3 1300533
  //   2200893 73 406282b3 fe0294e3 140413 f00f93 1f47433 1c41413 800293 100313 49d993 89e9b3 1300533
  //   2200893 73 406282b3 fe0294e3 1c45413 406b0b33 b0463 f95ff06f 2b3 fff2c293 1029293 fff2e293 500533
  //   2200893 73 f5dff06f 1112023 410113 a12023 410113 812023 410113 1312023 410113 1412023 410113 1512023
  //   410113 1612023 410113 100b13 300a13 100a93 1600433 441413 14469b3 1300533 2200893 73 fe0416e3
  //   415a0a33 fe0a10e3 ffc10113 12b03 ffc10113 12a83 ffc10113 12a03 ffc10113 12983 ffc10113 12403
  //   ffc10113 12503 ffc10113 12883 200073 1112023 410113 a12023 410113 812023 410113 1312023 410113
  //   1412023 410113 1512023 410113 1612023 410113 200b13 300a13 100a93 1600433 441413 14469b3 1300533
  //   2200893 73 fe0416e3 415a0a33 fe0a10e3 ffc10113 12b03 ffc10113 12a83 ffc10113 12a03 ffc10113 12983
  //   ffc10113 12403 ffc10113 12503 ffc10113 12883 200073 1112023 410113 a12023 410113 812023 410113
  //   1312023 410113 1412023 410113 1512023 410113 1612023 410113 300b13 300a13 100a93 1600433 441413
  //   14469b3 1300533 2200893 73 fe0416e3 415a0a33 fe0a10e3 ffc10113 12b03 ffc10113 12a83 ffc10113 12a03
  //   ffc10113 12983 ffc10113 12403 ffc10113 12503 ffc10113 12883 200073
  //   PC+4
  //   指令字
  //   JAL
  //   JALR
  //   URET
  //   I型
  //   S型
  //   B型
  //   J型
  //   Beq
  //   Bne
  //   MemToReg
  //   MemWrite
  //   AluOP
  //   AluSrcB
  //   RegWrite
  //   S_Tyoe
  //   rs1
  //   rs2
  //   rd
  //   为方便自动评测，需要输出PC，IR，寄存器堆写如数据RDin
  //   RAM写使能MemWrite、RAM写入数据MDin等信号
  //   数据存储器
endmodule

module \单周期_多级中断  (
  output RegWrite,
  output MemWrite,
  output [31:0] PC,
  output [31:0] IR,
  output [31:0] RDin,
  output [31:0] MDin,
  output [31:0] LedData
);

  wire and_1_out, and_2_out, and_3_out, and_4_out, and_5_out, and_6_out, and_7_out, and_8_out, and_9_out,
       and_10_out, and_11_out, and_12_out, and_13_out, and_14_out, and_15_out, and_16_out, and_17_out,
       and_19_out, AUIPC, Beq, Bge, Bne, CLK, clock_2_out, Clr1, Clr1out, Clr2, Clr2out, Clr3, Clr3out,
       comparator_1_eq, comparator_2_eq, comparator_3_eq, comparator_4_eq, comparator_5_eq, comparator_6_eq,
       comparator_7_eq, comparator_7_gt, comparator_8_eq, comparator_8_lt, comparator_9_gt, comparator_10_eq,
       comparator_11_eq, comparator_12_eq, CSRRCI, CSRRCIen1, CSRRCIen2, CSRRSI, CSRRSIen3, d_ff_4_q, ecall,
       equal, Go, halt, Intout1, Intout2, Intout3, IntR, IntR1, IntR2, IntR3, IntRe1, IntRe2, IntRe3,
       IntStatus, IntStatus1, IntStatus2, IntStatus3, IntSuper, IR1, IR1_2_q, IR1_3_q, IR1_4_q, IR1_q, IR2,
       IR2_2_q, IR2_q, IR3, IRA, IRa_t, IRB, IRb_t, IRC, IRc_t, J, lb, nand_1_out, not_1_out, not_2_out,
       not_3_out, not_7_out, not_8_out, not_12_out, or_1_out, or_2_out, or_11_out, or_12_out, or_13_out,
       PCSrc, register_1_q, register_2_q, register_3_q, RST, tunnel, URET, W1, W2, W3, \关中断1 , \关中断2 ,
       \关中断3 , \单周期硬布线控制器_1_alu_src , \单周期硬布线控制器_1_s_type , \开中断 , \开中断1 , \开中断2 , \开中断3 ;
  wire [0:0] \单周期硬布线控制器_1_memtoreg ;
  wire [1:0] IntCur, IntSel, multiplexer_14_out;
  wire [2:0] Instr;
  wire [3:0] \单周期硬布线控制器_1_alu_op ;
  wire [4:0] multiplexer_4_out, multiplexer_5_out;
  wire [11:0] multiplexer_6_out;
  wire [12:0] CNT_num;
  wire [15:0] \总周期数 ;
  wire [31:0] adder_2_out, adder_3_out, adder_4_out, alu_1_result, and_18_out, auipc_res, bit_extender_1_out,
       bit_extender_2_out, bit_extender_3_out, bit_extender_4_out, bit_extender_5_out, bit_extender_6_out,
       bit_extender_7_out, bit_extender_8_out, IntPrc, mEPCout, mEPCout1, mEPCout2, mEPCout3,
       multiplexer_2_out, multiplexer_8_out, multiplexer_10_out, multiplexer_11_out, multiplexer_12_out,
       PC_4, PC_next, R1, ram_1_data, shifter_1_out, shifter_2_out, shifter_3_out;

  Clock #(.highDuration(1), .lowDuration(1)) clock_1 ();  // open: out
  Button _1 (.out(IRa_t));
  Button _2 (.out(IRb_t));
  Button _3 (.out(IRc_t));
  Button \u_继续运行  (.out(Go));
  LED #(.active("true")) led_1 (.in(W1));
  LED #(.active("true")) led_2 (.in(W2));
  LED #(.active("true")) led_3 (.in(W3));
  Hex_Digit_Display hex_digit_display_1 (.value(LedData[31:28]));  // open: dp
  Comparator #(.width(16), .mode("twosComplement")) comparator_1 (
    .a(\总周期数 ), .b(16'h7), .eq(comparator_1_eq));  // open: gt, lt
  Comparator #(.width(16), .mode("twosComplement")) comparator_2 (
    .a(\总周期数 ), .b(16'h241), .eq(comparator_2_eq));  // open: gt, lt
  D_Flip_Flop #(.trigger("rising"), .Pre_Clr_Positions("LEGACY"), .NegatePresetClear("false"), .enable("true"), .NewFFLayout("false")) d_ff_1 (
    .clk(CLK), .D(1'b1), .Q(\开中断1 ), .Qn(\关中断1 ), .en(and_1_out), .reset(and_4_out));  // open: preset
  and and_1 (and_1_out, IntStatus1, CSRRSI);
  D_Flip_Flop #(.trigger("rising"), .Pre_Clr_Positions("LEGACY"), .NegatePresetClear("false"), .enable("true"), .NewFFLayout("false")) d_ff_2 (
    .clk(CLK), .D(1'b1), .Q(\开中断2 ), .Qn(\关中断2 ), .en(and_2_out), .reset(and_5_out));  // open: preset
  and and_2 (and_2_out, IntStatus2, CSRRSI);
  D_Flip_Flop #(.trigger("rising"), .Pre_Clr_Positions("LEGACY"), .NegatePresetClear("false"), .enable("true"), .NewFFLayout("false")) d_ff_3 (
    .clk(CLK), .D(1'b1), .Q(\开中断3 ), .Qn(\关中断3 ), .en(and_3_out), .reset(and_6_out));  // open: preset
  and and_3 (and_3_out, IntStatus3, CSRRSI);
  Hex_Digit_Display hex_digit_display_2 (.value(LedData[27:24]));  // open: dp
  Hex_Digit_Display hex_digit_display_3 (.value(LedData[23:20]));  // open: dp
  Comparator #(.width(16), .mode("twosComplement")) comparator_3 (
    .a(16'h258), .b(\总周期数 ), .eq(comparator_3_eq));  // open: gt, lt
  or or_1 (or_1_out, comparator_3_eq, comparator_4_eq);
  Comparator #(.width(16), .mode("twosComplement")) comparator_4 (
    .a(\总周期数 ), .b(16'h1), .eq(comparator_4_eq));  // open: gt, lt
  Comparator #(.width(16), .mode("twosComplement")) comparator_5 (
    .a(\总周期数 ), .b(16'h4), .eq(comparator_5_eq));  // open: gt, lt
  or or_2 (or_2_out, comparator_1_eq, comparator_2_eq);
  and and_4 (and_4_out, CSRRCI, CSRRCIen1);
  and and_5 (and_5_out, CSRRCI, CSRRCIen2);
  and and_6 (and_6_out, CSRRCI, CSRRSIen3);
  Multiplexer #(.select(2), .width(1), .disabled("Z"), .enable("false")) multiplexer_1 (
    .in0(\开中断1 ), .in1(\开中断2 ), .in2(\开中断3 ), .out(\开中断 ), .sel(IntCur));  // open: in3
  Hex_Digit_Display hex_digit_display_4 (.value(LedData[15:12]));  // open: dp
  Hex_Digit_Display hex_digit_display_5 (.value(LedData[19:16]));  // open: dp
  Pull_Resistor #(.pull(0)) pull_resistor_1 (.node(IRA));
  assign IRA = or_1_out ? ~CLK : 1'bz;  // Controlled_Inverter controlled_inverter_1
  Pull_Resistor #(.pull(0)) pull_resistor_2 (.node(IRB));
  assign IRB = comparator_5_eq ? ~CLK : 1'bz;  // Controlled_Inverter controlled_inverter_2
  Pull_Resistor #(.pull(0)) pull_resistor_3 (.node(IRC));
  assign IRC = or_2_out ? ~CLK : 1'bz;  // Controlled_Inverter controlled_inverter_3
  Hex_Digit_Display hex_digit_display_6 (.value(LedData[7:4]));  // open: dp
  Hex_Digit_Display hex_digit_display_7 (.value(LedData[11:8]));  // open: dp
  // Probe on \总周期数 
  Hex_Digit_Display hex_digit_display_8 (.value(LedData[3:0]));  // open: dp
  Multiplexer #(.select(2), .width(32), .disabled("Z"), .enable("false")) multiplexer_2 (
    .in0(PC_4), .in1(multiplexer_10_out), .in2(mEPCout), .in3(mEPCout), .out(multiplexer_2_out),
    .sel({URET, PCSrc}));
  not not_1 (not_1_out, halt);
  and and_7 (and_7_out, tunnel, Bge);
  and and_8 (and_8_out, Beq, equal);
  and and_9 (and_9_out, Bne, not_2_out);
  not not_2 (not_2_out, equal);
  or or_3 (W1, IR1_4_q, IR1_q);
  or or_4 (W2, IR2_q, IR1_2_q);
  or or_5 (W3, IR2_2_q, IR1_3_q);
  Register #(.width(32), .trigger("rising"), .Select("low")) u_PC (
    .D(multiplexer_2_out), .en(not_1_out), .Q(PC_next), .clk(CLK), .clr(RST));
  or or_6 (J, Instr[2], Instr[0]);
  or or_7 (Instr[1], Beq, Bge, Bne);
  or or_8 (IR1, IRa_t, IRA);
  D_Flip_Flop #(.trigger("rising"), .Pre_Clr_Positions("LEGACY"), .NegatePresetClear("false"), .enable("true"), .NewFFLayout("false")) u_IR1 (
    .clk(IR1), .D(1'b1), .Q(IR1_q), .reset(IR1_4_q));  // open: Qn, preset, en
  D_Flip_Flop #(.trigger("rising"), .Pre_Clr_Positions("LEGACY"), .NegatePresetClear("false"), .enable("true"), .NewFFLayout("false")) IR1_2 (
    .clk(IR2), .D(1'b1), .Q(IR1_2_q), .reset(IR2_q));  // open: Qn, preset, en
  D_Flip_Flop #(.trigger("rising"), .Pre_Clr_Positions("LEGACY"), .NegatePresetClear("false"), .enable("true"), .NewFFLayout("false")) IR1_3 (
    .clk(IR3), .D(1'b1), .Q(IR1_3_q), .reset(IR2_2_q));  // open: Qn, preset, en
  Multiplexer #(.select(1), .width(32), .disabled("Z"), .enable("false")) multiplexer_3 (
    .in0(PC_next), .in1(IntPrc), .out(PC), .sel(IntR));
  or or_9 (PCSrc, and_8_out, and_7_out, and_9_out, J);
  or or_10 (IR2, IRb_t, IRB);
  or or_11 (or_11_out, IR1_q, IR1_4_q);
  or or_12 (or_12_out, IR1_2_q, IR2_q);
  or or_13 (or_13_out, IR1_3_q, IR2_2_q);
  Adder #(.width(32)) adder_1 (.a(PC), .b(32'h4), .out(PC_4));  // open: cin, cout
  and and_10 (and_10_out, or_11_out, ~Clr1);  // AND_Gate
  and and_11 (and_11_out, or_12_out, ~Clr2);  // AND_Gate
  and and_12 (and_12_out, or_13_out, ~Clr3);  // AND_Gate
  and and_13 (and_13_out, Intout1, IntSuper, IntRe1);
  // RiscV_Probe riscv_probe_1: pin names not known; wires that end beside it: IR
  or or_14 (IR3, IRc_t, IRC);
  Register #(.width(1), .trigger("rising"), .Select("low")) \u_中断使能寄存器IE  (
    .D(and_13_out), .Q(IntR1), .clk(CLK));  // open: en, clr
  and and_14 (and_14_out, Intout2, IntSuper, IntRe2);
  Register #(.width(1), .trigger("rising"), .Select("low")) \u_中断使能寄存器IE_2  (
    .D(and_14_out), .Q(IntR2), .clk(CLK));  // open: en, clr
  Register #(.width(1), .trigger("rising"), .Select("low")) \u_中断使能寄存器IE_3  (
    .D(and_15_out), .Q(IntR3), .clk(CLK));  // open: en, clr
  and and_15 (and_15_out, Intout3, IntSuper, IntRe3);
  ROM #(.addrWidth(10), .dataWidth(32), .Select("high")) rom_1 (.addr(PC[11:2]), .data(IR));
  Comparator #(.width(32), .mode("unsigned")) comparator_6 (.a(R1), .b(32'h22), .eq(comparator_6_eq));  // open: gt, lt
  D_Flip_Flop #(.trigger("rising"), .Pre_Clr_Positions("LEGACY"), .NegatePresetClear("false"), .enable("true"), .NewFFLayout("false")) IR1_4 (
    .clk(CLK), .D(and_10_out), .Q(IR1_4_q));  // open: Qn, preset, en, reset
  D_Flip_Flop #(.trigger("rising"), .Pre_Clr_Positions("LEGACY"), .NegatePresetClear("false"), .enable("true"), .NewFFLayout("false")) u_IR2 (
    .clk(CLK), .D(and_11_out), .Q(IR2_q));  // open: Qn, preset, en, reset
  D_Flip_Flop #(.trigger("rising"), .Pre_Clr_Positions("LEGACY"), .NegatePresetClear("false"), .enable("true"), .NewFFLayout("false")) IR2_2 (
    .clk(CLK), .D(and_12_out), .Q(IR2_2_q));  // open: Qn, preset, en, reset
  \cpu24_int_riscv__单周期硬布线控制器  \u_单周期硬布线控制器_1  (
    .Funct({IR[30], IR[25], IR[14:12]}), .OP(IR[6:2]), .ALU_OP(\单周期硬布线控制器_1_alu_op ),
    .MemToReg(\单周期硬布线控制器_1_memtoreg [0]), .ecall(ecall), .in_3(IR[21]), .uret(URET), .CSRRSI(CSRRSI),
    .CSRRCI(CSRRCI), .MemWrite(MemWrite), .RegWrite(RegWrite), .lb(lb), .S_type(\单周期硬布线控制器_1_s_type ),
    .Beq(Beq), .Bge(Bge), .ALU_SRC(\单周期硬布线控制器_1_alu_src ), .AUIPC(AUIPC), .Jalr(Instr[0]), .JAL(Instr[2]),
    .Bne(Bne));
  Multiplexer #(.select(1), .width(5), .disabled("Z"), .enable("false")) multiplexer_4 (
    .in0(IR[19:15]), .in1(5'b10001), .out(multiplexer_4_out), .sel(ecall));
  Multiplexer #(.select(1), .width(5), .disabled("Z"), .enable("false")) multiplexer_5 (
    .in0(IR[24:20]), .in1(5'b01010), .out(multiplexer_5_out), .sel(ecall));
  Comparator #(.width(32), .mode("twosComplement")) comparator_7 (
    .a(R1), .b(MDin), .gt(comparator_7_gt), .eq(comparator_7_eq));  // open: lt
  Multiplexer #(.select(1), .width(12), .disabled("Z"), .enable("false")) multiplexer_6 (
    .in0(IR[31:20]), .in1({IR[31:25], IR[11:7]}), .out(multiplexer_6_out), .sel(\单周期硬布线控制器_1_s_type ));
  assign bit_extender_1_out = {{20{multiplexer_6_out[11]}}, multiplexer_6_out};  // Bit_Extender bit_extender_1
  assign bit_extender_2_out = {{20{IR[31]}}, {IR[31], IR[7], IR[30:25], IR[11:8]}};  // Bit_Extender bit_extender_2
  assign bit_extender_3_out = {{12{IR[31]}}, {IR[31], IR[19:12], IR[20], IR[30:21]}};  // Bit_Extender bit_extender_3
  assign bit_extender_4_out = {{12{IR[31]}}, IR[31:12]};  // Bit_Extender bit_extender_4
  or or_15 (tunnel, comparator_7_gt, comparator_7_eq);
  and and_16 (and_16_out, ecall, comparator_6_eq);
  and and_17 (and_17_out, ecall, ~comparator_6_eq);  // AND_Gate
  Register #(.width(32), .trigger("rising"), .Select("low")) mEPC (
    .D(PC_next), .en(IntR1), .Q(mEPCout1), .clk(CLK), .clr(Clr1out));
  Register #(.width(32), .trigger("rising"), .Select("low")) mEPC_2 (
    .D(PC_next), .en(IntR2), .Q(mEPCout2), .clk(CLK), .clr(Clr2out));
  Register #(.width(32), .trigger("rising"), .Select("low")) mEPC_3 (
    .D(PC_next), .en(IntR3), .Q(mEPCout3), .clk(CLK), .clr(Clr3out));
  cpu24_int_riscv__Regifile regifile_1 (
    .Din(RDin), .Clk(CLK), .R1(R1), .R2(MDin), .WE(RegWrite), .W_num(IR[11:7]), .R1_num(multiplexer_4_out),
    .R2_num(multiplexer_5_out));
  Shifter #(.width(32), .shift("ll")) shifter_1 (.in(bit_extender_2_out), .\dist (5'b00001), .out(shifter_1_out));
  Shifter #(.width(32), .shift("ll")) shifter_2 (.in(bit_extender_3_out), .\dist (5'b00001), .out(shifter_2_out));
  Shifter #(.width(32), .shift("ll")) shifter_3 (.in(bit_extender_4_out), .\dist (5'b01100), .out(shifter_3_out));
  Multiplexer #(.select(1), .width(1), .disabled("Z"), .enable("false")) multiplexer_7 (
    .in0(and_17_out), .in1(1'b0), .out(halt), .sel(Go));
  Priority_Encoder #(.select(2), .disabled("Z")) priority_encoder_1 (
    .in0(IR1_4_q), .in1(IR2_q), .in2(IR2_2_q), .out(IntSel), .en_in(1'b1));  // open: in3, gs, en_out
  or or_16 (IntR, IntR1, IntR2, IntR3);
  Adder #(.width(32)) adder_2 (.a(bit_extender_1_out), .b(R1), .out(adder_2_out));  // open: cin, cout
  Adder #(.width(32)) adder_3 (.a(shifter_1_out), .b(PC), .out(adder_3_out));  // open: cin, cout
  Adder #(.width(32)) adder_4 (.a(shifter_2_out), .b(PC), .out(adder_4_out));  // open: cin, cout
  Adder #(.width(32)) adder_5 (.a(shifter_3_out), .b(PC), .out(auipc_res));  // open: cin, cout
  Multiplexer #(.select(1), .width(32), .disabled("Z"), .enable("false")) multiplexer_8 (
    .in0(MDin), .in1(bit_extender_1_out), .out(multiplexer_8_out), .sel(\单周期硬布线控制器_1_alu_src ));
  assign and_18_out = adder_2_out & 32'hfffffffe;  // AND_Gate and_18, 32 bits wide
  D_Flip_Flop #(.trigger("high"), .Pre_Clr_Positions("LEGACY"), .NegatePresetClear("false"), .enable("true"), .NewFFLayout("false")) d_ff_4 (.Q(d_ff_4_q));  // open: clk, D, Qn, preset, en, reset
  // Probe on 13'h230
  Decoder #(.select(2), .tristate("false"), .disabled(0), .enable("false")) decoder_1 (
    .out0(Intout1), .out1(Intout2), .out2(Intout3), .sel(IntSel));  // open: out3
  Multiplexer #(.select(2), .width(32), .disabled("Z"), .enable("false")) multiplexer_9 (
    .in0(32'h30ac), .in1(32'h3158), .in2(32'h3204), .out(IntPrc), .sel(IntSel));  // open: in3
  Register #(.width(1), .trigger("rising"), .Select("low")) register_1 (
    .D(1'b0), .en(URET), .Q(register_1_q), .clk(CLK), .preset(IntR1));  // open: clr, cs
  Register #(.width(1), .trigger("rising"), .Select("low")) register_2 (
    .D(1'b0), .en(URET), .Q(register_2_q), .clk(CLK), .preset(IntR2));  // open: clr, cs
  Register #(.width(1), .trigger("rising"), .Select("low")) register_3 (
    .D(1'b0), .en(URET), .Q(register_3_q), .clk(CLK), .preset(IntR3));  // open: clr, cs
  cpu24_int_riscv__ALU alu_1 (
    .X(R1), .Y(multiplexer_8_out), .AluOP(\单周期硬布线控制器_1_alu_op ), .Equal(equal), .Result(alu_1_result));  // open: Result_2, out_4, out_6
  Register #(.width(32), .trigger("rising"), .Select("low")) register_4 (
    .D(MDin), .en(and_16_out), .Q(LedData), .clk(CLK));  // open: clr
  Counter #(.width(16), .max('hffff), .ongoal("stay"), .trigger("rising"), .behavior("old")) counter_1 (
    .count(not_3_out), .Q(\总周期数 ), .clk(CLK));  // open: load, D, carry, clr, preset
  not not_3 (not_3_out, halt);
  Comparator #(.width(13), .mode("twosComplement")) comparator_8 (
    .a(CNT_num), .b(13'h230), .eq(comparator_8_eq), .lt(comparator_8_lt));  // open: gt
  Clock #(.highDuration(1), .lowDuration(1)) clock_2 (.out(clock_2_out));
  not not_4 (IntRe1, register_1_q);
  not not_5 (IntRe2, register_2_q);
  not not_6 (IntRe3, register_3_q);
  Counter #(.width(13), .max('h1fff), .ongoal("stay"), .trigger("rising"), .behavior("old")) counter_2 (
    .count(comparator_8_lt), .Q(CNT_num), .clk(clock_2_out));  // open: load, D, carry, clr, preset
  Multiplexer #(.select(3), .width(32), .disabled("Z"), .enable("false")) multiplexer_10 (
    .in1(and_18_out), .in2(adder_3_out), .in4(adder_4_out), .out(multiplexer_10_out), .sel(Instr));  // open: in0, in3, in5, in6, in7
  nand nand_1 (nand_1_out, d_ff_4_q, comparator_8_eq);
  not not_7 (not_7_out, MemWrite);
  assign CLK = nand_1_out ? clock_2_out : 1'bz;  // Controlled_Buffer controlled_buffer_1
  Pull_Resistor #(.pull(1)) pull_resistor_4 (.node(CLK));
  RAM #(.addrWidth(10), .dataWidth(32), .bus("separate"), .Select("high")) ram_1 (
    .addr(alu_1_result[11:2]), .din(MDin), .data(ram_1_data), .str(MemWrite), .clk(CLK), .ld(not_7_out));  // open: sel, clr
  Comparator #(.width(2), .mode("unsigned")) comparator_9 (
    .a(IntSel), .b(IntCur), .gt(comparator_9_gt));  // open: eq, lt
  Priority_Encoder #(.select(2), .disabled("Z")) priority_encoder_2 (
    .in0(IntStatus1), .in1(IntStatus2), .in2(IntStatus3), .out(IntCur), .en_in(1'b1));  // open: in3, gs, en_out
  not not_8 (not_8_out, IntStatus);
  and and_19 (and_19_out, IntStatus, comparator_9_gt, \开中断 );
  assign bit_extender_5_out = {{24{ram_1_data[7]}}, ram_1_data[7:0]};  // Bit_Extender bit_extender_5
  assign bit_extender_6_out = {{24{ram_1_data[15]}}, ram_1_data[15:8]};  // Bit_Extender bit_extender_6
  assign bit_extender_7_out = {{24{ram_1_data[23]}}, ram_1_data[23:16]};  // Bit_Extender bit_extender_7
  assign bit_extender_8_out = {{24{ram_1_data[31]}}, ram_1_data[31:24]};  // Bit_Extender bit_extender_8
  not not_9 (IntStatus1, comparator_10_eq);
  Comparator #(.width(32), .mode("unsigned")) comparator_10 (
    .a(mEPCout1), .b({32{1'b0}}), .eq(comparator_10_eq));  // open: gt, lt
  not not_10 (IntStatus2, comparator_11_eq);
  Comparator #(.width(32), .mode("unsigned")) comparator_11 (
    .a(mEPCout2), .b({32{1'b0}}), .eq(comparator_11_eq));  // open: gt, lt
  Comparator #(.width(32), .mode("unsigned")) comparator_12 (
    .a(mEPCout3), .b({32{1'b0}}), .eq(comparator_12_eq));  // open: gt, lt
  not not_11 (IntStatus3, comparator_12_eq);
  or or_17 (IntSuper, not_8_out, and_19_out);
  Multiplexer #(.select(2), .width(32), .disabled("Z"), .enable("false")) multiplexer_11 (
    .in0(bit_extender_5_out), .in1(bit_extender_6_out), .in2(bit_extender_7_out), .in3(bit_extender_8_out),
    .out(multiplexer_11_out), .sel(alu_1_result[1:0]));
  Decoder #(.select(2), .tristate("false"), .disabled(0), .enable("false")) decoder_2 (
    .out0(CSRRCIen1), .out1(CSRRCIen2), .out2(CSRRSIen3), .sel(IntCur));  // open: out3
  Decoder #(.select(2), .tristate("false"), .disabled(0), .enable("true")) decoder_3 (
    .out0(Clr1), .out1(Clr2), .out2(Clr3), .sel(IntCur), .en(URET));  // open: out3
  Multiplexer #(.select(2), .width(32), .disabled("Z"), .enable("false")) multiplexer_12 (
    .in0(alu_1_result), .in1(ram_1_data), .in3(multiplexer_11_out), .out(multiplexer_12_out),
    .sel({lb, \单周期硬布线控制器_1_memtoreg [0]}));  // open: in2
  Multiplexer #(.select(2), .width(32), .disabled("Z"), .enable("false")) multiplexer_13 (
    .in0(multiplexer_12_out), .in1(PC_4), .in2(auipc_res), .out(RDin), .sel({AUIPC, J}));  // open: in3
  not not_12 (not_12_out, IntStatus);
  or or_18 (IntStatus, IntStatus1, IntStatus2, IntStatus3);
  Multiplexer #(.select(1), .width(2), .disabled("Z"), .enable("false")) multiplexer_14 (
    .in0(IntCur), .in1(2'b00), .out(multiplexer_14_out), .sel(not_12_out));
  Multiplexer #(.select(2), .width(32), .disabled("Z"), .enable("false")) multiplexer_15 (
    .in0(mEPCout1), .in1(mEPCout2), .in2(mEPCout3), .out(mEPCout), .sel(multiplexer_14_out));  // open: in3
  Register #(.width(1), .trigger("rising"), .Select("low")) register_5 (
    .D(Clr1), .Q(Clr1out), .clk(CLK));  // open: en, clr
  Register #(.width(1), .trigger("rising"), .Select("low")) register_6 (
    .D(Clr2), .Q(Clr2out), .clk(CLK));  // open: en, clr
  Register #(.width(1), .trigger("rising"), .Select("low")) register_7 (
    .D(Clr3), .Q(Clr3out), .clk(CLK));  // open: en, clr

  // Other names for the same wires on the sheet: JALR = Instr[0]; JAL = Instr[2]

  // Notes on the sheet:
  //   中断源
  //   中断等待指示
  //   总复位信号应将除ROM以外所有存储组件全部清零
  //   多级中断测试信号模拟器
  //   数码管输出
  //   中断请求生成
  //   开关中断逻辑
  //   数码管输出应该用寄存器锁存，否则显示数据只能一闪而过
  //   中断使能逻辑
  //   中断按键采样逻辑
  //   指令探针
  //   指令存储器
  //   PC+4
  //   指令字
  //   contents of rom_1 (hex, n*v repeats v):
  //   7d000113 100413 1f41993 41f9d993 433 c00913 800b13 140413 f47413 800293 100313 499993 89e9b3 1300533
  //   2200893 73 406282b3 fe0294e3 140413 f00f93 1f47433 1c41413 800293 100313 49d993 89e9b3 1300533
  //   2200893 73 406282b3 fe0294e3 1c45413 406b0b33 b0463 f95ff06f 2b3 fff2c293 1029293 fff2e293 500533
  //   2200893 73 f5dff06f 1112023 410113 a12023 410113 812023 410113 1312023 410113 1412023 410113 1512023
  //   410113 1612023 410113 40e073 100b13 300a13 100a93 1600433 441413 14469b3 1300533 2200893 73 fe0416e3
  //   415a0a33 fe0a10e3 40f073 ffc10113 12b03 ffc10113 12a83 ffc10113 12a03 ffc10113 12983 ffc10113 12403
  //   ffc10113 12503 ffc10113 12883 200073 1112023 410113 a12023 410113 812023 410113 1312023 410113
  //   1412023 410113 1512023 410113 1612023 410113 40e073 200b13 300a13 100a93 1600433 441413 14469b3
  //   1300533 2200893 73 fe0416e3 415a0a33 fe0a10e3 40f073 ffc10113 12b03 ffc10113 12a83 ffc10113 12a03
  //   ffc10113 12983 ffc10113 12403 ffc10113 12503 ffc10113 12883 200073 1112023 410113 a12023 410113
  //   812023 410113 1312023 410113 1412023 410113 1512023 410113 1612023 410113 40e073 300b13 300a13
  //   100a93 1600433 441413 14469b3 1300533 2200893 73 fe0416e3 415a0a33 fe0a10e3 40f073 ffc10113 12b03
  //   ffc10113 12a83 ffc10113 12a03 ffc10113 12983 ffc10113 12403 ffc10113 12503 ffc10113 12883 200073
  //   JAL
  //   JALR
  //   URET
  //   Beq
  //   Bne
  //   MemToReg
  //   MemWrite
  //   AluOP
  //   AluSrcB
  //   RegWrite
  //   S_Tyoe
  //   I型
  //   S型
  //   B型
  //   J型
  //   为方便自动评测，需要输出PC，IR，寄存器堆写如数据RDin
  //   rs1
  //   rs2
  //   rd
  //   RAM写使能MemWrite、RAM写入数据MDin等信号
  //   中断入口信号
  //   控制位
  //   暂停节拍，不能为0
  //   入口地址
  //   戳工具置1进入计数暂停模式，ctrl+k时钟自动运行到对应节拍暂停
  //   ctrl+k关闭时钟连续运行，将控制位置零，进入单步调试模式调试
  //   用这个时钟源需要去掉电路中的其他时钟源
  //   数据存储器
  //   可计数暂停的时钟源
  //   高级中断低级使能逻辑
  //   中断状态逻辑plus，承接中断等级比较以及开中断信号和清零信号
  //   中断状态逻辑
  //   中断出口逻辑
  //   清零信号滞留
endmodule

module \封装正确性测试  (
);

  wire IR1, IR2, IR3, MemW, RegW;
  wire [31:0] EX_PC, ID_PC, IF_PC, IR, LED, MDin, MDinr, MEM_PC, PC, RDin, RDinr, WB_PC;

  \单周期RISC_V  \u_单周期risc_v_1  (
    .IR1(IR1), .IR2(IR2), .IR3(IR3), .RegWrite(RegW), .MemWrite(MemW), .PC(PC), .IR(IR), .RDin(RDin),
    .MDin(MDin), .LedData(LED));
  \气泡流水线  \u_气泡流水线_1  (
    .RegWrite(RegW), .MemWrite(MemW), .IF_PC(IF_PC), .ID_PC(ID_PC), .EX_PC(EX_PC), .M_PC(MEM_PC),
    .WB_PC(WB_PC), .RDin(RDinr), .MDin(MDinr), .LedData(LED));
  \单周期_单级中断  \u_单周期_单级中断_1  (
    .IR1(IR1), .IR2(IR2), .IR3(IR3), .RegWrite(RegW), .MemWrite(MemW), .PC(PC), .IR(IR), .RDin(RDin),
    .MDin(MDin), .LedData(LED));
  \理想流水线  \u_理想流水线_1  (
    .RegWrite(RegW), .MemWrite(MemW), .IF_PC(IF_PC), .ID_PC(ID_PC), .EX_PC(EX_PC), .M_PC(MEM_PC),
    .WB_PC(WB_PC), .RDin(RDinr), .MDin(MDinr), .LedData(LED));
  \重定向中断流水线  \u_重定向中断流水线_1  (
    .MemWrite(MemW), .IF_PC(IF_PC), .ID_PC(ID_PC), .EX_PC(EX_PC), .M_PC(MEM_PC), .WB_PC(WB_PC), .RDin(RDinr),
    .LedData(LED), .MDin(MDinr), .RegWrite(RegW));
  \单周期_多级中断  \u_单周期_多级中断_1  (
    .RegWrite(RegW), .MemWrite(MemW), .PC(PC), .IR(IR), .RDin(RDin), .MDin(MDin), .LedData(LED));

  // Notes on the sheet:
  //   单周期封装测试
  //   气泡流水封装测试
  //   单周期+单级中断封装测试
  //   请检查上面封装有无位宽不匹配，引脚标签是否和连接的标签相对应，否则无法在educoder平台上正确测试
  //   理想流水封装测试
  //   重定向流水封装测试
  //   单周期+多级中断封装测试
endmodule

module \IF_ID流水寄存器  (
  input  IntR,
  input  [31:0] IR,
  input  [31:0] PC,
  input  [31:0] PC_4,
  input  CLK,
  input  \同步清零_气泡_高电平有效 ,
  input  \使能端_低电平有效_stall_高电平有效 ,
  output IntRout,
  output [31:0] IRout,
  output [31:0] PCout,
  output [31:0] PC_4out
);

  wire multiplexer_1_out, pull_resistor_2_node;
  wire [31:0] multiplexer_2_out, multiplexer_3_out, multiplexer_4_out;

  Multiplexer #(.select(1), .width(1), .disabled("Z"), .enable("false")) multiplexer_1 (
    .in0(IntR), .in1(1'b0), .out(multiplexer_1_out), .sel(\同步清零_气泡_高电平有效 ));
  Multiplexer #(.select(1), .width(32), .disabled("Z"), .enable("false")) multiplexer_2 (
    .in0(IR), .in1({32{1'b0}}), .out(multiplexer_2_out), .sel(\同步清零_气泡_高电平有效 ));
  Multiplexer #(.select(1), .width(32), .disabled("Z"), .enable("false")) multiplexer_3 (
    .in0(PC), .in1({32{1'b0}}), .out(multiplexer_3_out), .sel(\同步清零_气泡_高电平有效 ));
  Multiplexer #(.select(1), .width(32), .disabled("Z"), .enable("false")) multiplexer_4 (
    .in0(PC_4), .in1({32{1'b0}}), .out(multiplexer_4_out), .sel(\同步清零_气泡_高电平有效 ));
  Pull_Resistor #(.pull(0)) pull_resistor_1 (.node(\同步清零_气泡_高电平有效 ));
  Register #(.width(1), .trigger("rising"), .Select("low")) register_1 (
    .D(multiplexer_1_out), .en(pull_resistor_2_node), .Q(IntRout), .clk(CLK));  // open: clr
  Register #(.width(32), .trigger("rising"), .Select("low")) register_2 (
    .D(multiplexer_2_out), .en(pull_resistor_2_node), .Q(IRout), .clk(CLK));  // open: clr
  Register #(.width(32), .trigger("rising"), .Select("low")) register_3 (
    .D(multiplexer_3_out), .en(pull_resistor_2_node), .Q(PCout), .clk(CLK));  // open: clr
  Register #(.width(32), .trigger("rising"), .Select("low")) register_4 (
    .D(multiplexer_4_out), .en(pull_resistor_2_node), .Q(PC_4out), .clk(CLK));  // open: clr
  Pull_Resistor #(.pull(0)) pull_resistor_2 (.node(pull_resistor_2_node));
  not not_1 (pull_resistor_2_node, \使能端_低电平有效_stall_高电平有效 );
endmodule

module \ID_EX流水寄存器  (
  input  IntR,
  input  lb,
  input  AUIPC,
  input  JAL,
  input  JALR,
  input  URET,
  input  Beq,
  input  Bge,
  input  Bne,
  input  MemToReg,
  input  MemWrite,
  input  [3:0] AluOp,
  input  AluSrcB,
  input  RegWrite,
  input  ecall,
  input  [1:0] R1Src,
  input  [31:0] R1,
  input  [1:0] R2Src,
  input  [31:0] R2,
  input  [4:0] Rd,
  input  [31:0] PC,
  input  [31:0] PC_4,
  input  [31:0] IR,
  input  [31:0] I_S,
  input  [31:0] B,
  input  [31:0] I,
  input  [31:0] U,
  input  CLK,
  input  \同步清零_气泡_高电平有效 ,
  input  \使能端_低电平有效_stall_高电平有效 ,
  output IntRout,
  output lbout,
  output AUIPCout,
  output JALout,
  output JALRout,
  output URETout,
  output Beqout,
  output Bgeout,
  output Bneout,
  output MemToRegout,
  output MemWriteout,
  output [3:0] AluOpout,
  output AluSrcBout,
  output RegWrite_2,
  output ecallout,
  output [1:0] R1Srcout,
  output [31:0] R1out,
  output [1:0] ecallout_2,
  output [31:0] R2out,
  output [4:0] Rdout,
  output [31:0] PCout,
  output [31:0] PC_4out,
  output [31:0] IRout,
  output [31:0] I_Sout,
  output [31:0] Bout,
  output [31:0] Iout,
  output [31:0] Uout
);

  wire multiplexer_1_out, multiplexer_2_out, multiplexer_3_out, multiplexer_4_out, multiplexer_5_out,
       multiplexer_6_out, multiplexer_7_out, multiplexer_8_out, multiplexer_9_out, multiplexer_10_out,
       multiplexer_11_out, multiplexer_13_out, multiplexer_14_out, multiplexer_15_out, not_1_out;
  wire [1:0] multiplexer_16_out, multiplexer_18_out;
  wire [3:0] multiplexer_12_out;
  wire [4:0] multiplexer_20_out;
  wire [31:0] multiplexer_17_out, multiplexer_19_out, multiplexer_21_out, multiplexer_22_out,
       multiplexer_23_out, multiplexer_24_out, multiplexer_25_out, multiplexer_26_out, multiplexer_27_out;

  Multiplexer #(.select(1), .width(1), .disabled("Z"), .enable("false")) multiplexer_1 (
    .in0(IntR), .in1(1'b0), .out(multiplexer_1_out), .sel(\同步清零_气泡_高电平有效 ));
  Multiplexer #(.select(1), .width(1), .disabled("Z"), .enable("false")) multiplexer_2 (
    .in0(lb), .in1(1'b0), .out(multiplexer_2_out), .sel(\同步清零_气泡_高电平有效 ));
  Multiplexer #(.select(1), .width(1), .disabled("Z"), .enable("false")) multiplexer_3 (
    .in0(AUIPC), .in1(1'b0), .out(multiplexer_3_out), .sel(\同步清零_气泡_高电平有效 ));
  Multiplexer #(.select(1), .width(1), .disabled("Z"), .enable("false")) multiplexer_4 (
    .in0(JAL), .in1(1'b0), .out(multiplexer_4_out), .sel(\同步清零_气泡_高电平有效 ));
  Multiplexer #(.select(1), .width(1), .disabled("Z"), .enable("false")) multiplexer_5 (
    .in0(JALR), .in1(1'b0), .out(multiplexer_5_out), .sel(\同步清零_气泡_高电平有效 ));
  Multiplexer #(.select(1), .width(1), .disabled("Z"), .enable("false")) multiplexer_6 (
    .in0(URET), .in1(1'b0), .out(multiplexer_6_out), .sel(\同步清零_气泡_高电平有效 ));
  Multiplexer #(.select(1), .width(1), .disabled("Z"), .enable("false")) multiplexer_7 (
    .in0(Beq), .in1(1'b0), .out(multiplexer_7_out), .sel(\同步清零_气泡_高电平有效 ));
  Multiplexer #(.select(1), .width(1), .disabled("Z"), .enable("false")) multiplexer_8 (
    .in0(Bge), .in1(1'b0), .out(multiplexer_8_out), .sel(\同步清零_气泡_高电平有效 ));
  Multiplexer #(.select(1), .width(1), .disabled("Z"), .enable("false")) multiplexer_9 (
    .in0(Bne), .in1(1'b0), .out(multiplexer_9_out), .sel(\同步清零_气泡_高电平有效 ));
  Multiplexer #(.select(1), .width(1), .disabled("Z"), .enable("false")) multiplexer_10 (
    .in0(MemToReg), .in1(1'b0), .out(multiplexer_10_out), .sel(\同步清零_气泡_高电平有效 ));
  Multiplexer #(.select(1), .width(1), .disabled("Z"), .enable("false")) multiplexer_11 (
    .in0(MemWrite), .in1(1'b0), .out(multiplexer_11_out), .sel(\同步清零_气泡_高电平有效 ));
  Multiplexer #(.select(1), .width(4), .disabled("Z"), .enable("false")) multiplexer_12 (
    .in0(AluOp), .in1(4'b0000), .out(multiplexer_12_out), .sel(\同步清零_气泡_高电平有效 ));
  Multiplexer #(.select(1), .width(1), .disabled("Z"), .enable("false")) multiplexer_13 (
    .in0(AluSrcB), .in1(1'b0), .out(multiplexer_13_out), .sel(\同步清零_气泡_高电平有效 ));
  Multiplexer #(.select(1), .width(1), .disabled("Z"), .enable("false")) multiplexer_14 (
    .in0(RegWrite), .in1(1'b0), .out(multiplexer_14_out), .sel(\同步清零_气泡_高电平有效 ));
  Multiplexer #(.select(1), .width(1), .disabled("Z"), .enable("false")) multiplexer_15 (
    .in0(ecall), .in1(1'b0), .out(multiplexer_15_out), .sel(\同步清零_气泡_高电平有效 ));
  Multiplexer #(.select(1), .width(2), .disabled("Z"), .enable("false")) multiplexer_16 (
    .in0(R1Src), .in1(2'b00), .out(multiplexer_16_out), .sel(\同步清零_气泡_高电平有效 ));
  Multiplexer #(.select(1), .width(32), .disabled("Z"), .enable("false")) multiplexer_17 (
    .in0(R1), .in1({32{1'b0}}), .out(multiplexer_17_out), .sel(\同步清零_气泡_高电平有效 ));
  Multiplexer #(.select(1), .width(2), .disabled("Z"), .enable("false")) multiplexer_18 (
    .in0(R2Src), .in1(2'b00), .out(multiplexer_18_out), .sel(\同步清零_气泡_高电平有效 ));
  Multiplexer #(.select(1), .width(32), .disabled("Z"), .enable("false")) multiplexer_19 (
    .in0(R2), .in1({32{1'b0}}), .out(multiplexer_19_out), .sel(\同步清零_气泡_高电平有效 ));
  Multiplexer #(.select(1), .width(5), .disabled("Z"), .enable("false")) multiplexer_20 (
    .in0(Rd), .in1({5{1'b0}}), .out(multiplexer_20_out), .sel(\同步清零_气泡_高电平有效 ));
  Multiplexer #(.select(1), .width(32), .disabled("Z"), .enable("false")) multiplexer_21 (
    .in0(PC), .in1({32{1'b0}}), .out(multiplexer_21_out), .sel(\同步清零_气泡_高电平有效 ));
  Multiplexer #(.select(1), .width(32), .disabled("Z"), .enable("false")) multiplexer_22 (
    .in0(PC_4), .in1({32{1'b0}}), .out(multiplexer_22_out), .sel(\同步清零_气泡_高电平有效 ));
  Multiplexer #(.select(1), .width(32), .disabled("Z"), .enable("false")) multiplexer_23 (
    .in0(IR), .in1({32{1'b0}}), .out(multiplexer_23_out), .sel(\同步清零_气泡_高电平有效 ));
  Multiplexer #(.select(1), .width(32), .disabled("Z"), .enable("false")) multiplexer_24 (
    .in0(I_S), .in1({32{1'b0}}), .out(multiplexer_24_out), .sel(\同步清零_气泡_高电平有效 ));
  Multiplexer #(.select(1), .width(32), .disabled("Z"), .enable("false")) multiplexer_25 (
    .in0(B), .in1({32{1'b0}}), .out(multiplexer_25_out), .sel(\同步清零_气泡_高电平有效 ));
  Multiplexer #(.select(1), .width(32), .disabled("Z"), .enable("false")) multiplexer_26 (
    .in0(I), .in1({32{1'b0}}), .out(multiplexer_26_out), .sel(\同步清零_气泡_高电平有效 ));
  Multiplexer #(.select(1), .width(32), .disabled("Z"), .enable("false")) multiplexer_27 (
    .in0(U), .in1({32{1'b0}}), .out(multiplexer_27_out), .sel(\同步清零_气泡_高电平有效 ));
  Pull_Resistor #(.pull(0)) pull_resistor_1 (.node(\同步清零_气泡_高电平有效 ));
  not not_1 (not_1_out, \使能端_低电平有效_stall_高电平有效 );
  Register #(.width(1), .trigger("rising"), .Select("low")) register_1 (
    .D(multiplexer_1_out), .en(not_1_out), .Q(IntRout), .clk(CLK));  // open: clr
  Register #(.width(1), .trigger("rising"), .Select("low")) register_2 (
    .D(multiplexer_2_out), .en(not_1_out), .Q(lbout), .clk(CLK));  // open: clr
  Register #(.width(1), .trigger("rising"), .Select("low")) register_3 (
    .D(multiplexer_3_out), .en(not_1_out), .Q(AUIPCout), .clk(CLK));  // open: clr
  Register #(.width(1), .trigger("rising"), .Select("low")) register_4 (
    .D(multiplexer_4_out), .en(not_1_out), .Q(JALout), .clk(CLK));  // open: clr
  Register #(.width(1), .trigger("rising"), .Select("low")) register_5 (
    .D(multiplexer_5_out), .en(not_1_out), .Q(JALRout), .clk(CLK));  // open: clr
  Register #(.width(1), .trigger("rising"), .Select("low")) register_6 (
    .D(multiplexer_6_out), .en(not_1_out), .Q(URETout), .clk(CLK));  // open: clr
  Register #(.width(1), .trigger("rising"), .Select("low")) register_7 (
    .D(multiplexer_7_out), .en(not_1_out), .Q(Beqout), .clk(CLK));  // open: clr
  Register #(.width(1), .trigger("rising"), .Select("low")) register_8 (
    .D(multiplexer_8_out), .en(not_1_out), .Q(Bgeout), .clk(CLK));  // open: clr
  Register #(.width(1), .trigger("rising"), .Select("low")) register_9 (
    .D(multiplexer_9_out), .en(not_1_out), .Q(Bneout), .clk(CLK));  // open: clr
  Register #(.width(1), .trigger("rising"), .Select("low")) register_10 (
    .D(multiplexer_10_out), .en(not_1_out), .Q(MemToRegout), .clk(CLK));  // open: clr
  Register #(.width(1), .trigger("rising"), .Select("low")) register_11 (
    .D(multiplexer_11_out), .en(not_1_out), .Q(MemWriteout), .clk(CLK));  // open: clr
  Register #(.width(4), .trigger("rising"), .Select("low")) register_12 (
    .D(multiplexer_12_out), .en(not_1_out), .Q(AluOpout), .clk(CLK));  // open: clr
  Register #(.width(1), .trigger("rising"), .Select("low")) register_13 (
    .D(multiplexer_13_out), .en(not_1_out), .Q(AluSrcBout), .clk(CLK));  // open: clr
  Register #(.width(1), .trigger("rising"), .Select("low")) register_14 (
    .D(multiplexer_14_out), .en(not_1_out), .Q(RegWrite_2), .clk(CLK));  // open: clr
  Register #(.width(1), .trigger("rising"), .Select("low")) register_15 (
    .D(multiplexer_15_out), .en(not_1_out), .Q(ecallout), .clk(CLK));  // open: clr
  Register #(.width(2), .trigger("rising"), .Select("low")) register_16 (
    .D(multiplexer_16_out), .en(not_1_out), .Q(R1Srcout), .clk(CLK));  // open: clr
  Register #(.width(32), .trigger("rising"), .Select("low")) register_17 (
    .D(multiplexer_17_out), .en(not_1_out), .Q(R1out), .clk(CLK));  // open: clr
  Register #(.width(2), .trigger("rising"), .Select("low")) register_18 (
    .D(multiplexer_18_out), .en(not_1_out), .Q(ecallout_2), .clk(CLK));  // open: clr
  Register #(.width(32), .trigger("rising"), .Select("low")) register_19 (
    .D(multiplexer_19_out), .en(not_1_out), .Q(R2out), .clk(CLK));  // open: clr
  Register #(.width(5), .trigger("rising"), .Select("low")) register_20 (
    .D(multiplexer_20_out), .en(not_1_out), .Q(Rdout), .clk(CLK));  // open: clr
  Register #(.width(32), .trigger("rising"), .Select("low")) register_21 (
    .D(multiplexer_21_out), .en(not_1_out), .Q(PCout), .clk(CLK));  // open: clr
  Register #(.width(32), .trigger("rising"), .Select("low")) register_22 (
    .D(multiplexer_22_out), .en(not_1_out), .Q(PC_4out), .clk(CLK));  // open: clr
  Register #(.width(32), .trigger("rising"), .Select("low")) register_23 (
    .D(multiplexer_23_out), .en(not_1_out), .Q(IRout), .clk(CLK));  // open: clr
  Register #(.width(32), .trigger("rising"), .Select("low")) register_24 (
    .D(multiplexer_24_out), .en(not_1_out), .Q(I_Sout), .clk(CLK));  // open: clr
  Register #(.width(32), .trigger("rising"), .Select("low")) register_25 (
    .D(multiplexer_25_out), .en(not_1_out), .Q(Bout), .clk(CLK));  // open: clr
  Register #(.width(32), .trigger("rising"), .Select("low")) register_26 (
    .D(multiplexer_26_out), .en(not_1_out), .Q(Iout), .clk(CLK));  // open: clr
  Register #(.width(32), .trigger("rising"), .Select("low")) register_27 (
    .D(multiplexer_27_out), .en(not_1_out), .Q(Uout), .clk(CLK));  // open: clr
  Pull_Resistor #(.pull(0)) pull_resistor_2 (.node(not_1_out));
endmodule

module \EX_MEM流水寄存器  (
  input  lb,
  input  AUIPC,
  input  J,
  input  MemToReg,
  input  MemWrite,
  input  RegWrite,
  input  ecall,
  input  [31:0] R1,
  input  [31:0] AluResult,
  input  [31:0] WriteData,
  input  [4:0] Rd,
  input  [31:0] PC,
  input  [31:0] PC_4,
  input  [31:0] IR,
  input  [31:0] auipc_res,
  input  CLK,
  input  \同步清零_气泡_高电平有效 ,
  input  \使能端_低电平有效_stall_高电平有效 ,
  output lbout,
  output AUIPCout,
  output Jout,
  output MemToRegout,
  output MemWriteout,
  output RegWriteout,
  output ecallout,
  output [31:0] R1out,
  output [31:0] AluResultout,
  output [31:0] WriteDataout,
  output [4:0] Rdout,
  output [31:0] PCout,
  output [31:0] PC_4out,
  output [31:0] IRout,
  output [31:0] auipc_out
);

  wire multiplexer_1_out, multiplexer_2_out, multiplexer_3_out, multiplexer_4_out, multiplexer_5_out,
       multiplexer_6_out, multiplexer_7_out, not_1_out;
  wire [4:0] multiplexer_11_out;
  wire [31:0] multiplexer_8_out, multiplexer_9_out, multiplexer_10_out, multiplexer_12_out,
       multiplexer_13_out, multiplexer_14_out, multiplexer_15_out;

  Multiplexer #(.select(1), .width(1), .disabled("Z"), .enable("false")) multiplexer_1 (
    .in0(lb), .in1(1'b0), .out(multiplexer_1_out), .sel(\同步清零_气泡_高电平有效 ));
  Multiplexer #(.select(1), .width(1), .disabled("Z"), .enable("false")) multiplexer_2 (
    .in0(AUIPC), .in1(1'b0), .out(multiplexer_2_out), .sel(\同步清零_气泡_高电平有效 ));
  Multiplexer #(.select(1), .width(1), .disabled("Z"), .enable("false")) multiplexer_3 (
    .in0(J), .in1(1'b0), .out(multiplexer_3_out), .sel(\同步清零_气泡_高电平有效 ));
  Multiplexer #(.select(1), .width(1), .disabled("Z"), .enable("false")) multiplexer_4 (
    .in0(MemToReg), .in1(1'b0), .out(multiplexer_4_out), .sel(\同步清零_气泡_高电平有效 ));
  Multiplexer #(.select(1), .width(1), .disabled("Z"), .enable("false")) multiplexer_5 (
    .in0(MemWrite), .in1(1'b0), .out(multiplexer_5_out), .sel(\同步清零_气泡_高电平有效 ));
  Multiplexer #(.select(1), .width(1), .disabled("Z"), .enable("false")) multiplexer_6 (
    .in0(RegWrite), .in1(1'b0), .out(multiplexer_6_out), .sel(\同步清零_气泡_高电平有效 ));
  Multiplexer #(.select(1), .width(1), .disabled("Z"), .enable("false")) multiplexer_7 (
    .in0(ecall), .in1(1'b0), .out(multiplexer_7_out), .sel(\同步清零_气泡_高电平有效 ));
  Multiplexer #(.select(1), .width(32), .disabled("Z"), .enable("false")) multiplexer_8 (
    .in0(R1), .in1({32{1'b0}}), .out(multiplexer_8_out), .sel(\同步清零_气泡_高电平有效 ));
  Multiplexer #(.select(1), .width(32), .disabled("Z"), .enable("false")) multiplexer_9 (
    .in0(AluResult), .in1({32{1'b0}}), .out(multiplexer_9_out), .sel(\同步清零_气泡_高电平有效 ));
  Multiplexer #(.select(1), .width(32), .disabled("Z"), .enable("false")) multiplexer_10 (
    .in0(WriteData), .in1({32{1'b0}}), .out(multiplexer_10_out), .sel(\同步清零_气泡_高电平有效 ));
  Multiplexer #(.select(1), .width(5), .disabled("Z"), .enable("false")) multiplexer_11 (
    .in0(Rd), .in1({5{1'b0}}), .out(multiplexer_11_out), .sel(\同步清零_气泡_高电平有效 ));
  Multiplexer #(.select(1), .width(32), .disabled("Z"), .enable("false")) multiplexer_12 (
    .in0(PC), .in1({32{1'b0}}), .out(multiplexer_12_out), .sel(\同步清零_气泡_高电平有效 ));
  Multiplexer #(.select(1), .width(32), .disabled("Z"), .enable("false")) multiplexer_13 (
    .in0(PC_4), .in1({32{1'b0}}), .out(multiplexer_13_out), .sel(\同步清零_气泡_高电平有效 ));
  Multiplexer #(.select(1), .width(32), .disabled("Z"), .enable("false")) multiplexer_14 (
    .in0(IR), .in1({32{1'b0}}), .out(multiplexer_14_out), .sel(\同步清零_气泡_高电平有效 ));
  Multiplexer #(.select(1), .width(32), .disabled("Z"), .enable("false")) multiplexer_15 (
    .in0(auipc_res), .in1({32{1'b0}}), .out(multiplexer_15_out), .sel(\同步清零_气泡_高电平有效 ));
  Pull_Resistor #(.pull(0)) pull_resistor_1 (.node(\同步清零_气泡_高电平有效 ));
  not not_1 (not_1_out, \使能端_低电平有效_stall_高电平有效 );
  Register #(.width(1), .trigger("rising"), .Select("low")) register_1 (
    .D(multiplexer_1_out), .en(not_1_out), .Q(lbout), .clk(CLK));  // open: clr
  Register #(.width(1), .trigger("rising"), .Select("low")) register_2 (
    .D(multiplexer_2_out), .en(not_1_out), .Q(AUIPCout), .clk(CLK));  // open: clr
  Register #(.width(1), .trigger("rising"), .Select("low")) register_3 (
    .D(multiplexer_3_out), .en(not_1_out), .Q(Jout), .clk(CLK));  // open: clr
  Register #(.width(1), .trigger("rising"), .Select("low")) register_4 (
    .D(multiplexer_4_out), .en(not_1_out), .Q(MemToRegout), .clk(CLK));  // open: clr
  Register #(.width(1), .trigger("rising"), .Select("low")) register_5 (
    .D(multiplexer_5_out), .en(not_1_out), .Q(MemWriteout), .clk(CLK));  // open: clr
  Register #(.width(1), .trigger("rising"), .Select("low")) register_6 (
    .D(multiplexer_6_out), .en(not_1_out), .Q(RegWriteout), .clk(CLK));  // open: clr
  Register #(.width(1), .trigger("rising"), .Select("low")) register_7 (
    .D(multiplexer_7_out), .en(not_1_out), .Q(ecallout), .clk(CLK));  // open: clr
  Register #(.width(32), .trigger("rising"), .Select("low")) register_8 (
    .D(multiplexer_8_out), .en(not_1_out), .Q(R1out), .clk(CLK));  // open: clr
  Register #(.width(32), .trigger("rising"), .Select("low")) register_9 (
    .D(multiplexer_9_out), .en(not_1_out), .Q(AluResultout), .clk(CLK));  // open: clr
  Register #(.width(32), .trigger("rising"), .Select("low")) register_10 (
    .D(multiplexer_10_out), .en(not_1_out), .Q(WriteDataout), .clk(CLK));  // open: clr
  Register #(.width(5), .trigger("rising"), .Select("low")) register_11 (
    .D(multiplexer_11_out), .en(not_1_out), .Q(Rdout), .clk(CLK));  // open: clr
  Register #(.width(32), .trigger("rising"), .Select("low")) register_12 (
    .D(multiplexer_12_out), .en(not_1_out), .Q(PCout), .clk(CLK));  // open: clr
  Register #(.width(32), .trigger("rising"), .Select("low")) register_13 (
    .D(multiplexer_13_out), .en(not_1_out), .Q(PC_4out), .clk(CLK));  // open: clr
  Register #(.width(32), .trigger("rising"), .Select("low")) register_14 (
    .D(multiplexer_14_out), .en(not_1_out), .Q(IRout), .clk(CLK));  // open: clr
  Register #(.width(32), .trigger("rising"), .Select("low")) register_15 (
    .D(multiplexer_15_out), .en(not_1_out), .Q(auipc_out), .clk(CLK));  // open: clr
  Pull_Resistor #(.pull(0)) pull_resistor_2 (.node(not_1_out));
endmodule

module \MEM_WB流水寄存器  (
  input  lb,
  input  AUIPC,
  input  J,
  input  MemToReg,
  input  RegWrite,
  input  ecall,
  input  [31:0] R1,
  input  [31:0] R2,
  input  [31:0] AluResult,
  input  [1:0] sel,
  input  [31:0] WriteData,
  input  [31:0] PC,
  input  [31:0] PC_4,
  input  [4:0] Rd,
  input  [31:0] IR,
  input  [31:0] auipc_2,
  input  CLK,
  input  \同步清零_气泡_高电平有效 ,
  input  \使能端_低电平有效_stall_高电平有效 ,
  output lbout,
  output AUIPCout,
  output Jout,
  output MemToRegout,
  output RegWriteout,
  output ecallout,
  output [31:0] R1out,
  output [31:0] R2out,
  output [31:0] AluResultout,
  output [1:0] selout,
  output [31:0] WriteDataout,
  output [31:0] PCout,
  output [31:0] PC_4out,
  output [4:0] Rdout,
  output [31:0] IRout,
  output [31:0] auipc_out
);

  wire multiplexer_1_out, multiplexer_2_out, multiplexer_3_out, multiplexer_4_out, multiplexer_5_out,
       multiplexer_6_out, not_1_out;
  wire [1:0] multiplexer_10_out;
  wire [4:0] multiplexer_14_out;
  wire [31:0] multiplexer_7_out, multiplexer_8_out, multiplexer_9_out, multiplexer_11_out,
       multiplexer_12_out, multiplexer_13_out, multiplexer_15_out, multiplexer_16_out;

  Multiplexer #(.select(1), .width(1), .disabled("Z"), .enable("false")) multiplexer_1 (
    .in0(lb), .in1(1'b0), .out(multiplexer_1_out), .sel(\同步清零_气泡_高电平有效 ));
  Multiplexer #(.select(1), .width(1), .disabled("Z"), .enable("false")) multiplexer_2 (
    .in0(AUIPC), .in1(1'b0), .out(multiplexer_2_out), .sel(\同步清零_气泡_高电平有效 ));
  Multiplexer #(.select(1), .width(1), .disabled("Z"), .enable("false")) multiplexer_3 (
    .in0(J), .in1(1'b0), .out(multiplexer_3_out), .sel(\同步清零_气泡_高电平有效 ));
  Multiplexer #(.select(1), .width(1), .disabled("Z"), .enable("false")) multiplexer_4 (
    .in0(MemToReg), .in1(1'b0), .out(multiplexer_4_out), .sel(\同步清零_气泡_高电平有效 ));
  Multiplexer #(.select(1), .width(1), .disabled("Z"), .enable("false")) multiplexer_5 (
    .in0(RegWrite), .in1(1'b0), .out(multiplexer_5_out), .sel(\同步清零_气泡_高电平有效 ));
  Multiplexer #(.select(1), .width(1), .disabled("Z"), .enable("false")) multiplexer_6 (
    .in0(ecall), .in1(1'b0), .out(multiplexer_6_out), .sel(\同步清零_气泡_高电平有效 ));
  Multiplexer #(.select(1), .width(32), .disabled("Z"), .enable("false")) multiplexer_7 (
    .in0(R1), .in1({32{1'b0}}), .out(multiplexer_7_out), .sel(\同步清零_气泡_高电平有效 ));
  Multiplexer #(.select(1), .width(32), .disabled("Z"), .enable("false")) multiplexer_8 (
    .in0(R2), .in1({32{1'b0}}), .out(multiplexer_8_out), .sel(\同步清零_气泡_高电平有效 ));
  Multiplexer #(.select(1), .width(32), .disabled("Z"), .enable("false")) multiplexer_9 (
    .in0(AluResult), .in1({32{1'b0}}), .out(multiplexer_9_out), .sel(\同步清零_气泡_高电平有效 ));
  Multiplexer #(.select(1), .width(2), .disabled("Z"), .enable("false")) multiplexer_10 (
    .in0(sel), .in1(2'b00), .out(multiplexer_10_out), .sel(\同步清零_气泡_高电平有效 ));
  Multiplexer #(.select(1), .width(32), .disabled("Z"), .enable("false")) multiplexer_11 (
    .in0(WriteData), .in1({32{1'b0}}), .out(multiplexer_11_out), .sel(\同步清零_气泡_高电平有效 ));
  Multiplexer #(.select(1), .width(32), .disabled("Z"), .enable("false")) multiplexer_12 (
    .in0(PC), .in1({32{1'b0}}), .out(multiplexer_12_out), .sel(\同步清零_气泡_高电平有效 ));
  Multiplexer #(.select(1), .width(32), .disabled("Z"), .enable("false")) multiplexer_13 (
    .in0(PC_4), .in1({32{1'b0}}), .out(multiplexer_13_out), .sel(\同步清零_气泡_高电平有效 ));
  Multiplexer #(.select(1), .width(5), .disabled("Z"), .enable("false")) multiplexer_14 (
    .in0(Rd), .in1({5{1'b0}}), .out(multiplexer_14_out), .sel(\同步清零_气泡_高电平有效 ));
  Multiplexer #(.select(1), .width(32), .disabled("Z"), .enable("false")) multiplexer_15 (
    .in0(IR), .in1({32{1'b0}}), .out(multiplexer_15_out), .sel(\同步清零_气泡_高电平有效 ));
  Multiplexer #(.select(1), .width(32), .disabled("Z"), .enable("false")) multiplexer_16 (
    .in0(auipc_2), .in1({32{1'b0}}), .out(multiplexer_16_out), .sel(\同步清零_气泡_高电平有效 ));
  Pull_Resistor #(.pull(0)) pull_resistor_1 (.node(\同步清零_气泡_高电平有效 ));
  not not_1 (not_1_out, \使能端_低电平有效_stall_高电平有效 );
  Register #(.width(1), .trigger("rising"), .Select("low")) register_1 (
    .D(multiplexer_1_out), .en(not_1_out), .Q(lbout), .clk(CLK));  // open: clr
  Register #(.width(1), .trigger("rising"), .Select("low")) register_2 (
    .D(multiplexer_2_out), .en(not_1_out), .Q(AUIPCout), .clk(CLK));  // open: clr
  Register #(.width(1), .trigger("rising"), .Select("low")) register_3 (
    .D(multiplexer_3_out), .en(not_1_out), .Q(Jout), .clk(CLK));  // open: clr
  Register #(.width(1), .trigger("rising"), .Select("low")) register_4 (
    .D(multiplexer_4_out), .en(not_1_out), .Q(MemToRegout), .clk(CLK));  // open: clr
  Register #(.width(1), .trigger("rising"), .Select("low")) register_5 (
    .D(multiplexer_5_out), .en(not_1_out), .Q(RegWriteout), .clk(CLK));  // open: clr
  Register #(.width(1), .trigger("rising"), .Select("low")) register_6 (
    .D(multiplexer_6_out), .en(not_1_out), .Q(ecallout), .clk(CLK));  // open: clr
  Register #(.width(32), .trigger("rising"), .Select("low")) register_7 (
    .D(multiplexer_7_out), .en(not_1_out), .Q(R1out), .clk(CLK));  // open: clr
  Register #(.width(32), .trigger("rising"), .Select("low")) register_8 (
    .D(multiplexer_8_out), .en(not_1_out), .Q(R2out), .clk(CLK));  // open: clr
  Register #(.width(32), .trigger("rising"), .Select("low")) register_9 (
    .D(multiplexer_9_out), .en(not_1_out), .Q(AluResultout), .clk(CLK));  // open: clr
  Register #(.width(2), .trigger("rising"), .Select("low")) register_10 (
    .D(multiplexer_10_out), .en(not_1_out), .Q(selout), .clk(CLK));  // open: clr
  Register #(.width(32), .trigger("rising"), .Select("low")) register_11 (
    .D(multiplexer_11_out), .en(not_1_out), .Q(WriteDataout), .clk(CLK));  // open: clr
  Register #(.width(32), .trigger("rising"), .Select("low")) register_12 (
    .D(multiplexer_12_out), .en(not_1_out), .Q(PCout), .clk(CLK));  // open: clr
  Register #(.width(32), .trigger("rising"), .Select("low")) register_13 (
    .D(multiplexer_13_out), .en(not_1_out), .Q(PC_4out), .clk(CLK));  // open: clr
  Register #(.width(5), .trigger("rising"), .Select("low")) register_14 (
    .D(multiplexer_14_out), .en(not_1_out), .Q(Rdout), .clk(CLK));  // open: clr
  Register #(.width(32), .trigger("rising"), .Select("low")) register_15 (
    .D(multiplexer_15_out), .en(not_1_out), .Q(IRout), .clk(CLK));  // open: clr
  Register #(.width(32), .trigger("rising"), .Select("low")) register_16 (
    .D(multiplexer_16_out), .en(not_1_out), .Q(auipc_out), .clk(CLK));  // open: clr
  Pull_Resistor #(.pull(0)) pull_resistor_2 (.node(not_1_out));
endmodule
