// Logisim project cpu24-int-riscv.circ as structural Verilog: 6 circuits, main circuit ◆单周期硬布线控制器
// 单周期硬布线控制器
module \单周期硬布线控制器  (
  input  [4:0] OP,
  input  [4:0] Funct,
  input  in_3,
  output [3:0] ALU_OP,
  output CSRRSI,
  output uret,
  output CSRRCI,
  output MemToReg,
  output AUIPC,
  output lb,
  output MemWrite,
  output ecall,
  output Bge,
  output ALU_SRC,
  output RegWrite,
  output S_type,
  output Beq,
  output Bne,
  output Jalr,
  output JAL
);

  wire \控制信号自动生成_1_ecall ;

  \运算控制器自动生成  \u_运算控制器自动生成_1  (
    .OP2(OP[0]), .OP3(OP[1]), .OP4(OP[2]), .OP5(OP[3]), .OP6(OP[4]), .F12(Funct[0]), .F13(Funct[1]),
    .F14(Funct[2]), .F25(Funct[3]), .F30(Funct[4]), .S0(ALU_OP[0]), .S1(ALU_OP[1]), .S2(ALU_OP[2]),
    .S3(ALU_OP[3]));
  \控制信号自动生成  \u_控制信号自动生成_1  (
    .OP2(OP[0]), .CSRRSI(CSRRSI), .OP3(OP[1]), .OP4(OP[2]), .OP5(OP[3]), .CSRRCI(CSRRCI), .OP6(OP[4]),
    .F12(Funct[0]), .F13(Funct[1]), .F14(Funct[2]), .F25(Funct[3]), .F30(Funct[4]), .MemToReg(MemToReg),
    .AUIPC(AUIPC), .lb(lb), .MemWrite(MemWrite), .Bge(Bge), .ALU_SRC(ALU_SRC), .RegWrite(RegWrite),
    .ecall(\控制信号自动生成_1_ecall ), .S_Type(S_type), .BEQ(Beq), .BNE(Bne), .JALR(Jalr), .JAL(JAL));
  and and_1 (uret, in_3, \控制信号自动生成_1_ecall );
  and and_2 (ecall, ~in_3, \控制信号自动生成_1_ecall );  // AND_Gate

  // Other names for the same wires on the sheet: IR21 = in_3; OP_CODE[4:0] = OP

  // Notes on the sheet:
  //   运算器控制器，根据指令生成运算器功能选择信号
  //   控制信号生成，产生数据通路需要的其他控制信号
endmodule

// 运算器控制器
module \运算控制器自动生成  (
  input  OP2,
  input  OP3,
  input  OP4,
  input  OP5,
  input  OP6,
  input  F12,
  input  F13,
  input  F14,
  input  F25,
  input  F30,
  output S0,
  output S1,
  output S2,
  output S3
);

  wire and_1_out, and_2_out, and_3_out, and_4_out, and_5_out, and_6_out, and_7_out, and_8_out, and_9_out,
       and_10_out, and_11_out, and_12_out, and_13_out, and_14_out, and_15_out, and_16_out, and_17_out,
       and_18_out, and_19_out, and_20_out, and_21_out, and_22_out, and_23_out, and_24_out, and_25_out,
       and_26_out, and_27_out, and_28_out, and_29_out, and_30_out, and_31_out, and_32_out, and_33_out,
       and_34_out, not_1_out, not_2_out, not_3_out, not_4_out, not_5_out, not_6_out, not_7_out, not_8_out,
       not_9_out, not_10_out, not_11_out, not_12_out, not_13_out, not_14_out, not_15_out, not_16_out,
       not_17_out, not_18_out, not_19_out, not_20_out, not_21_out, not_22_out, not_23_out, not_24_out,
       not_25_out, not_26_out, not_27_out, not_28_out, not_29_out, not_30_out, not_31_out, not_32_out,
       not_33_out, not_34_out, not_35_out, not_36_out, not_37_out, not_38_out, not_39_out, not_40_out,
       not_41_out, not_42_out, not_43_out, not_44_out, not_45_out, not_46_out, not_47_out, not_48_out,
       not_49_out, not_50_out, not_51_out, not_52_out, not_53_out, not_54_out, not_55_out, not_56_out,
       not_57_out, not_58_out, not_59_out, not_60_out, not_61_out, not_62_out, not_63_out, not_64_out,
       not_65_out, not_66_out, not_67_out, not_68_out, not_69_out, not_70_out, not_71_out, not_72_out,
       not_73_out, not_74_out, not_75_out, not_76_out, not_77_out, not_78_out, not_79_out, not_80_out,
       not_81_out, not_82_out, not_83_out, not_84_out, not_85_out, not_86_out, not_87_out, not_88_out,
       not_89_out, not_90_out, not_91_out, not_92_out, not_93_out, not_94_out, not_95_out, not_96_out,
       not_97_out, not_98_out, not_99_out, not_100_out, not_101_out, not_102_out, not_103_out, not_104_out,
       not_105_out, not_106_out, not_107_out, not_108_out, not_109_out, not_110_out, not_111_out,
       not_112_out, not_113_out, not_114_out, not_115_out, not_116_out, not_117_out, not_118_out,
       not_119_out, not_120_out, not_121_out, not_122_out, not_123_out, not_124_out, not_125_out,
       not_126_out, not_127_out, not_128_out, not_129_out, not_130_out, not_131_out, not_132_out,
       not_133_out, not_134_out, not_135_out, not_136_out, not_137_out, not_138_out, not_139_out,
       not_140_out, not_141_out, not_142_out, not_143_out, not_144_out, not_145_out, not_146_out,
       not_147_out, not_148_out, not_149_out, not_150_out, not_151_out, not_152_out, not_153_out,
       not_154_out, not_155_out, not_156_out, not_157_out, not_158_out, not_159_out, not_160_out,
       not_161_out, not_162_out, not_163_out, not_164_out, not_165_out, not_166_out, not_167_out,
       not_168_out, not_169_out, not_170_out, not_171_out, not_172_out, not_173_out, not_174_out,
       not_175_out, not_176_out, not_177_out, not_178_out, not_179_out, not_180_out, not_181_out,
       not_182_out, not_183_out, not_184_out, not_185_out, not_186_out, not_187_out, not_188_out,
       not_189_out, not_190_out, not_191_out, not_192_out, not_193_out, not_194_out, not_195_out,
       not_196_out, not_197_out, not_198_out, not_199_out, not_200_out, not_201_out, not_202_out,
       not_203_out, not_204_out, not_205_out, not_206_out, not_207_out, not_208_out, not_209_out, not_210_out;

  not not_1 (not_1_out, F30);
  not not_2 (not_2_out, F25);
  not not_3 (not_3_out, F14);
  not not_4 (not_4_out, F13);
  not not_5 (not_5_out, F12);
  not not_6 (not_6_out, OP6);
  not not_7 (not_7_out, OP3);
  not not_8 (not_8_out, OP2);
  not not_9 (not_9_out, F30);
  not not_10 (not_10_out, F25);
  not not_11 (not_11_out, OP6);
  not not_12 (not_12_out, OP3);
  not not_13 (not_13_out, OP2);
  not not_14 (not_14_out, F30);
  not not_15 (not_15_out, F25);
  not not_16 (not_16_out, F14);
  not not_17 (not_17_out, F12);
  not not_18 (not_18_out, OP6);
  not not_19 (not_19_out, OP3);
  not not_20 (not_20_out, OP2);
  not not_21 (not_21_out, F14);
  not not_22 (not_22_out, F13);
  not not_23 (not_23_out, F12);
  not not_24 (not_24_out, OP6);
  not not_25 (not_25_out, OP5);
  not not_26 (not_26_out, OP3);
  not not_27 (not_27_out, OP2);
  not not_28 (not_28_out, OP6);
  not not_29 (not_29_out, OP5);
  not not_30 (not_30_out, OP3);
  not not_31 (not_31_out, OP2);
  not not_32 (not_32_out, F13);
  not not_33 (not_33_out, F12);
  not not_34 (not_34_out, OP6);
  not not_35 (not_35_out, OP5);
  not not_36 (not_36_out, OP3);
  not not_37 (not_37_out, OP2);
  not not_38 (not_38_out, F14);
  not not_39 (not_39_out, F12);
  not not_40 (not_40_out, OP6);
  not not_41 (not_41_out, OP5);
  not not_42 (not_42_out, OP3);
  not not_43 (not_43_out, OP2);
  not not_44 (not_44_out, F25);
  not not_45 (not_45_out, F13);
  not not_46 (not_46_out, OP6);
  not not_47 (not_47_out, OP5);
  not not_48 (not_48_out, OP3);
  not not_49 (not_49_out, OP2);
  not not_50 (not_50_out, F14);
  not not_51 (not_51_out, F12);
  not not_52 (not_52_out, OP6);
  not not_53 (not_53_out, OP5);
  not not_54 (not_54_out, OP4);
  not not_55 (not_55_out, OP3);
  not not_56 (not_56_out, OP2);
  not not_57 (not_57_out, F14);
  not not_58 (not_58_out, F12);
  not not_59 (not_59_out, OP6);
  not not_60 (not_60_out, OP4);
  not not_61 (not_61_out, OP3);
  not not_62 (not_62_out, OP2);
  not not_63 (not_63_out, F14);
  not not_64 (not_64_out, F13);
  not not_65 (not_65_out, F12);
  not not_66 (not_66_out, OP6);
  not not_67 (not_67_out, OP5);
  not not_68 (not_68_out, OP4);
  not not_69 (not_69_out, OP3);
  not not_70 (not_70_out, OP2);
  not not_71 (not_71_out, F25);
  not not_72 (not_72_out, F14);
  not not_73 (not_73_out, F13);
  not not_74 (not_74_out, F12);
  not not_75 (not_75_out, OP6);
  not not_76 (not_76_out, OP3);
  not not_77 (not_77_out, OP2);
  not not_78 (not_78_out, F30);
  not not_79 (not_79_out, F25);
  not not_80 (not_80_out, OP6);
  not not_81 (not_81_out, OP3);
  not not_82 (not_82_out, OP2);
  not not_83 (not_83_out, F30);
  not not_84 (not_84_out, F25);
  not not_85 (not_85_out, F14);
  not not_86 (not_86_out, F12);
  not not_87 (not_87_out, OP6);
  not not_88 (not_88_out, OP3);
  not not_89 (not_89_out, OP2);
  not not_90 (not_90_out, OP6);
  not not_91 (not_91_out, OP5);
  not not_92 (not_92_out, OP3);
  not not_93 (not_93_out, OP2);
  not not_94 (not_94_out, F14);
  not not_95 (not_95_out, F12);
  not not_96 (not_96_out, OP6);
  not not_97 (not_97_out, OP5);
  not not_98 (not_98_out, OP3);
  not not_99 (not_99_out, OP2);
  not not_100 (not_100_out, F30);
  not not_101 (not_101_out, F25);
  not not_102 (not_102_out, F13);
  not not_103 (not_103_out, OP6);
  not not_104 (not_104_out, OP5);
  not not_105 (not_105_out, OP3);
  not not_106 (not_106_out, OP2);
  not not_107 (not_107_out, F30);
  not not_108 (not_108_out, F25);
  not not_109 (not_109_out, F14);
  not not_110 (not_110_out, F13);
  not not_111 (not_111_out, F12);
  not not_112 (not_112_out, OP6);
  not not_113 (not_113_out, OP3);
  not not_114 (not_114_out, OP2);
  not not_115 (not_115_out, F25);
  not not_116 (not_116_out, F14);
  not not_117 (not_117_out, F13);
  not not_118 (not_118_out, F12);
  not not_119 (not_119_out, OP6);
  not not_120 (not_120_out, OP3);
  not not_121 (not_121_out, OP2);
  not not_122 (not_122_out, F30);
  not not_123 (not_123_out, F25);
  not not_124 (not_124_out, OP6);
  not not_125 (not_125_out, OP3);
  not not_126 (not_126_out, OP2);
  not not_127 (not_127_out, F30);
  not not_128 (not_128_out, F25);
  not not_129 (not_129_out, F14);
  not not_130 (not_130_out, OP6);
  not not_131 (not_131_out, OP3);
  not not_132 (not_132_out, OP2);
  not not_133 (not_133_out, F14);
  not not_134 (not_134_out, F13);
  not not_135 (not_135_out, F12);
  not not_136 (not_136_out, OP6);
  not not_137 (not_137_out, OP5);
  not not_138 (not_138_out, OP3);
  not not_139 (not_139_out, OP2);
  not not_140 (not_140_out, OP6);
  not not_141 (not_141_out, OP5);
  not not_142 (not_142_out, OP3);
  not not_143 (not_143_out, OP2);
  not not_144 (not_144_out, F14);
  not not_145 (not_145_out, F12);
  not not_146 (not_146_out, OP6);
  not not_147 (not_147_out, OP5);
  not not_148 (not_148_out, OP4);
  not not_149 (not_149_out, OP3);
  not not_150 (not_150_out, OP2);
  not not_151 (not_151_out, F14);
  not not_152 (not_152_out, F12);
  not not_153 (not_153_out, OP6);
  not not_154 (not_154_out, OP4);
  not not_155 (not_155_out, OP3);
  not not_156 (not_156_out, OP2);
  not not_157 (not_157_out, F14);
  not not_158 (not_158_out, OP6);
  not not_159 (not_159_out, OP5);
  not not_160 (not_160_out, OP3);
  not not_161 (not_161_out, OP2);
  not not_162 (not_162_out, F14);
  not not_163 (not_163_out, F13);
  not not_164 (not_164_out, F12);
  not not_165 (not_165_out, OP6);
  not not_166 (not_166_out, OP5);
  not not_167 (not_167_out, OP4);
  not not_168 (not_168_out, OP3);
  not not_169 (not_169_out, OP2);
  not not_170 (not_170_out, F30);
  not not_171 (not_171_out, F25);
  not not_172 (not_172_out, F12);
  not not_173 (not_173_out, OP6);
  not not_174 (not_174_out, OP3);
  not not_175 (not_175_out, OP2);
  not not_176 (not_176_out, F30);
  not not_177 (not_177_out, F25);
  not not_178 (not_178_out, F14);
  not not_179 (not_179_out, F12);
  not not_180 (not_180_out, OP6);
  not not_181 (not_181_out, OP3);
  not not_182 (not_182_out, OP2);
  not not_183 (not_183_out, F30);
  not not_184 (not_184_out, F25);
  not not_185 (not_185_out, F14);
  not not_186 (not_186_out, OP6);
  not not_187 (not_187_out, OP3);
  not not_188 (not_188_out, OP2);
  not not_189 (not_189_out, F12);
  not not_190 (not_190_out, OP6);
  not not_191 (not_191_out, OP5);
  not not_192 (not_192_out, OP3);
  not not_193 (not_193_out, OP2);
  not not_194 (not_194_out, F13);
  not not_195 (not_195_out, F12);
  not not_196 (not_196_out, OP6);
  not not_197 (not_197_out, OP5);
  not not_198 (not_198_out, OP3);
  not not_199 (not_199_out, OP2);
  not not_200 (not_200_out, F14);
  not not_201 (not_201_out, F12);
  not not_202 (not_202_out, OP6);
  not not_203 (not_203_out, OP5);
  not not_204 (not_204_out, OP3);
  not not_205 (not_205_out, OP2);
  not not_206 (not_206_out, F14);
  not not_207 (not_207_out, OP6);
  not not_208 (not_208_out, OP5);
  not not_209 (not_209_out, OP3);
  not not_210 (not_210_out, OP2);
  and and_1 (and_1_out, not_1_out, not_2_out, not_3_out, not_4_out, not_5_out, not_6_out, OP5, OP4, not_7_out, not_8_out);
  and and_2 (and_2_out, not_9_out, not_10_out, F14, F13, F12, not_11_out, OP5, OP4, not_12_out, not_13_out);
  and and_3 (and_3_out, not_14_out, not_15_out, not_16_out, F13, not_17_out, not_18_out, OP5, OP4, not_19_out, not_20_out);
  and and_4 (and_4_out, not_21_out, not_22_out, not_23_out, not_24_out, not_25_out, OP4, not_26_out, not_27_out);
  and and_5 (and_5_out, F14, F13, F12, not_28_out, not_29_out, OP4, not_30_out, not_31_out);
  and and_6 (and_6_out, F14, not_32_out, not_33_out, not_34_out, not_35_out, OP4, not_36_out, not_37_out);
  and and_7 (and_7_out, not_38_out, F13, not_39_out, not_40_out, not_41_out, OP4, not_42_out, not_43_out);
  and and_8 (and_8_out, F30, not_44_out, F14, not_45_out, F12, not_46_out, not_47_out, OP4, not_48_out, not_49_out);
  and and_9 (and_9_out, not_50_out, F13, not_51_out, not_52_out, not_53_out, not_54_out, not_55_out, not_56_out);
  and and_10 (and_10_out, not_57_out, F13, not_58_out, not_59_out, OP5, not_60_out, not_61_out, not_62_out);
  and and_11 (and_11_out, not_63_out, not_64_out, not_65_out, not_66_out, not_67_out, not_68_out, not_69_out, not_70_out);
  and and_12 (and_12_out, F30, not_71_out, not_72_out, not_73_out, not_74_out, not_75_out, OP5, OP4, not_76_out, not_77_out);
  and and_13 (and_13_out, not_78_out, not_79_out, F14, F13, F12, not_80_out, OP5, OP4, not_81_out, not_82_out);
  and and_14 (and_14_out, not_83_out, not_84_out, not_85_out, F13, not_86_out, not_87_out, OP5, OP4, not_88_out, not_89_out);
  and and_15 (and_15_out, F14, F13, F12, not_90_out, not_91_out, OP4, not_92_out, not_93_out);
  and and_16 (and_16_out, not_94_out, F13, not_95_out, not_96_out, not_97_out, OP4, not_98_out, not_99_out);
  and and_17 (and_17_out, not_100_out, not_101_out, F14, not_102_out, F12, not_103_out, not_104_out, OP4, not_105_out, not_106_out);
  and and_18 (and_18_out, not_107_out, not_108_out, not_109_out, not_110_out, not_111_out, not_112_out, OP5, OP4, not_113_out, not_114_out);
  and and_19 (and_19_out, F30, not_115_out, not_116_out, not_117_out, not_118_out, not_119_out, OP5, OP4, not_120_out, not_121_out);
  and and_20 (and_20_out, not_122_out, not_123_out, F14, F13, F12, not_124_out, OP5, OP4, not_125_out, not_126_out);
  and and_21 (and_21_out, not_127_out, not_128_out, not_129_out, F13, F12, not_130_out, OP5, OP4, not_131_out, not_132_out);
  and and_22 (and_22_out, not_133_out, not_134_out, not_135_out, not_136_out, not_137_out, OP4, not_138_out, not_139_out);
  and and_23 (and_23_out, F14, F13, F12, not_140_out, not_141_out, OP4, not_142_out, not_143_out);
  and and_24 (and_24_out, not_144_out, F13, not_145_out, not_146_out, not_147_out, not_148_out, not_149_out, not_150_out);
  and and_25 (and_25_out, not_151_out, F13, not_152_out, not_153_out, OP5, not_154_out, not_155_out, not_156_out);
  and and_26 (and_26_out, not_157_out, F13, F12, not_158_out, not_159_out, OP4, not_160_out, not_161_out);
  and and_27 (and_27_out, not_162_out, not_163_out, not_164_out, not_165_out, not_166_out, not_167_out, not_168_out, not_169_out);
  and and_28 (and_28_out, not_170_out, not_171_out, F14, F13, not_172_out, not_173_out, OP5, OP4, not_174_out, not_175_out);
  and and_29 (and_29_out, not_176_out, not_177_out, not_178_out, F13, not_179_out, not_180_out, OP5, OP4, not_181_out, not_182_out);
  and and_30 (and_30_out, not_183_out, not_184_out, not_185_out, F13, F12, not_186_out, OP5, OP4, not_187_out, not_188_out);
  and and_31 (and_31_out, F14, F13, not_189_out, not_190_out, not_191_out, OP4, not_192_out, not_193_out);
  and and_32 (and_32_out, F14, not_194_out, not_195_out, not_196_out, not_197_out, OP4, not_198_out, not_199_out);
  and and_33 (and_33_out, not_200_out, F13, not_201_out, not_202_out, not_203_out, OP4, not_204_out, not_205_out);
  and and_34 (and_34_out, not_206_out, F13, F12, not_207_out, not_208_out, OP4, not_209_out, not_210_out);
  or or_1 (S0, and_1_out, and_2_out, and_3_out, and_4_out, and_5_out, and_6_out, and_7_out, and_8_out, and_9_out, and_10_out, and_11_out);
  or or_2 (S1, and_12_out, and_13_out, and_14_out, and_15_out, and_16_out, and_17_out);
  or or_3 (S2, and_18_out, and_19_out, and_20_out, and_21_out, and_22_out, and_23_out, and_24_out, and_25_out, and_26_out, and_27_out);
  or or_4 (S3, and_28_out, and_29_out, and_30_out, and_31_out, and_32_out, and_33_out, and_34_out);
endmodule

// 控制信号生成
module \控制信号自动生成  (
  input  OP2,
  input  OP3,
  input  OP4,
  input  OP5,
  input  OP6,
  input  F12,
  input  F13,
  input  F14,
  input  F25,
  input  F30,
  output CSRRSI,
  output CSRRCI,
  output MemToReg,
  output AUIPC,
  output lb,
  output MemWrite,
  output Bge,
  output ALU_SRC,
  output RegWrite,
  output ecall,
  output S_Type,
  output BEQ,
  output BNE,
  output JALR,
  output JAL
);

  wire and_3_out, and_4_out, and_9_out, and_10_out, and_11_out, and_12_out, and_13_out, and_14_out,
       and_15_out, and_16_out, and_17_out, and_18_out, and_19_out, and_20_out, and_21_out, and_22_out,
       and_23_out, and_24_out, and_25_out, and_26_out, and_27_out, and_28_out, and_29_out, and_30_out,
       and_31_out, and_32_out, and_33_out, and_34_out, and_35_out, and_36_out, and_37_out, and_38_out,
       and_39_out, and_40_out, and_41_out, not_1_out, not_2_out, not_3_out, not_4_out, not_5_out, not_6_out,
       not_7_out, not_8_out, not_9_out, not_10_out, not_11_out, not_12_out, not_13_out, not_14_out,
       not_15_out, not_16_out, not_17_out, not_18_out, not_19_out, not_20_out, not_21_out, not_22_out,
       not_23_out, not_24_out, not_25_out, not_26_out, not_27_out, not_28_out, not_29_out, not_30_out,
       not_31_out, not_32_out, not_33_out, not_34_out, not_35_out, not_36_out, not_37_out, not_38_out,
       not_39_out, not_40_out, not_41_out, not_42_out, not_43_out, not_44_out, not_45_out, not_46_out,
       not_47_out, not_48_out, not_49_out, not_50_out, not_51_out, not_52_out, not_53_out, not_54_out,
       not_55_out, not_56_out, not_57_out, not_58_out, not_59_out, not_60_out, not_61_out, not_62_out,
       not_63_out, not_64_out, not_65_out, not_66_out, not_67_out, not_68_out, not_69_out, not_70_out,
       not_71_out, not_72_out, not_73_out, not_74_out, not_75_out, not_76_out, not_77_out, not_78_out,
       not_79_out, not_80_out, not_81_out, not_82_out, not_83_out, not_84_out, not_85_out, not_86_out,
       not_87_out, not_88_out, not_89_out, not_90_out, not_91_out, not_92_out, not_93_out, not_94_out,
       not_95_out, not_96_out, not_97_out, not_98_out, not_99_out, not_100_out, not_101_out, not_102_out,
       not_103_out, not_104_out, not_105_out, not_106_out, not_107_out, not_108_out, not_109_out,
       not_110_out, not_111_out, not_112_out, not_113_out, not_114_out, not_115_out, not_116_out,
       not_117_out, not_118_out, not_119_out, not_120_out, not_121_out, not_122_out, not_123_out,
       not_124_out, not_125_out, not_126_out, not_127_out, not_128_out, not_129_out, not_130_out,
       not_131_out, not_132_out, not_133_out, not_134_out, not_135_out, not_136_out, not_137_out,
       not_138_out, not_139_out, not_140_out, not_141_out, not_142_out, not_143_out, not_144_out,
       not_145_out, not_146_out, not_147_out, not_148_out, not_149_out, not_150_out, not_151_out,
       not_152_out, not_153_out, not_154_out, not_155_out, not_156_out, not_157_out, not_158_out,
       not_159_out, not_160_out, not_161_out, not_162_out, not_163_out, not_164_out, not_165_out,
       not_166_out, not_167_out, not_168_out, not_169_out, not_170_out, not_171_out, not_172_out,
       not_173_out, not_174_out, not_175_out, not_176_out, not_177_out, not_178_out, not_179_out,
       not_180_out, not_181_out, not_182_out, not_183_out, not_184_out, not_185_out, not_186_out,
       not_187_out, not_188_out, not_189_out, not_190_out, not_191_out, not_192_out, not_193_out,
       not_194_out, not_195_out, not_196_out, not_197_out, not_198_out, not_199_out, not_200_out,
       not_201_out, not_202_out, not_203_out, not_204_out, not_205_out, not_206_out, not_207_out,
       not_208_out, not_209_out, not_210_out, not_211_out, not_212_out, not_213_out, not_214_out,
       not_215_out, not_216_out, not_217_out, not_218_out, not_219_out, not_220_out, not_221_out,
       not_222_out, not_223_out, not_224_out, not_225_out, not_226_out, not_227_out, not_228_out,
       not_229_out, not_230_out, not_231_out, not_232_out, not_233_out, not_234_out, not_235_out,
       not_236_out, not_237_out, not_238_out, not_239_out, not_240_out, not_241_out, not_242_out,
       not_243_out, not_244_out, not_245_out, not_246_out, not_247_out, not_248_out, not_249_out,
       not_250_out, not_251_out, not_252_out, not_253_out, not_254_out, not_255_out, not_256_out,
       not_257_out, not_258_out, not_259_out, not_260_out, not_261_out, not_262_out, not_263_out,
       not_264_out, not_265_out, not_266_out, not_267_out, not_268_out;

  not not_1 (not_1_out, F12);
  not not_2 (not_2_out, OP3);
  not not_3 (not_3_out, OP2);
  not not_4 (not_4_out, OP3);
  not not_5 (not_5_out, OP2);
  not not_6 (not_6_out, F14);
  not not_7 (not_7_out, F12);
  not not_8 (not_8_out, OP6);
  not not_9 (not_9_out, OP5);
  not not_10 (not_10_out, OP4);
  not not_11 (not_11_out, OP3);
  not not_12 (not_12_out, OP2);
  not not_13 (not_13_out, F14);
  not not_14 (not_14_out, F13);
  not not_15 (not_15_out, F12);
  not not_16 (not_16_out, OP6);
  not not_17 (not_17_out, OP5);
  not not_18 (not_18_out, OP4);
  not not_19 (not_19_out, OP3);
  not not_20 (not_20_out, OP2);
  not not_21 (not_21_out, OP6);
  not not_22 (not_22_out, OP5);
  not not_23 (not_23_out, OP3);
  not not_24 (not_24_out, F14);
  not not_25 (not_25_out, F13);
  not not_26 (not_26_out, F12);
  not not_27 (not_27_out, OP6);
  not not_28 (not_28_out, OP5);
  not not_29 (not_29_out, OP4);
  not not_30 (not_30_out, OP3);
  not not_31 (not_31_out, OP2);
  not not_32 (not_32_out, F14);
  not not_33 (not_33_out, F12);
  not not_34 (not_34_out, OP6);
  not not_35 (not_35_out, OP4);
  not not_36 (not_36_out, OP3);
  not not_37 (not_37_out, OP2);
  not not_38 (not_38_out, F13);
  not not_39 (not_39_out, OP4);
  not not_40 (not_40_out, OP3);
  not not_41 (not_41_out, OP2);
  not not_42 (not_42_out, F14);
  not not_43 (not_43_out, F13);
  not not_44 (not_44_out, F12);
  not not_45 (not_45_out, OP6);
  not not_46 (not_46_out, OP5);
  not not_47 (not_47_out, OP3);
  not not_48 (not_48_out, OP2);
  not not_49 (not_49_out, OP6);
  not not_50 (not_50_out, OP5);
  not not_51 (not_51_out, OP3);
  not not_52 (not_52_out, OP2);
  not not_53 (not_53_out, F12);
  not not_54 (not_54_out, OP6);
  not not_55 (not_55_out, OP5);
  not not_56 (not_56_out, OP3);
  not not_57 (not_57_out, OP2);
  not not_58 (not_58_out, F13);
  not not_59 (not_59_out, F12);
  not not_60 (not_60_out, OP6);
  not not_61 (not_61_out, OP5);
  not not_62 (not_62_out, OP3);
  not not_63 (not_63_out, OP2);
  not not_64 (not_64_out, F14);
  not not_65 (not_65_out, F12);
  not not_66 (not_66_out, OP6);
  not not_67 (not_67_out, OP5);
  not not_68 (not_68_out, OP3);
  not not_69 (not_69_out, OP2);
  not not_70 (not_70_out, F30);
  not not_71 (not_71_out, F25);
  not not_72 (not_72_out, F14);
  not not_73 (not_73_out, F13);
  not not_74 (not_74_out, OP6);
  not not_75 (not_75_out, OP5);
  not not_76 (not_76_out, OP3);
  not not_77 (not_77_out, OP2);
  not not_78 (not_78_out, F30);
  not not_79 (not_79_out, F25);
  not not_80 (not_80_out, F13);
  not not_81 (not_81_out, OP6);
  not not_82 (not_82_out, OP5);
  not not_83 (not_83_out, OP3);
  not not_84 (not_84_out, OP2);
  not not_85 (not_85_out, F25);
  not not_86 (not_86_out, F13);
  not not_87 (not_87_out, OP6);
  not not_88 (not_88_out, OP5);
  not not_89 (not_89_out, OP3);
  not not_90 (not_90_out, OP2);
  not not_91 (not_91_out, F14);
  not not_92 (not_92_out, F12);
  not not_93 (not_93_out, OP6);
  not not_94 (not_94_out, OP5);
  not not_95 (not_95_out, OP4);
  not not_96 (not_96_out, OP3);
  not not_97 (not_97_out, OP2);
  not not_98 (not_98_out, F14);
  not not_99 (not_99_out, F12);
  not not_100 (not_100_out, OP6);
  not not_101 (not_101_out, OP4);
  not not_102 (not_102_out, OP3);
  not not_103 (not_103_out, OP2);
  not not_104 (not_104_out, F14);
  not not_105 (not_105_out, F13);
  not not_106 (not_106_out, F12);
  not not_107 (not_107_out, OP4);
  not not_108 (not_108_out, OP3);
  not not_109 (not_109_out, F14);
  not not_110 (not_110_out, OP6);
  not not_111 (not_111_out, OP5);
  not not_112 (not_112_out, OP3);
  not not_113 (not_113_out, OP2);
  not not_114 (not_114_out, F14);
  not not_115 (not_115_out, F13);
  not not_116 (not_116_out, F12);
  not not_117 (not_117_out, OP6);
  not not_118 (not_118_out, OP5);
  not not_119 (not_119_out, OP4);
  not not_120 (not_120_out, OP3);
  not not_121 (not_121_out, OP2);
  not not_122 (not_122_out, F30);
  not not_123 (not_123_out, F25);
  not not_124 (not_124_out, F14);
  not not_125 (not_125_out, F13);
  not not_126 (not_126_out, F12);
  not not_127 (not_127_out, OP6);
  not not_128 (not_128_out, OP3);
  not not_129 (not_129_out, OP2);
  not not_130 (not_130_out, F25);
  not not_131 (not_131_out, F14);
  not not_132 (not_132_out, F13);
  not not_133 (not_133_out, F12);
  not not_134 (not_134_out, OP6);
  not not_135 (not_135_out, OP3);
  not not_136 (not_136_out, OP2);
  not not_137 (not_137_out, F30);
  not not_138 (not_138_out, F25);
  not not_139 (not_139_out, OP6);
  not not_140 (not_140_out, OP3);
  not not_141 (not_141_out, OP2);
  not not_142 (not_142_out, F30);
  not not_143 (not_143_out, F25);
  not not_144 (not_144_out, F12);
  not not_145 (not_145_out, OP6);
  not not_146 (not_146_out, OP3);
  not not_147 (not_147_out, OP2);
  not not_148 (not_148_out, F30);
  not not_149 (not_149_out, F25);
  not not_150 (not_150_out, F14);
  not not_151 (not_151_out, F12);
  not not_152 (not_152_out, OP6);
  not not_153 (not_153_out, OP3);
  not not_154 (not_154_out, OP2);
  not not_155 (not_155_out, F30);
  not not_156 (not_156_out, F25);
  not not_157 (not_157_out, F14);
  not not_158 (not_158_out, OP6);
  not not_159 (not_159_out, OP3);
  not not_160 (not_160_out, OP2);
  not not_161 (not_161_out, F14);
  not not_162 (not_162_out, F13);
  not not_163 (not_163_out, F12);
  not not_164 (not_164_out, OP6);
  not not_165 (not_165_out, OP5);
  not not_166 (not_166_out, OP3);
  not not_167 (not_167_out, OP2);
  not not_168 (not_168_out, OP6);
  not not_169 (not_169_out, OP5);
  not not_170 (not_170_out, OP3);
  not not_171 (not_171_out, OP2);
  not not_172 (not_172_out, F12);
  not not_173 (not_173_out, OP6);
  not not_174 (not_174_out, OP5);
  not not_175 (not_175_out, OP3);
  not not_176 (not_176_out, OP2);
  not not_177 (not_177_out, F13);
  not not_178 (not_178_out, F12);
  not not_179 (not_179_out, OP6);
  not not_180 (not_180_out, OP5);
  not not_181 (not_181_out, OP3);
  not not_182 (not_182_out, OP2);
  not not_183 (not_183_out, F14);
  not not_184 (not_184_out, F12);
  not not_185 (not_185_out, OP6);
  not not_186 (not_186_out, OP5);
  not not_187 (not_187_out, OP3);
  not not_188 (not_188_out, OP2);
  not not_189 (not_189_out, F30);
  not not_190 (not_190_out, F25);
  not not_191 (not_191_out, F14);
  not not_192 (not_192_out, F13);
  not not_193 (not_193_out, OP6);
  not not_194 (not_194_out, OP5);
  not not_195 (not_195_out, OP3);
  not not_196 (not_196_out, OP2);
  not not_197 (not_197_out, F30);
  not not_198 (not_198_out, F25);
  not not_199 (not_199_out, F13);
  not not_200 (not_200_out, OP6);
  not not_201 (not_201_out, OP5);
  not not_202 (not_202_out, OP3);
  not not_203 (not_203_out, OP2);
  not not_204 (not_204_out, F25);
  not not_205 (not_205_out, F13);
  not not_206 (not_206_out, OP6);
  not not_207 (not_207_out, OP5);
  not not_208 (not_208_out, OP3);
  not not_209 (not_209_out, OP2);
  not not_210 (not_210_out, F14);
  not not_211 (not_211_out, F12);
  not not_212 (not_212_out, OP6);
  not not_213 (not_213_out, OP5);
  not not_214 (not_214_out, OP4);
  not not_215 (not_215_out, OP3);
  not not_216 (not_216_out, OP2);
  not not_217 (not_217_out, OP4);
  not not_218 (not_218_out, F14);
  not not_219 (not_219_out, F13);
  not not_220 (not_220_out, F12);
  not not_221 (not_221_out, OP4);
  not not_222 (not_222_out, OP3);
  not not_223 (not_223_out, OP6);
  not not_224 (not_224_out, OP5);
  not not_225 (not_225_out, OP3);
  not not_226 (not_226_out, F14);
  not not_227 (not_227_out, OP6);
  not not_228 (not_228_out, OP5);
  not not_229 (not_229_out, OP3);
  not not_230 (not_230_out, OP2);
  not not_231 (not_231_out, F14);
  not not_232 (not_232_out, F13);
  not not_233 (not_233_out, F12);
  not not_234 (not_234_out, OP6);
  not not_235 (not_235_out, OP5);
  not not_236 (not_236_out, OP4);
  not not_237 (not_237_out, OP3);
  not not_238 (not_238_out, OP2);
  not not_239 (not_239_out, F30);
  not not_240 (not_240_out, F25);
  not not_241 (not_241_out, F14);
  not not_242 (not_242_out, F13);
  not not_243 (not_243_out, F12);
  not not_244 (not_244_out, OP3);
  not not_245 (not_245_out, OP2);
  not not_246 (not_246_out, F14);
  not not_247 (not_247_out, F12);
  not not_248 (not_248_out, OP6);
  not not_249 (not_249_out, OP4);
  not not_250 (not_250_out, OP3);
  not not_251 (not_251_out, OP2);
  not not_252 (not_252_out, F14);
  not not_253 (not_253_out, F13);
  not not_254 (not_254_out, F12);
  not not_255 (not_255_out, OP4);
  not not_256 (not_256_out, OP3);
  not not_257 (not_257_out, OP2);
  not not_258 (not_258_out, F14);
  not not_259 (not_259_out, F13);
  not not_260 (not_260_out, OP4);
  not not_261 (not_261_out, OP3);
  not not_262 (not_262_out, OP2);
  not not_263 (not_263_out, F14);
  not not_264 (not_264_out, F13);
  not not_265 (not_265_out, F12);
  not not_266 (not_266_out, OP4);
  not not_267 (not_267_out, OP3);
  not not_268 (not_268_out, OP4);
  and and_1 (CSRRSI, F14, F13, not_1_out, OP6, OP5, OP4, not_2_out, not_3_out);
  and and_2 (CSRRCI, F14, F13, F12, OP6, OP5, OP4, not_4_out, not_5_out);
  and and_3 (and_3_out, not_6_out, F13, not_7_out, not_8_out, not_9_out, not_10_out, not_11_out, not_12_out);
  and and_4 (and_4_out, not_13_out, not_14_out, not_15_out, not_16_out, not_17_out, not_18_out, not_19_out, not_20_out);
  and and_5 (AUIPC, not_21_out, not_22_out, OP4, not_23_out, OP2);
  and and_6 (lb, not_24_out, not_25_out, not_26_out, not_27_out, not_28_out, not_29_out, not_30_out, not_31_out);
  and and_7 (MemWrite, not_32_out, F13, not_33_out, not_34_out, OP5, not_35_out, not_36_out, not_37_out);
  and and_8 (Bge, F14, not_38_out, F12, OP6, OP5, not_39_out, not_40_out, not_41_out);
  and and_9 (and_9_out, not_42_out, not_43_out, not_44_out, not_45_out, not_46_out, OP4, not_47_out, not_48_out);
  and and_10 (and_10_out, F14, F13, F12, not_49_out, not_50_out, OP4, not_51_out, not_52_out);
  and and_11 (and_11_out, F14, F13, not_53_out, not_54_out, not_55_out, OP4, not_56_out, not_57_out);
  and and_12 (and_12_out, F14, not_58_out, not_59_out, not_60_out, not_61_out, OP4, not_62_out, not_63_out);
  and and_13 (and_13_out, not_64_out, F13, not_65_out, not_66_out, not_67_out, OP4, not_68_out, not_69_out);
  and and_14 (and_14_out, not_70_out, not_71_out, not_72_out, not_73_out, F12, not_74_out, not_75_out, OP4, not_76_out, not_77_out);
  and and_15 (and_15_out, not_78_out, not_79_out, F14, not_80_out, F12, not_81_out, not_82_out, OP4, not_83_out, not_84_out);
  and and_16 (and_16_out, F30, not_85_out, F14, not_86_out, F12, not_87_out, not_88_out, OP4, not_89_out, not_90_out);
  and and_17 (and_17_out, not_91_out, F13, not_92_out, not_93_out, not_94_out, not_95_out, not_96_out, not_97_out);
  and and_18 (and_18_out, not_98_out, F13, not_99_out, not_100_out, OP5, not_101_out, not_102_out, not_103_out);
  and and_19 (and_19_out, not_104_out, not_105_out, not_106_out, OP6, OP5, not_107_out, not_108_out, OP2);
  and and_20 (and_20_out, not_109_out, F13, F12, not_110_out, not_111_out, OP4, not_112_out, not_113_out);
  and and_21 (and_21_out, not_114_out, not_115_out, not_116_out, not_117_out, not_118_out, not_119_out, not_120_out, not_121_out);
  and and_22 (and_22_out, not_122_out, not_123_out, not_124_out, not_125_out, not_126_out, not_127_out, OP5, OP4, not_128_out, not_129_out);
  and and_23 (and_23_out, F30, not_130_out, not_131_out, not_132_out, not_133_out, not_134_out, OP5, OP4, not_135_out, not_136_out);
  and and_24 (and_24_out, not_137_out, not_138_out, F14, F13, F12, not_139_out, OP5, OP4, not_140_out, not_141_out);
  and and_25 (and_25_out, not_142_out, not_143_out, F14, F13, not_144_out, not_145_out, OP5, OP4, not_146_out, not_147_out);
  and and_26 (and_26_out, not_148_out, not_149_out, not_150_out, F13, not_151_out, not_152_out, OP5, OP4, not_153_out, not_154_out);
  and and_27 (and_27_out, not_155_out, not_156_out, not_157_out, F13, F12, not_158_out, OP5, OP4, not_159_out, not_160_out);
  and and_28 (and_28_out, not_161_out, not_162_out, not_163_out, not_164_out, not_165_out, OP4, not_166_out, not_167_out);
  and and_29 (and_29_out, F14, F13, F12, not_168_out, not_169_out, OP4, not_170_out, not_171_out);
  and and_30 (and_30_out, F14, F13, not_172_out, not_173_out, not_174_out, OP4, not_175_out, not_176_out);
  and and_31 (and_31_out, F14, not_177_out, not_178_out, not_179_out, not_180_out, OP4, not_181_out, not_182_out);
  and and_32 (and_32_out, not_183_out, F13, not_184_out, not_185_out, not_186_out, OP4, not_187_out, not_188_out);
  and and_33 (and_33_out, not_189_out, not_190_out, not_191_out, not_192_out, F12, not_193_out, not_194_out, OP4, not_195_out, not_196_out);
  and and_34 (and_34_out, not_197_out, not_198_out, F14, not_199_out, F12, not_200_out, not_201_out, OP4, not_202_out, not_203_out);
  and and_35 (and_35_out, F30, not_204_out, F14, not_205_out, F12, not_206_out, not_207_out, OP4, not_208_out, not_209_out);
  and and_36 (and_36_out, not_210_out, F13, not_211_out, not_212_out, not_213_out, not_214_out, not_215_out, not_216_out);
  and and_37 (and_37_out, OP6, OP5, not_217_out, OP3, OP2);
  and and_38 (and_38_out, not_218_out, not_219_out, not_220_out, OP6, OP5, not_221_out, not_222_out, OP2);
  and and_39 (and_39_out, not_223_out, not_224_out, OP4, not_225_out, OP2);
  and and_40 (and_40_out, not_226_out, F13, F12, not_227_out, not_228_out, OP4, not_229_out, not_230_out);
  and and_41 (and_41_out, not_231_out, not_232_out, not_233_out, not_234_out, not_235_out, not_236_out, not_237_out, not_238_out);
  and and_42 (ecall, not_239_out, not_240_out, not_241_out, not_242_out, not_243_out, OP6, OP5, OP4, not_244_out, not_245_out);
  and and_43 (S_Type, not_246_out, F13, not_247_out, not_248_out, OP5, not_249_out, not_250_out, not_251_out);
  and and_44 (BEQ, not_252_out, not_253_out, not_254_out, OP6, OP5, not_255_out, not_256_out, not_257_out);
  and and_45 (BNE, not_258_out, not_259_out, F12, OP6, OP5, not_260_out, not_261_out, not_262_out);
  and and_46 (JALR, not_263_out, not_264_out, not_265_out, OP6, OP5, not_266_out, not_267_out, OP2);
  and and_47 (JAL, OP6, OP5, not_268_out, OP3, OP2);
  or or_1 (MemToReg, and_3_out, and_4_out);
  or or_2 (ALU_SRC, and_9_out, and_10_out, and_11_out, and_12_out, and_13_out, and_14_out, and_15_out, and_16_out, and_17_out, and_18_out, and_19_out, and_20_out, and_21_out);
  or or_3 (RegWrite, and_22_out, and_23_out, and_24_out, and_25_out, and_26_out, and_27_out, and_28_out, and_29_out, and_30_out, and_31_out, and_32_out, and_33_out, and_34_out, and_35_out, and_36_out, and_37_out, and_38_out, and_39_out, and_40_out, and_41_out);
endmodule

// ALU
module ALU (
  input  [31:0] X,
  input  [31:0] Y,
  input  [3:0] AluOP,
  output out_4,
  output Equal,
  output out_6,
  output [31:0] Result,
  output [31:0] Result_2
);

  wire [0:0] comparator_1_lt, comparator_2_lt;
  wire [31:0] adder_1_out, AND_out, divider_1_out, divider_1_rem, multiplier_1_cout, multiplier_1_out,
       NOR_out, OR_out, shifter_1_out, shifter_2_out, shifter_3_out, subtractor_1_out, XOR_out;

  assign AND_out = X & Y;  // AND_Gate AND, 32 bits wide
  assign OR_out = X | Y;  // OR_Gate OR, 32 bits wide
  Shifter #(.width(32), .shift("ll")) shifter_1 (.in(X), .\dist (Y[4:0]), .out(shifter_1_out));
  Shifter #(.width(32), .shift("ar")) shifter_2 (.in(X), .\dist (Y[4:0]), .out(shifter_2_out));
  Shifter #(.width(32), .shift("lr")) shifter_3 (.in(X), .\dist (Y[4:0]), .out(shifter_3_out));
  Multiplier #(.width(32)) multiplier_1 (.a(X), .b(Y), .out(multiplier_1_out), .cout(multiplier_1_cout));  // open: cin
  Divider #(.width(32)) divider_1 (.a(X), .b(Y), .out(divider_1_out), .rem(divider_1_rem));  // open: upper
  Adder #(.width(32)) adder_1 (.a(X), .b(Y), .out(adder_1_out));  // open: cin, cout
  Subtractor #(.width(32)) subtractor_1 (.a(X), .b(Y), .out(subtractor_1_out));  // open: bin, bout
  assign XOR_out = X ^ Y;  // XOR_Gate XOR, 32 bits wide
  assign NOR_out = ~(X | Y);  // NOR_Gate NOR, 32 bits wide
  Comparator #(.width(32), .mode("twosComplement")) comparator_1 (
    .a(X), .b(Y), .eq(Equal), .lt(comparator_1_lt[0]));  // open: gt
  Comparator #(.width(32), .mode("unsigned")) comparator_2 (.a(X), .b(Y), .lt(comparator_2_lt[0]));  // open: gt, eq
  Multiplexer #(.select(4), .width(32), .disabled("Z"), .enable("false")) multiplexer_1 (
    .in0(shifter_1_out), .in1(shifter_2_out), .in2(shifter_3_out), .in3(multiplier_1_out),
    .in4(divider_1_out), .in5(adder_1_out), .in6(subtractor_1_out), .in7(AND_out), .in8(OR_out),
    .in9(XOR_out), .in10(NOR_out), .in11({{31{1'b0}}, comparator_1_lt[0]}),
    .in12({{31{1'b0}}, comparator_2_lt[0]}), .in13({32{1'b0}}), .in14({32{1'b0}}), .in15({32{1'b0}}),
    .out(Result), .sel(AluOP));
  Multiplexer #(.select(4), .width(32), .disabled("Z"), .enable("false")) multiplexer_2 (
    .in0({32{1'b0}}), .in1({32{1'b0}}), .in2({32{1'b0}}), .in3(multiplier_1_cout), .in4(divider_1_rem),
    .in5({32{1'b0}}), .in6({32{1'b0}}), .in7({32{1'b0}}), .in8({32{1'b0}}), .in9({32{1'b0}}),
    .in10({32{1'b0}}), .in11({32{1'b0}}), .in12({32{1'b0}}), .in13({32{1'b0}}), .in14({32{1'b0}}),
    .in15({32{1'b0}}), .out(Result_2), .sel(AluOP));
  Multiplexer #(.select(4), .width(1), .disabled("Z"), .enable("false")) multiplexer_3 (
    .in0(1'b0), .in1(1'b0), .in2(1'b0), .in3(1'b0), .in4(1'b0), .in5(1'b0), .in6(1'b0), .in7(1'b0),
    .in8(1'b0), .in9(1'b0), .in10(1'b0), .in11(comparator_1_lt[0]), .in12(comparator_2_lt[0]), .in13(1'b0),
    .in14(1'b0), .in15(1'b0), .out(out_6), .sel(AluOP));
  not not_1 (out_4, out_6);

  // Other names for the same wires on the sheet: Result2[31:0] = Result_2; S[3:0] = AluOP; tunnel = out_6;
  //   tunnel_t = out_4

  // Notes on the sheet:
  //   不要改变此引脚区域内容，也不要改变ALU封装形式
  //   输入引脚
  //   输出引脚
endmodule

module Regifile (
  input  [31:0] Din,
  input  Clk,
  input  WE,
  input  [4:0] R1_num,
  input  [4:0] W_num,
  input  [4:0] R2_num,
  output [31:0] R1,
  output [31:0] R2
);

  // RegisterFile registerfile_1: pin names not known; wires that end beside it: Din, Clk, WE, W_num, R1_num, R2_num, R1, R2
endmodule

module \单周期_多级中断  (
  output RegWrite,
  output MemWrite,
  output [31:0] PC,
  output [31:0] IR,
  output [31:0] RDin,
  output [31:0] MDin,
  output [31:0] LedData
);

  wire and_1_out, and_2_out, and_3_out, and_4_out, and_5_out, and_6_out, and_7_out, and_8_out, and_9_out,
       and_10_out, and_11_out, and_12_out, and_13_out, and_14_out, and_15_out, and_16_out, and_17_out,
       and_19_out, AUIPC, Beq, Bge, Bne, CLK, clock_2_out, Clr1, Clr1out, Clr2, Clr2out, Clr3, Clr3out,
       comparator_1_eq, comparator_2_eq, comparator_3_eq, comparator_4_eq, comparator_5_eq, comparator_6_eq,
       comparator_7_eq, comparator_7_gt, comparator_8_eq, comparator_8_lt, comparator_9_gt, comparator_10_eq,
       comparator_11_eq, comparator_12_eq, CSRRCI, CSRRSI, CSRRSIen1, CSRRSIen2, CSRRSIen3, d_ff_4_q, ecall,
       equal, Go, halt, Intout1, Intout2, Intout3, IntR, IntR1, IntR2, IntR3, IntRe1, IntRe2, IntRe3,
       IntStatus, IntStatus1, IntStatus2, IntStatus3, IntSuper, IR1, IR1_2_q, IR1_3_q, IR1_4_q, IR1_q, IR2,
       IR2_2_q, IR2_q, IR3, IRA, IRa_t, IRB, IRb_t, IRC, IRc_t, J, lb, nand_1_out, not_1_out, not_2_out,
       not_3_out, not_7_out, not_8_out, not_12_out, or_1_out, or_2_out, or_11_out, or_12_out, or_13_out,
       PCSrc, register_1_q, register_2_q, register_3_q, RST, tunnel, URET, W1, W2, W3, \关中断1 , \关中断2 ,
       \关中断3 , \单周期硬布线控制器_1_alu_src , \单周期硬布线控制器_1_s_type , \开中断 , \开中断1 , \开中断2 , \开中断3 ;
  wire [0:0] \单周期硬布线控制器_1_memtoreg ;
  wire [1:0] IntCur, IntSel, multiplexer_14_out, register_5_q;
  wire [2:0] Instr;
  wire [3:0] \单周期硬布线控制器_1_alu_op ;
  wire [4:0] multiplexer_4_out, multiplexer_5_out;
  wire [11:0] multiplexer_6_out;
  wire [12:0] CNT_num;
  wire [15:0] \总周期数 ;
  wire [31:0] adder_2_out, adder_3_out, adder_4_out, alu_1_result, and_18_out, auipc_res, bit_extender_1_out,
       bit_extender_2_out, bit_extender_3_out, bit_extender_4_out, bit_extender_5_out, bit_extender_6_out,
       bit_extender_7_out, bit_extender_8_out, IntPrc, mEPCout, mEPCout1, mEPCout2, mEPCout3,
       multiplexer_2_out, multiplexer_8_out, multiplexer_10_out, multiplexer_11_out, multiplexer_12_out,
       PC_4, PC_next, R1, ram_1_data, shifter_1_out, shifter_2_out, shifter_3_out;

  Clock #(.highDuration(1), .lowDuration(1)) clock_1 ();  // open: out
  Button _1 (.out(IRa_t));
  Button _2 (.out(IRb_t));
  Button _3 (.out(IRc_t));
  Button \u_继续运行  (.out(Go));
  LED #(.active("true")) led_1 (.in(W1));
  LED #(.active("true")) led_2 (.in(W2));
  LED #(.active("true")) led_3 (.in(W3));
  Hex_Digit_Display hex_digit_display_1 (.value(LedData[31:28]));  // open: dp
  Comparator #(.width(16), .mode("twosComplement")) comparator_1 (
    .a(\总周期数 ), .b(16'h7), .eq(comparator_1_eq));  // open: gt, lt
  Comparator #(.width(16), .mode("twosComplement")) comparator_2 (
    .a(\总周期数 ), .b(16'h241), .eq(comparator_2_eq));  // open: gt, lt
  D_Flip_Flop #(.trigger("rising"), .Pre_Clr_Positions("LEGACY"), .NegatePresetClear("false"), .enable("true"), .NewFFLayout("false")) d_ff_1 (
    .clk(CLK), .D(1'b1), .Q(\开中断1 ), .Qn(\关中断1 ), .en(and_1_out), .reset(and_4_out));  // open: preset
  and and_1 (and_1_out, IntStatus1, CSRRSI);
  D_Flip_Flop #(.trigger("rising"), .Pre_Clr_Positions("LEGACY"), .NegatePresetClear("false"), .enable("true"), .NewFFLayout("false")) d_ff_2 (
    .clk(CLK), .D(1'b1), .Q(\开中断2 ), .Qn(\关中断2 ), .en(and_2_out), .reset(and_5_out));  // open: preset
  and and_2 (and_2_out, IntStatus2, CSRRSI);
  D_Flip_Flop #(.trigger("rising"), .Pre_Clr_Positions("LEGACY"), .NegatePresetClear("false"), .enable("true"), .NewFFLayout("false")) d_ff_3 (
    .clk(CLK), .D(1'b1), .Q(\开中断3 ), .Qn(\关中断3 ), .en(and_3_out), .reset(and_6_out));  // open: preset
  and and_3 (and_3_out, IntStatus3, CSRRSI);
  Hex_Digit_Display hex_digit_display_2 (.value(LedData[23:20]));  // open: dp
  Hex_Digit_Display hex_digit_display_3 (.value(LedData[27:24]));  // open: dp
  Comparator #(.width(16), .mode("twosComplement")) comparator_3 (
    .a(16'h258), .b(\总周期数 ), .eq(comparator_3_eq));  // open: gt, lt
  or or_1 (or_1_out, comparator_3_eq, comparator_4_eq);
  Comparator #(.width(16), .mode("twosComplement")) comparator_4 (
    .a(\总周期数 ), .b(16'h1), .eq(comparator_4_eq));  // open: gt, lt
  Comparator #(.width(16), .mode("twosComplement")) comparator_5 (
    .a(\总周期数 ), .b(16'h4), .eq(comparator_5_eq));  // open: gt, lt
  or or_2 (or_2_out, comparator_1_eq, comparator_2_eq);
  and and_4 (and_4_out, CSRRCI, CSRRSIen1);
  and and_5 (and_5_out, CSRRCI, CSRRSIen2);
  and and_6 (and_6_out, CSRRCI, CSRRSIen3);
  Multiplexer #(.select(2), .width(1), .disabled("Z"), .enable("false")) multiplexer_1 (
    .in0(\开中断1 ), .in1(\开中断2 ), .in2(\开中断3 ), .out(\开中断 ), .sel(IntCur));  // open: in3
  Hex_Digit_Display hex_digit_display_4 (.value(LedData[15:12]));  // open: dp
  Hex_Digit_Display hex_digit_display_5 (.value(LedData[19:16]));  // open: dp
  Pull_Resistor #(.pull(0)) pull_resistor_1 (.node(IRA));
  assign IRA = or_1_out ? ~CLK : 1'bz;  // Controlled_Inverter controlled_inverter_1
  Pull_Resistor #(.pull(0)) pull_resistor_2 (.node(IRB));
  assign IRB = comparator_5_eq ? ~CLK : 1'bz;  // Controlled_Inverter controlled_inverter_2
  Pull_Resistor #(.pull(0)) pull_resistor_3 (.node(IRC));
  assign IRC = or_2_out ? ~CLK : 1'bz;  // Controlled_Inverter controlled_inverter_3
  Hex_Digit_Display hex_digit_display_6 (.value(LedData[7:4]));  // open: dp
  Hex_Digit_Display hex_digit_display_7 (.value(LedData[11:8]));  // open: dp
  // Probe on \总周期数 
  Hex_Digit_Display hex_digit_display_8 (.value(LedData[3:0]));  // open: dp
  Multiplexer #(.select(2), .width(32), .disabled("Z"), .enable("false")) multiplexer_2 (
    .in0(PC_4), .in1(multiplexer_10_out), .in2(mEPCout), .in3(mEPCout), .out(multiplexer_2_out),
    .sel({URET, PCSrc}));
  not not_1 (not_1_out, halt);
  and and_7 (and_7_out, tunnel, Bge);
  and and_8 (and_8_out, Beq, equal);
  and and_9 (and_9_out, Bne, not_2_out);
  not not_2 (not_2_out, equal);
  or or_3 (W1, IR1_4_q, IR1_q);
  or or_4 (W2, IR2_q, IR1_2_q);
  or or_5 (W3, IR2_2_q, IR1_3_q);
  Register #(.width(32), .trigger("rising"), .Select("low")) u_PC (
    .D(multiplexer_2_out), .en(not_1_out), .Q(PC_next), .clk(CLK), .clr(RST));
  or or_6 (J, Instr[2], Instr[0]);
  or or_7 (Instr[1], Beq, Bge, Bne);
  or or_8 (IR1, IRa_t, IRA);
  D_Flip_Flop #(.trigger("rising"), .Pre_Clr_Positions("LEGACY"), .NegatePresetClear("false"), .enable("true"), .NewFFLayout("false")) u_IR1 (
    .clk(IR1), .D(1'b1), .Q(IR1_q), .reset(IR1_4_q));  // open: Qn, preset, en
  D_Flip_Flop #(.trigger("rising"), .Pre_Clr_Positions("LEGACY"), .NegatePresetClear("false"), .enable("true"), .NewFFLayout("false")) IR1_2 (
    .clk(IR2), .D(1'b1), .Q(IR1_2_q), .reset(IR2_q));  // open: Qn, preset, en
  D_Flip_Flop #(.trigger("rising"), .Pre_Clr_Positions("LEGACY"), .NegatePresetClear("false"), .enable("true"), .NewFFLayout("false")) IR1_3 (
    .clk(IR3), .D(1'b1), .Q(IR1_3_q), .reset(IR2_2_q));  // open: Qn, preset, en
  Multiplexer #(.select(1), .width(32), .disabled("Z"), .enable("false")) multiplexer_3 (
    .in0(PC_next), .in1(IntPrc), .out(PC), .sel(IntR));
  or or_9 (PCSrc, and_8_out, and_7_out, and_9_out, J);
  or or_10 (IR2, IRb_t, IRB);
  or or_11 (or_11_out, IR1_q, IR1_4_q);
  or or_12 (or_12_out, IR1_2_q, IR2_q);
  or or_13 (or_13_out, IR1_3_q, IR2_2_q);
  Adder #(.width(32)) adder_1 (.a(PC), .b(32'h4), .out(PC_4));  // open: cin, cout
  and and_10 (and_10_out, or_11_out, ~Clr1);  // AND_Gate
  and and_11 (and_11_out, or_12_out, ~Clr2);  // AND_Gate
  and and_12 (and_12_out, or_13_out, ~Clr3);  // AND_Gate
  and and_13 (and_13_out, Intout1, IntSuper, IntRe1);
  // RiscV_Probe riscv_probe_1: pin names not known; wires that end beside it: IR
  or or_14 (IR3, IRc_t, IRC);
  Register #(.width(1), .trigger("rising"), .Select("low")) \u_中断使能寄存器IE  (
    .D(and_13_out), .Q(IntR1), .clk(CLK));  // open: en, clr
  and and_14 (and_14_out, Intout2, IntSuper, IntRe2);
  Register #(.width(1), .trigger("rising"), .Select("low")) \u_中断使能寄存器IE_2  (
    .D(and_14_out), .Q(IntR2), .clk(CLK));  // open: en, clr
  Register #(.width(1), .trigger("rising"), .Select("low")) \u_中断使能寄存器IE_3  (
    .D(and_15_out), .Q(IntR3), .clk(CLK));  // open: en, clr
  and and_15 (and_15_out, Intout3, IntSuper, IntRe3);
  ROM #(.addrWidth(10), .dataWidth(32), .Select("high")) rom_1 (.addr(PC[11:2]), .data(IR));
  Comparator #(.width(32), .mode("unsigned")) comparator_6 (.a(R1), .b(32'h22), .eq(comparator_6_eq));  // open: gt, lt
  D_Flip_Flop #(.trigger("rising"), .Pre_Clr_Positions("LEGACY"), .NegatePresetClear("false"), .enable("true"), .NewFFLayout("false")) IR1_4 (
    .clk(CLK), .D(and_10_out), .Q(IR1_4_q));  // open: Qn, preset, en, reset
  D_Flip_Flop #(.trigger("rising"), .Pre_Clr_Positions("LEGACY"), .NegatePresetClear("false"), .enable("true"), .NewFFLayout("false")) u_IR2 (
    .clk(CLK), .D(and_11_out), .Q(IR2_q));  // open: Qn, preset, en, reset
  D_Flip_Flop #(.trigger("rising"), .Pre_Clr_Positions("LEGACY"), .NegatePresetClear("false"), .enable("true"), .NewFFLayout("false")) IR2_2 (
    .clk(CLK), .D(and_12_out), .Q(IR2_2_q));  // open: Qn, preset, en, reset
  \单周期硬布线控制器  \u_单周期硬布线控制器_1  (
    .Funct({IR[30], IR[25], IR[14:12]}), .OP(IR[6:2]), .ALU_OP(\单周期硬布线控制器_1_alu_op ),
    .MemToReg(\单周期硬布线控制器_1_memtoreg [0]), .ecall(ecall), .in_3(IR[21]), .uret(URET), .CSRRSI(CSRRSI),
    .CSRRCI(CSRRCI), .MemWrite(MemWrite), .RegWrite(RegWrite), .lb(lb), .S_type(\单周期硬布线控制器_1_s_type ),
    .Beq(Beq), .Bge(Bge), .ALU_SRC(\单周期硬布线控制器_1_alu_src ), .AUIPC(AUIPC), .Jalr(Instr[0]), .JAL(Instr[2]),
    .Bne(Bne));
  Multiplexer #(.select(1), .width(5), .disabled("Z"), .enable("false")) multiplexer_4 (
    .in0(IR[19:15]), .in1(5'b10001), .out(multiplexer_4_out), .sel(ecall));
  Multiplexer #(.select(1), .width(5), .disabled("Z"), .enable("false")) multiplexer_5 (
    .in0(IR[24:20]), .in1(5'b01010), .out(multiplexer_5_out), .sel(ecall));
  Comparator #(.width(32), .mode("twosComplement")) comparator_7 (
    .a(R1), .b(MDin), .gt(comparator_7_gt), .eq(comparator_7_eq));  // open: lt
  assign bit_extender_1_out = {{20{multiplexer_6_out[11]}}, multiplexer_6_out};  // Bit_Extender bit_extender_1
  Multiplexer #(.select(1), .width(12), .disabled("Z"), .enable("false")) multiplexer_6 (
    .in0(IR[31:20]), .in1({IR[31:25], IR[11:7]}), .out(multiplexer_6_out), .sel(\单周期硬布线控制器_1_s_type ));
  assign bit_extender_2_out = {{20{IR[31]}}, {IR[31], IR[7], IR[30:25], IR[11:8]}};  // Bit_Extender bit_extender_2
  assign bit_extender_3_out = {{12{IR[31]}}, {IR[31], IR[19:12], IR[20], IR[30:21]}};  // Bit_Extender bit_extender_3
  assign bit_extender_4_out = {{12{IR[31]}}, IR[31:12]};  // Bit_Extender bit_extender_4
  or or_15 (tunnel, comparator_7_gt, comparator_7_eq);
  and and_16 (and_16_out, ecall, comparator_6_eq);
  and and_17 (and_17_out, ecall, ~comparator_6_eq);  // AND_Gate
  Register #(.width(32), .trigger("rising"), .Select("low")) mEPC (
    .D(PC_next), .en(IntR1), .Q(mEPCout1), .clk(CLK), .clr(Clr1out));
  Register #(.width(32), .trigger("rising"), .Select("low")) mEPC_2 (
    .D(PC_next), .en(IntR2), .Q(mEPCout2), .clk(CLK), .clr(Clr2out));
  Register #(.width(32), .trigger("rising"), .Select("low")) mEPC_3 (
    .D(PC_next), .en(IntR3), .Q(mEPCout3), .clk(CLK), .clr(Clr3out));
  Regifile regifile_1 (
    .Din(RDin), .Clk(CLK), .R1(R1), .R2(MDin), .WE(RegWrite), .W_num(IR[11:7]), .R1_num(multiplexer_4_out),
    .R2_num(multiplexer_5_out));
  Shifter #(.width(32), .shift("ll")) shifter_1 (.in(bit_extender_2_out), .\dist (5'b00001), .out(shifter_1_out));
  Shifter #(.width(32), .shift("ll")) shifter_2 (.in(bit_extender_3_out), .\dist (5'b00001), .out(shifter_2_out));
  Shifter #(.width(32), .shift("ll")) shifter_3 (.in(bit_extender_4_out), .\dist (5'b01100), .out(shifter_3_out));
  Multiplexer #(.select(1), .width(1), .disabled("Z"), .enable("false")) multiplexer_7 (
    .in0(and_17_out), .in1(1'b0), .out(halt), .sel(Go));
  Priority_Encoder #(.select(2), .disabled("Z")) priority_encoder_1 (
    .in0(IR1_4_q), .in1(IR2_q), .in2(IR2_2_q), .out(IntSel), .en_in(1'b1));  // open: in3, gs, en_out
  or or_16 (IntR, IntR1, IntR2, IntR3);
  Adder #(.width(32)) adder_2 (.a(bit_extender_1_out), .b(R1), .out(adder_2_out));  // open: cin, cout
  Adder #(.width(32)) adder_3 (.a(shifter_1_out), .b(PC), .out(adder_3_out));  // open: cin, cout
  Adder #(.width(32)) adder_4 (.a(shifter_2_out), .b(PC), .out(adder_4_out));  // open: cin, cout
  Adder #(.width(32)) adder_5 (.a(shifter_3_out), .b(PC), .out(auipc_res));  // open: cin, cout
  Multiplexer #(.select(1), .width(32), .disabled("Z"), .enable("false")) multiplexer_8 (
    .in0(MDin), .in1(bit_extender_1_out), .out(multiplexer_8_out), .sel(\单周期硬布线控制器_1_alu_src ));
  assign and_18_out = adder_2_out & 32'hfffffffe;  // AND_Gate and_18, 32 bits wide
  D_Flip_Flop #(.trigger("high"), .Pre_Clr_Positions("LEGACY"), .NegatePresetClear("false"), .enable("true"), .NewFFLayout("false")) d_ff_4 (.Q(d_ff_4_q));  // open: clk, D, Qn, preset, en, reset
  // Probe on 13'h230
  Decoder #(.select(2), .tristate("false"), .disabled(0), .enable("false")) decoder_1 (
    .out0(Intout1), .out1(Intout2), .out2(Intout3), .sel(IntSel));  // open: out3
  Multiplexer #(.select(2), .width(32), .disabled("Z"), .enable("false")) multiplexer_9 (
    .in0(32'h30ac), .in1(32'h3158), .in2(32'h3204), .out(IntPrc), .sel(IntSel));  // open: in3
  Register #(.width(1), .trigger("rising"), .Select("low")) register_1 (
    .D(1'b0), .en(URET), .Q(register_1_q), .clk(CLK), .preset(IntR1));  // open: clr, cs
  Register #(.width(1), .trigger("rising"), .Select("low")) register_2 (
    .D(1'b0), .en(URET), .Q(register_2_q), .clk(CLK), .preset(IntR2));  // open: clr, cs
  Register #(.width(1), .trigger("rising"), .Select("low")) register_3 (
    .D(1'b0), .en(URET), .Q(register_3_q), .clk(CLK), .preset(IntR3));  // open: clr, cs
  ALU alu_1 (
    .X(R1), .Y(multiplexer_8_out), .AluOP(\单周期硬布线控制器_1_alu_op ), .Equal(equal), .Result(alu_1_result));  // open: Result_2, out_4, out_6
  Register #(.width(32), .trigger("rising"), .Select("low")) register_4 (
    .D(MDin), .en(and_16_out), .Q(LedData), .clk(CLK));  // open: clr
  Counter #(.width(16), .max('hffff), .ongoal("stay"), .trigger("rising"), .behavior("old")) counter_1 (
    .count(not_3_out), .Q(\总周期数 ), .clk(CLK));  // open: load, D, carry, clr, preset
  not not_3 (not_3_out, halt);
  Comparator #(.width(13), .mode("twosComplement")) comparator_8 (
    .a(CNT_num), .b(13'h230), .eq(comparator_8_eq), .lt(comparator_8_lt));  // open: gt
  Clock #(.highDuration(1), .lowDuration(1)) clock_2 (.out(clock_2_out));
  not not_4 (IntRe1, register_1_q);
  not not_5 (IntRe2, register_2_q);
  not not_6 (IntRe3, register_3_q);
  Counter #(.width(13), .max('h1fff), .ongoal("stay"), .trigger("rising"), .behavior("old")) counter_2 (
    .count(comparator_8_lt), .Q(CNT_num), .clk(clock_2_out));  // open: load, D, carry, clr, preset
  Multiplexer #(.select(3), .width(32), .disabled("Z"), .enable("false")) multiplexer_10 (
    .in1(and_18_out), .in2(adder_3_out), .in4(adder_4_out), .out(multiplexer_10_out), .sel(Instr));  // open: in0, in3, in5, in6, in7
  nand nand_1 (nand_1_out, d_ff_4_q, comparator_8_eq);
  not not_7 (not_7_out, MemWrite);
  assign CLK = nand_1_out ? clock_2_out : 1'bz;  // Controlled_Buffer controlled_buffer_1
  Pull_Resistor #(.pull(1)) pull_resistor_4 (.node(CLK));
  RAM #(.addrWidth(10), .dataWidth(32), .bus("separate"), .Select("high")) ram_1 (
    .addr(alu_1_result[11:2]), .din(MDin), .data(ram_1_data), .str(MemWrite), .clk(CLK), .ld(not_7_out));  // open: sel, clr
  Comparator #(.width(2), .mode("unsigned")) comparator_9 (
    .a(IntSel), .b(IntCur), .gt(comparator_9_gt));  // open: eq, lt
  Priority_Encoder #(.select(2), .disabled("Z")) priority_encoder_2 (
    .in0(IntStatus1), .in1(IntStatus2), .in2(IntStatus3), .out(IntCur), .en_in(1'b1));  // open: in3, gs, en_out
  not not_8 (not_8_out, IntStatus);
  and and_19 (and_19_out, IntStatus, comparator_9_gt, \开中断 );
  assign bit_extender_5_out = {{24{ram_1_data[7]}}, ram_1_data[7:0]};  // Bit_Extender bit_extender_5
  assign bit_extender_6_out = {{24{ram_1_data[15]}}, ram_1_data[15:8]};  // Bit_Extender bit_extender_6
  assign bit_extender_7_out = {{24{ram_1_data[23]}}, ram_1_data[23:16]};  // Bit_Extender bit_extender_7
  assign bit_extender_8_out = {{24{ram_1_data[31]}}, ram_1_data[31:24]};  // Bit_Extender bit_extender_8
  Comparator #(.width(32), .mode("unsigned")) comparator_10 (
    .a(mEPCout1), .b({32{1'b0}}), .eq(comparator_10_eq));  // open: gt, lt
  not not_9 (IntStatus1, comparator_10_eq);
  not not_10 (IntStatus2, comparator_11_eq);
  Comparator #(.width(32), .mode("unsigned")) comparator_11 (
    .a(mEPCout2), .b({32{1'b0}}), .eq(comparator_11_eq));  // open: gt, lt
  not not_11 (IntStatus3, comparator_12_eq);
  Comparator #(.width(32), .mode("unsigned")) comparator_12 (
    .a(mEPCout3), .b({32{1'b0}}), .eq(comparator_12_eq));  // open: gt, lt
  or or_17 (IntSuper, not_8_out, and_19_out);
  Register #(.width(2), .trigger("rising"), .Select("low")) register_5 (
    .D(IntCur), .Q(register_5_q), .clk(CLK));  // open: en, clr
  Multiplexer #(.select(2), .width(32), .disabled("Z"), .enable("false")) multiplexer_11 (
    .in0(bit_extender_5_out), .in1(bit_extender_6_out), .in2(bit_extender_7_out), .in3(bit_extender_8_out),
    .out(multiplexer_11_out), .sel(alu_1_result[1:0]));
  Decoder #(.select(2), .tristate("false"), .disabled(0), .enable("false")) decoder_2 (
    .out0(CSRRSIen1), .out1(CSRRSIen2), .out2(CSRRSIen3), .sel(register_5_q));  // open: out3
  Decoder #(.select(2), .tristate("false"), .disabled(0), .enable("true")) decoder_3 (
    .out0(Clr1), .out1(Clr2), .out2(Clr3), .sel(register_5_q), .en(URET));  // open: out3
  Multiplexer #(.select(2), .width(32), .disabled("Z"), .enable("false")) multiplexer_12 (
    .in0(alu_1_result), .in1(ram_1_data), .in3(multiplexer_11_out), .out(multiplexer_12_out),
    .sel({lb, \单周期硬布线控制器_1_memtoreg [0]}));  // open: in2
  Multiplexer #(.select(2), .width(32), .disabled("Z"), .enable("false")) multiplexer_13 (
    .in0(multiplexer_12_out), .in1(PC_4), .in2(auipc_res), .out(RDin), .sel({AUIPC, J}));  // open: in3
  not not_12 (not_12_out, IntStatus);
  or or_18 (IntStatus, IntStatus1, IntStatus2, IntStatus3);
  Multiplexer #(.select(1), .width(2), .disabled("Z"), .enable("false")) multiplexer_14 (
    .in0(IntCur), .in1(2'b00), .out(multiplexer_14_out), .sel(not_12_out));
  Multiplexer #(.select(2), .width(32), .disabled("Z"), .enable("false")) multiplexer_15 (
    .in0(mEPCout1), .in1(mEPCout2), .in2(mEPCout3), .out(mEPCout), .sel(multiplexer_14_out));  // open: in3
  Register #(.width(1), .trigger("rising"), .Select("low")) register_6 (
    .D(Clr1), .Q(Clr1out), .clk(CLK));  // open: en, clr
  Register #(.width(1), .trigger("rising"), .Select("low")) register_7 (
    .D(Clr2), .Q(Clr2out), .clk(CLK));  // open: en, clr
  Register #(.width(1), .trigger("rising"), .Select("low")) register_8 (
    .D(Clr3), .Q(Clr3out), .clk(CLK));  // open: en, clr

  // Other names for the same wires on the sheet: JALR = Instr[0]; JAL = Instr[2]

  // Notes on the sheet:
  //   中断源
  //   中断等待指示
  //   总复位信号应将除ROM以外所有存储组件全部清零
  //   多级中断测试信号模拟器
  //   数码管输出
  //   中断请求生成
  //   开关中断逻辑
  //   数码管输出应该用寄存器锁存，否则显示数据只能一闪而过
  //   中断使能逻辑
  //   中断按键逻辑
  //   指令探针
  //   指令存储器
  //   PC+4
  //   指令字
  //   contents of rom_1 (hex, n*v repeats v):
  //   7d000113 100413 1f41993 41f9d993 433 c00913 800b13 140413 f47413 800293 100313 499993 89e9b3 1300533
  //   2200893 73 406282b3 fe0294e3 140413 f00f93 1f47433 1c41413 800293 100313 49d993 89e9b3 1300533
  //   2200893 73 406282b3 fe0294e3 1c45413 406b0b33 b0463 f95ff06f 2b3 fff2c293 1029293 fff2e293 500533
  //   2200893 73 f5dff06f 1112023 410113 a12023 410113 812023 410113 1312023 410113 1412023 410113 1512023
  //   410113 1612023 410113 40e073 100b13 300a13 100a93 1600433 441413 14469b3 1300533 2200893 73 fe0416e3
  //   415a0a33 fe0a10e3 40f073 ffc10113 12b03 ffc10113 12a83 ffc10113 12a03 ffc10113 12983 ffc10113 12403
  //   ffc10113 12503 ffc10113 12883 200073 1112023 410113 a12023 410113 812023 410113 1312023 410113
  //   1412023 410113 1512023 410113 1612023 410113 40e073 200b13 300a13 100a93 1600433 441413 14469b3
  //   1300533 2200893 73 fe0416e3 415a0a33 fe0a10e3 40f073 ffc10113 12b03 ffc10113 12a83 ffc10113 12a03
  //   ffc10113 12983 ffc10113 12403 ffc10113 12503 ffc10113 12883 200073 1112023 410113 a12023 410113
  //   812023 410113 1312023 410113 1412023 410113 1512023 410113 1612023 410113 40e073 300b13 300a13
  //   100a93 1600433 441413 14469b3 1300533 2200893 73 fe0416e3 415a0a33 fe0a10e3 40f073 ffc10113 12b03
  //   ffc10113 12a83 ffc10113 12a03 ffc10113 12983 ffc10113 12403 ffc10113 12503 ffc10113 12883 200073
  //   JAL
  //   JALR
  //   URET
  //   Beq
  //   Bne
  //   MemToReg
  //   MemWrite
  //   AluOP
  //   AluSrcB
  //   RegWrite
  //   S_Tyoe
  //   I型
  //   S型
  //   B型
  //   J型
  //   为方便自动评测，需要输出PC，IR，寄存器堆写如数据RDin
  //   rs1
  //   rs2
  //   rd
  //   RAM写使能MemWrite、RAM写入数据MDin等信号
  //   中断入口信号
  //   控制位
  //   暂停节拍，不能为0
  //   入口地址
  //   戳工具置1进入计数暂停模式，ctrl+k时钟自动运行到对应节拍暂停
  //   ctrl+k关闭时钟连续运行，将控制位置零，进入单步调试模式调试
  //   用这个时钟源需要去掉电路中的其他时钟源
  //   数据存储器
  //   可计数暂停的时钟源
  //   高级中断低级使能逻辑
  //   中断状态逻辑plus，承接中断等级比较以及开中断信号和清零信号
  //   中断状态逻辑
  //   中断出口逻辑
  //   清零信号滞留
endmodule
